// Logisim project 4-bit ALU.circ as structural Verilog: 4 circuits, main circuit 4-bit ALU
module _4_bit_ALU (
  input  [3:0] A,
  input  [3:0] B,
  input  [4:0] Input,
  output C_out,
  output [3:0] Output
);

  wire [3:0] arithmetic_circuit_ac_1_output, logical_circuit_lu_1_output, shift_circuit_su_1_output;

  Arithmetic_Circuit___AC arithmetic_circuit_ac_1 (
    .Cin(Input[2]), .S0(Input[4]), .S1(Input[3]), .Input_A(A), .Input_B(B),
    .Output(arithmetic_circuit_ac_1_output), .C_out(C_out));
  Logical_Circuit___LU logical_circuit_lu_1 (
    .S0(Input[4]), .S1(Input[3]), .S2(Input[2]), .Input_A(A), .Input_B(B),
    .Output(logical_circuit_lu_1_output));
  Shift_Circuit___SU shift_circuit_su_1 (.Input(A), .Output(shift_circuit_su_1_output), .S(Input[2]));
  Multiplexer #(.select(2), .width(4), .enable("false")) multiplexer_1 (
    .in0(4'b0000), .in1(arithmetic_circuit_ac_1_output), .in2(logical_circuit_lu_1_output),
    .in3(shift_circuit_su_1_output), .out(Output), .sel({Input[0], Input[1]}));

  // Other names for the same wires on the sheet: S3 = Input[1]; S4 = Input[0]; S2 = Input[2]; S1 = Input[3];
  //   S0 = Input[4]

  // Notes on the sheet:
  //   S0 S1 S2 S3 S4
  //   X    X    X    0    0
  //   0    0    0    1    0
  //   0    0    1    1    0
  //   1    0    1    1    0
  //   1    0    0    1    0
  //   0    1    1    1    0
  //   1    1    0    1    0
  //   0    1    0    1    0
  //   1    1    1    1    0
  //   0    0    0    0    1
  //   1    0    0    0    1
  //   0    1    0    0    1
  //   1    1    0    0    1
  //   0    0    1    0    1
  //   1    0    1    0    1
  //   0    1    1    0    1
  //   1    1    1    0    1
  //   X    X    0    1    1
  //   X    X    1    1    1
  //   SELECT BITS     |     OPERATIONS 
  //   |
  //   |
  //   |
  //   |
  //   |
  //   |
  //   |
  //   |
  //   |
  //   |
  //   |
  //   |
  //   |
  //   |
  //   |
  //   |
  //   |
  //   |
  //   |
  //   |
  //   |
  //   |
  //   |
  //   |
  //   |
  //   |
  //   |
  //   |
  //   |
  //   |
  //   |
  //   |
  //   |
  //   |
  //   O/P
  //   0
  //   A + B
  //   A + B + 1
  //   A - B
  //   A - B - 1
  //   A + 1
  //   A - 1
  //   A
  //   A
  //   A AND B
  //   A OR B
  //   A XOR B
  //   A'
  //   Selective Set
  //   Selective Clear
  //   Selective Complement
  //   Selective Mask
  //   Arithmetic Left Shift (*2)
  //   Arithmetic Right Shift (/2)
endmodule

module Arithmetic_Circuit___AC (
  input  Cin,
  input  S0,
  input  [3:0] Input_A,
  input  S1,
  input  [3:0] Input_B,
  output C_out,
  output [3:0] Output
);

  wire adder_1_cout, adder_2_cout, adder_3_cout, multiplexer_1_out, multiplexer_2_out, multiplexer_3_out,
       multiplexer_4_out, not_1_out, not_2_out, not_3_out, not_4_out;

  not not_1 (not_1_out, Input_B[0]);
  not not_2 (not_2_out, Input_B[1]);
  not not_3 (not_3_out, Input_B[2]);
  not not_4 (not_4_out, Input_B[3]);
  Multiplexer #(.select(2), .enable("false")) multiplexer_1 (
    .in0(Input_B[0]), .in1(not_1_out), .in2(1'b0), .in3(1'b1), .out(multiplexer_1_out), .sel({S1, S0}));
  Multiplexer #(.select(2), .enable("false")) multiplexer_2 (
    .in0(Input_B[1]), .in1(not_2_out), .in2(1'b0), .in3(1'b1), .out(multiplexer_2_out), .sel({S1, S0}));
  Multiplexer #(.select(2), .enable("false")) multiplexer_3 (
    .in0(Input_B[2]), .in1(not_3_out), .in2(1'b0), .in3(1'b1), .out(multiplexer_3_out), .sel({S1, S0}));
  Multiplexer #(.select(2), .enable("false")) multiplexer_4 (
    .in0(Input_B[3]), .in1(not_4_out), .in2(1'b0), .in3(1'b1), .out(multiplexer_4_out), .sel({S1, S0}));
  Adder #(.width(1)) adder_1 (.a(Input_A[0]), .b(multiplexer_1_out), .out(Output[0]), .cin(Cin), .cout(adder_1_cout));
  Adder #(.width(1)) adder_2 (
    .a(Input_A[1]), .b(multiplexer_2_out), .out(Output[1]), .cin(adder_1_cout), .cout(adder_2_cout));
  Adder #(.width(1)) adder_3 (
    .a(Input_A[2]), .b(multiplexer_3_out), .out(Output[2]), .cin(adder_2_cout), .cout(adder_3_cout));
  Adder #(.width(1)) adder_4 (.a(Input_A[3]), .b(multiplexer_4_out), .out(Output[3]), .cin(adder_3_cout), .cout(C_out));

  // Other names for the same wires on the sheet: A0 = Input_A[0]; A1 = Input_A[1]; A2 = Input_A[2]; A3 = Input_A[3];
  //   B0 = Input_B[0]; B1 = Input_B[1]; B2 = Input_B[2]; B3 = Input_B[3]; R0 = Output[0]; R1 = Output[1];
  //   R2 = Output[2]; R3 = Output[3]
endmodule

module Logical_Circuit___LU (
  input  S0,
  input  S1,
  input  [3:0] Input_A,
  input  S2,
  input  [3:0] Input_B,
  output [3:0] Output
);

  wire and_1_out, and_2_out, and_3_out, and_4_out, and_5_out, and_6_out, and_7_out, and_8_out, not_1_out,
       not_2_out, not_3_out, not_4_out, not_5_out, not_6_out, not_7_out, not_8_out, or_1_out, or_2_out,
       or_3_out, or_4_out, xor_1_out, xor_2_out, xor_3_out, xor_4_out;

  and and_1 (and_1_out, Input_A[0], Input_B[0]);
  or or_1 (or_1_out, Input_A[0], Input_B[0]);
  xor xor_1 (xor_1_out, Input_B[0], Input_A[0]);
  not not_1 (not_1_out, Input_A[0]);
  and and_2 (and_2_out, Input_A[1], Input_B[1]);
  or or_2 (or_2_out, Input_A[1], Input_B[1]);
  xor xor_2 (xor_2_out, Input_B[1], Input_A[1]);
  not not_2 (not_2_out, Input_A[1]);
  and and_3 (and_3_out, Input_A[2], Input_B[2]);
  or or_3 (or_3_out, Input_A[2], Input_B[2]);
  xor xor_3 (xor_3_out, Input_B[2], Input_A[2]);
  not not_3 (not_3_out, Input_A[2]);
  and and_4 (and_4_out, Input_A[3], Input_B[3]);
  or or_4 (or_4_out, Input_A[3], Input_B[3]);
  xor xor_4 (xor_4_out, Input_B[3], Input_A[3]);
  not not_4 (not_4_out, Input_A[3]);
  and and_5 (and_5_out, Input_A[0], not_5_out);
  not not_5 (not_5_out, Input_B[0]);
  and and_6 (and_6_out, Input_A[1], not_6_out);
  not not_6 (not_6_out, Input_B[1]);
  and and_7 (and_7_out, Input_A[2], not_7_out);
  not not_7 (not_7_out, Input_B[2]);
  and and_8 (and_8_out, Input_A[3], not_8_out);
  not not_8 (not_8_out, Input_B[3]);
  Multiplexer #(.select(3), .enable("false")) multiplexer_1 (
    .in0(and_1_out), .in1(or_1_out), .in2(xor_1_out), .in3(not_1_out), .in4(or_1_out), .in5(and_5_out),
    .in6(xor_1_out), .in7(and_1_out), .out(Output[0]), .sel({S2, S1, S0}));
  Multiplexer #(.select(3), .enable("false")) multiplexer_2 (
    .in0(and_2_out), .in1(or_2_out), .in2(xor_2_out), .in3(not_2_out), .in4(or_2_out), .in5(and_6_out),
    .in6(xor_2_out), .in7(and_2_out), .out(Output[1]), .sel({S2, S1, S0}));
  Multiplexer #(.select(3), .enable("false")) multiplexer_3 (
    .in0(and_3_out), .in1(or_3_out), .in2(xor_3_out), .in3(not_3_out), .in4(or_3_out), .in5(and_7_out),
    .in6(xor_3_out), .in7(and_3_out), .out(Output[2]), .sel({S2, S1, S0}));
  Multiplexer #(.select(3), .enable("false")) multiplexer_4 (
    .in0(and_4_out), .in1(or_4_out), .in2(xor_4_out), .in3(not_4_out), .in4(or_4_out), .in5(and_8_out),
    .in6(xor_4_out), .in7(and_4_out), .out(Output[3]), .sel({S2, S1, S0}));

  // Other names for the same wires on the sheet: A0 = Input_A[0]; A1 = Input_A[1]; A2 = Input_A[2]; A3 = Input_A[3];
  //   B0 = Input_B[0]; B1 = Input_B[1]; B2 = Input_B[2]; B3 = Input_B[3]; R0 = Output[0]; R1 = Output[1];
  //   R2 = Output[2]; R3 = Output[3]
endmodule

module Shift_Circuit___SU (
  input  [3:0] Input,
  input  S,
  output [3:0] Output
);

  Multiplexer #(.width(4), .enable("false")) multiplexer_1 (
    .in0({Input[2:0], 1'b0}), .in1({1'b0, Input[3:1]}), .out(Output), .sel(S));
endmodule
