// Logisim project Multiplier.circ as structural Verilog: 3 circuits, main circuit Shift and Add Multiplier
module Shift_and_Add_Multiplier (
  input  Restart,
  input  Start,
  input  [7:0] M,
  input  [3:0] Q,
  input  Register_Enable
);

  wire CLK_out, comparator_1_eq, not_1_out, not_2_out, or_1_out, or_2_out, or_3_out, or_4_out;
  wire [2:0] Count___C_q;
  wire [3:0] controlled_buffer_2_out, multiplexer_2_out, Q_Output, Q_t;
  wire [7:0] A, A_M, A_Output, controlled_buffer_1_out, controlled_buffer_3_out, M_Output, M_t,
       multiplexer_1_out, multiplexer_3_out;

  not not_1 (not_1_out, Start);
  assign controlled_buffer_1_out = not_2_out ? M_Output : 8'bz;  // Controlled_Buffer controlled_buffer_1
  assign controlled_buffer_2_out = not_2_out ? Q_Output : 4'bz;  // Controlled_Buffer controlled_buffer_2
  assign controlled_buffer_3_out = not_2_out ? A_Output : 8'bz;  // Controlled_Buffer controlled_buffer_3
  or or_1 (or_1_out, Start, not_1_out);
  or or_2 (or_2_out, Start, not_1_out);
  or or_3 (or_3_out, Start, not_1_out);
  or or_4 (or_4_out, Start, not_1_out);
  Clock CLK (.out(CLK_out));
  Multiplexer #(.width(8)) multiplexer_1 (
    .in0(M), .in1(controlled_buffer_1_out), .out(multiplexer_1_out), .sel(not_1_out), .en(or_1_out));
  Multiplexer #(.width(4)) multiplexer_2 (
    .in0(Q), .in1(controlled_buffer_2_out), .out(multiplexer_2_out), .sel(not_1_out), .en(or_2_out));
  Multiplexer #(.width(8)) multiplexer_3 (
    .in0({8{1'b0}}), .in1(controlled_buffer_3_out), .out(multiplexer_3_out), .sel(not_1_out), .en(or_3_out));
  Register Multiplicand___M (.D(multiplexer_1_out), .en(Register_Enable), .Q(M_t), .clk(CLK_out), .clr(Restart));
  Register #(.width(4)) Multiplier___Q (
    .D(multiplexer_2_out), .en(Register_Enable), .Q(Q_t), .clk(CLK_out), .clr(Restart));
  Register Accumulator___A (.D(multiplexer_3_out), .en(Register_Enable), .Q(A), .clk(CLK_out), .clr(Restart));
  Counter #(.width(3), .max('h4), .ongoal("stay")) Count___C (
    .load(or_4_out), .D(3'b100), .count(not_1_out), .Q(Count___C_q), .clk(CLK_out), .clr(Restart));  // open: carry
  Hex_Digit_Display hex_digit_display_1 (.value(M[7:4]));  // open: dp
  Comparator #(.width(3)) comparator_1 (.a(Count___C_q), .b(3'b000), .eq(comparator_1_eq));  // open: gt, lt
  Hex_Digit_Display hex_digit_display_2 (.value(M[3:0]));  // open: dp
  not not_2 (not_2_out, comparator_1_eq);
  Hex_Digit_Display hex_digit_display_3 (.value(Q));  // open: dp
  Adder adder_1 (.a(M_t), .b(A), .out(A_M), .cin(1'b0));  // open: cout
  Multiplexer #(.width(8), .enable("false")) multiplexer_4 (.in0(A), .in1(A_M), .out(A_Output), .sel(Q_t[0]));
  Shifter shifter_1 (.in(M_t), .\dist (3'b001), .out(M_Output));
  Shifter #(.width(4), .shift("lr")) shifter_2 (.in(Q_t), .\dist (2'b01), .out(Q_Output));
  LED Calculation_is_Over__When_LED_is_turned_off (.in(not_2_out));
  Hex_Digit_Display hex_digit_display_4 (.value(A[7:4]));  // open: dp
  Hex_Digit_Display hex_digit_display_5 (.value(A[3:0]));  // open: dp

  // Other names for the same wires on the sheet: LB_A[3:0] = A[3:0]; HB_A[3:0] = A[7:4]; LB_M[3:0] = M[3:0];
  //   M_Input[7:0] = M; HB_M[3:0] = M[7:4]; Q_Input[3:0] = Q

  // Notes on the sheet:
  //   STEPS TO RUN
  //   First, Load M and Q and then Press Start and Regiser Enable Buttons to Load the Value in the Registers with one clock cycle.
  //    Then, First turn off the Start Button but Keep the Register Enable button on after loading the Values in the Register.
  //   Then, Enable the Automatic Clock Ticks and wait until the LED goes off that is multiplication is over.
  //   X
  //   =
endmodule

module Improved_Shift_and_Add_Multiplier (
  input  Restart,
  input  Start,
  input  [3:0] M,
  input  [3:0] Q,
  input  Register_Enable
);

  wire CLK_out, comparator_1_eq, not_1_out, not_2_out, or_1_out, or_2_out, or_3_out;
  wire [2:0] Count___C_q;
  wire [3:0] A, A_M, A_Output_1, A_Output_2, AQ, controlled_buffer_1_out, controlled_buffer_2_out, M_t,
       multiplexer_1_out, multiplexer_2_out, Q_t;

  assign controlled_buffer_1_out = not_2_out ? AQ : 4'bz;  // Controlled_Buffer controlled_buffer_1
  assign controlled_buffer_2_out = not_2_out ? A_Output_2 : 4'bz;  // Controlled_Buffer controlled_buffer_2
  not not_1 (not_1_out, Start);
  or or_1 (or_1_out, Start, not_1_out);
  or or_2 (or_2_out, Start, not_1_out);
  or or_3 (or_3_out, Start, not_1_out);
  Multiplexer #(.width(4)) multiplexer_1 (
    .in0(Q), .in1(controlled_buffer_1_out), .out(multiplexer_1_out), .sel(not_1_out), .en(or_1_out));
  Multiplexer #(.width(4)) multiplexer_2 (
    .in0(4'b0000), .in1(controlled_buffer_2_out), .out(multiplexer_2_out), .sel(not_1_out), .en(or_2_out));
  Clock CLK (.out(CLK_out));
  Register #(.width(4)) Multiplicant___M (.D(M), .en(Register_Enable), .Q(M_t), .clk(CLK_out), .clr(Restart));
  Register #(.width(4)) Multiplier___Q (
    .D(multiplexer_1_out), .en(Register_Enable), .Q(Q_t), .clk(CLK_out), .clr(Restart));
  Register #(.width(4)) Accumulator___A (
    .D(multiplexer_2_out), .en(Register_Enable), .Q(A), .clk(CLK_out), .clr(Restart));
  Counter #(.width(3), .max('h4), .ongoal("stay")) Count___C (
    .load(or_3_out), .D(3'b100), .count(not_1_out), .Q(Count___C_q), .clk(CLK_out), .clr(Restart));  // open: carry
  Hex_Digit_Display hex_digit_display_1 (.value(M));  // open: dp
  not not_2 (not_2_out, comparator_1_eq);
  Comparator #(.width(3)) comparator_1 (.a(Count___C_q), .b(3'b000), .eq(comparator_1_eq));  // open: gt, lt
  LED Calculation_is_Over__When_LED_is_turned_off (.in(not_2_out));
  Hex_Digit_Display hex_digit_display_2 (.value(Q));  // open: dp
  Adder #(.width(4)) adder_1 (.a(M_t), .b(A), .out(A_M), .cin(1'b0));  // open: cout
  Multiplexer #(.width(4), .enable("false")) multiplexer_3 (.in0(A), .in1(A_M), .out(A_Output_1), .sel(Q_t[0]));
  Shifter #(.shift("ar")) shifter_1 (.in({A_Output_1, Q_t}), .\dist (3'b001), .out({A_Output_2, AQ}));
  Hex_Digit_Display hex_digit_display_3 (.value(A));  // open: dp
  Hex_Digit_Display hex_digit_display_4 (.value(Q_t));  // open: dp

  // Other names for the same wires on the sheet: Q_Output[3:0] = AQ; AQ[7:4] = A_Output_2; M_Input[3:0] = M;
  //   Q_Input[3:0] = Q

  // Notes on the sheet:
  //   STEPS TO RUN
  //   First, Load M and Q and then Press Start and Regiser Enable Buttons to Load the Value in the Registers with one clock cycle.
  //    Then, First turn off the Start Button but Keep the Register Enable button on after loading the Values in the Register.
  //   Then, Enable the Automatic Clock Ticks and wait until the LED goes off that is multiplication is over.
  //   X
  //   =
endmodule

module Booth_s_Multiplier (
  input  Restart,
  input  Start,
  input  [3:0] M,
  input  [3:0] Q,
  input  Register_Enable
);

  wire CLK_out, comparator_1_eq, controlled_buffer_3_out, multiplexer_3_out, not_1_out, not_2_out, or_1_out,
       or_2_out, or_3_out, or_4_out, Q__1;
  wire [2:0] Count___C_q;
  wire [3:0] A, A_M, A_M_t, A_Output_1, A_Output_2, controlled_buffer_1_out, controlled_buffer_2_out, M_t,
       multiplexer_1_out, multiplexer_2_out, not_3_out, Q_t;
  wire [4:0] AQ;

  assign controlled_buffer_1_out = not_2_out ? AQ[4:1] : 4'bz;  // Controlled_Buffer controlled_buffer_1
  assign controlled_buffer_2_out = not_2_out ? A_Output_2 : 4'bz;  // Controlled_Buffer controlled_buffer_2
  assign controlled_buffer_3_out = not_2_out ? AQ[0] : 1'bz;  // Controlled_Buffer controlled_buffer_3
  not not_1 (not_1_out, Start);
  or or_1 (or_1_out, Start, not_1_out);
  or or_2 (or_2_out, Start, not_1_out);
  or or_3 (or_3_out, Start, not_1_out);
  or or_4 (or_4_out, Start, not_1_out);
  Multiplexer #(.width(4)) multiplexer_1 (
    .in0(Q), .in1(controlled_buffer_1_out), .out(multiplexer_1_out), .sel(not_1_out), .en(or_1_out));
  Multiplexer #(.width(4)) multiplexer_2 (
    .in0(4'b0000), .in1(controlled_buffer_2_out), .out(multiplexer_2_out), .sel(not_1_out), .en(or_2_out));
  Multiplexer multiplexer_3 (
    .in0(1'b0), .in1(controlled_buffer_3_out), .out(multiplexer_3_out), .sel(not_1_out), .en(or_4_out));
  Clock CLK (.out(CLK_out));
  Register #(.width(4)) Multiplicant___M (.D(M), .en(Register_Enable), .Q(M_t), .clk(CLK_out), .clr(Restart));
  Register #(.width(4)) Multiplier___Q (
    .D(multiplexer_1_out), .en(Register_Enable), .Q(Q_t), .clk(CLK_out), .clr(Restart));
  Register #(.width(4)) Accumulator___A (
    .D(multiplexer_2_out), .en(Register_Enable), .Q(A), .clk(CLK_out), .clr(Restart));
  Counter #(.width(3), .max('h4), .ongoal("stay")) Count___C (
    .load(or_3_out), .D(3'b100), .count(not_1_out), .Q(Count___C_q), .clk(CLK_out), .clr(Restart));  // open: carry
  Register #(.width(1)) u_Q__1 (.D(multiplexer_3_out), .en(Register_Enable), .Q(Q__1), .clk(CLK_out), .clr(Restart));
  Hex_Digit_Display hex_digit_display_1 (.value(M));  // open: dp
  Comparator #(.width(3)) comparator_1 (.a(Count___C_q), .b(3'b000), .eq(comparator_1_eq));  // open: gt, lt
  not not_2 (not_2_out, comparator_1_eq);
  Adder #(.width(4)) adder_1 (.a(A), .b(M_t), .out(A_M), .cin(1'b0));  // open: cout
  LED Calculation_is_Over__When_LED_is_turned_off (.in(not_2_out));
  Hex_Digit_Display hex_digit_display_2 (.value(Q));  // open: dp
  Hex_Digit_Display hex_digit_display_3 (.value(A));  // open: dp
  assign not_3_out = ~M_t;  // NOT_Gate not_3, 4 bits wide
  Multiplexer #(.select(2), .width(4), .enable("false")) multiplexer_4 (
    .in0(A), .in1(A_M), .in2(A_M_t), .in3(A), .out(A_Output_1), .sel({Q_t[0], Q__1}));
  Shifter #(.width(9), .shift("ar")) shifter_1 (.in({A_Output_1, Q_t, Q__1}), .\dist (4'b0001), .out({A_Output_2, AQ}));
  Hex_Digit_Display hex_digit_display_4 (.value(Q_t));  // open: dp
  Adder #(.width(4)) adder_2 (.a(A), .b(not_3_out), .out(A_M_t), .cin(1'b1));  // open: cout

  // Other names for the same wires on the sheet: AQ[8:5] = A_Output_2; Q__1__O_P = AQ[0]; M_Input[3:0] = M;
  //   Q_Input[3:0] = Q; Q_Output[3:0] = AQ[4:1]

  // Notes on the sheet:
  //   STEPS TO RUN
  //   First, Load M and Q and then Press Start and Regiser Enable Buttons to Load the Value in the Registers with one clock cycle.
  //    Then, First turn off the Start Button but Keep the Register Enable button on after loading the Values in the Register.
  //   Then, Enable the Automatic Clock Ticks and wait until the LED goes off that is multiplication is over.
  //   X
  //   =
endmodule
