// Logisim project Control Unit - I.circ as structural Verilog: 8 circuits, main circuit Control Unit
module Control_Unit (
  input  [15:0] INPUT,
  input  Manually_Load_the_PC,
  input  in_3,
  input  in_4,
  input  in_5,
  input  in_6,
  input  in_7,
  input  in_8,
  output [15:0] out_9,
  output [15:0] out_10,
  output [15:0] out_11,
  output [15:0] out_12,
  output [11:0] out_13,
  output I,
  output [7:0] D0_D7,
  output [15:0] out_16
);

  wire CLK, not_1_out, not_2_out, or_1_out, or_2_out, T0, T1, T2;
  wire [1:0] MUX_Select_Lines;
  wire [11:0] bit_extender_1_out;
  wire [15:0] bit_extender_2_out, multiplexer_1_out;

  Bit_Extender #(.in_width(16), .out_width(12)) bit_extender_1 (.in(out_11), .out(bit_extender_1_out));
  or or_1 (or_1_out, CLK, Manually_Load_the_PC);
  or or_2 (or_2_out, T0, T2);
  or or_3 (MUX_Select_Lines[0], T1, T2, not_1_out);
  or or_4 (MUX_Select_Lines[1], T1, T2, not_2_out);
  Program_Counter_PC program_counter_pc_1 (
    .INPUT(INPUT), .CLK(or_1_out), .OUTPUT(out_10), .LOAD(in_3), .INC(T1), .CLR(in_4));
  Instruction_Register_IR instruction_register_ir_1 (
    .INPUT(out_11), .CLK(CLK), .OUTPUT(out_12), .LOAD(T1), .CLR(in_6), .INC(in_5));
  Address_Register_AR address_register_ar_1 (
    .INPUT(bit_extender_1_out), .CLK(CLK), .OUTPUT(out_13), .LOAD(or_2_out), .INC(in_7), .CLR(in_8));
  not not_1 (not_1_out, T0);
  not not_2 (not_2_out, T0);
  assign bit_extender_2_out = {{4{1'b0}}, out_13};  // Bit_Extender bit_extender_2
  Multiplexer #(.width(16), .enable("false")) multiplexer_1 (
    .in0(bit_extender_2_out), .in1(out_16), .out(multiplexer_1_out), .sel(T2));
  Clock #(.highDuration(2)) CLOCK (.out(CLK));
  ROM #(.addrWidth(12), .dataWidth(16)) rom_1 (.addr(out_13), .data(out_9));  // open: sel
  Multiplexer #(.select(2), .width(16), .enable("false")) multiplexer_2 (
    .in0(out_10), .in1(out_12), .in2(multiplexer_1_out), .in3(out_9), .out(out_11), .sel(MUX_Select_Lines));
  Timing_Signals_Generation_Circuit timing_signals_generation_circuit_1 (
    .T0(T0), .T1(T1), .T2(T2), .CLK(CLK), .Enable(1'b1));  // open: T3, T4, T5, T6, T7, T8, T9, T10, T11, T12, T13, T14, T15, CLR, INC
  IR_Decoding_Circuit ir_decoding_circuit_1 (.IR(out_12), .D0_D7(D0_D7), .Address(out_16), .I(I), .Enable(1'b1));

  // Other names for the same wires on the sheet: AR_Output[11:0] = out_13; Decoded_Addr[15:0] = out_16;
  //   IR_Output[15:0] = out_12; MUX_Output[15:0] = out_11; S0 = MUX_Select_Lines[0]; S1 = MUX_Select_Lines[1];
  //   PC_Output[15:0] = out_10; ROM_Output[15:0] = out_9

  // Notes on the sheet:
  //   For T0,
  //   For T1,
  //   For T2,
  //   Indirect Addressing Mode : 002 -> 2008 Instruction
  //   Location of Data : 008 -> 0004
  //   Direct Addressing Mode : 000 -> 1004 Instruction
  //   Data : 004 -> 000A
  //   contents of rom_1 (hex, n*v repeats v):
  //   1004 0 2008 0 a 0 0 0 4
endmodule

module Reg_12bit (
  input  [11:0] Input,
  input  CLK,
  input  INC,
  input  LOAD,
  input  CLR,
  output [11:0] Output
);

  wire multiplexer_2_out;
  wire [11:0] adder_1_out, multiplexer_1_out;

  Adder #(.width(12)) adder_1 (.a(12'h1), .b(Output), .out(adder_1_out));  // open: cin, cout
  Multiplexer #(.width(12), .enable("false")) multiplexer_1 (
    .in0(Input), .in1(adder_1_out), .out(multiplexer_1_out), .sel(INC));
  Register #(.width(12)) register_1 (.D(multiplexer_1_out), .en(multiplexer_2_out), .Q(Output), .clk(CLK), .clr(CLR));
  Multiplexer #(.enable("false")) multiplexer_2 (.in0(LOAD), .in1(INC), .out(multiplexer_2_out), .sel(INC));
endmodule

module Reg_16bit (
  input  [15:0] Input,
  input  CLK,
  input  INC,
  input  LOAD,
  input  CLR,
  output [15:0] Output
);

  wire multiplexer_2_out;
  wire [15:0] adder_1_out, multiplexer_1_out;

  Adder #(.width(16)) adder_1 (.a(16'h1), .b(Output), .out(adder_1_out));  // open: cin, cout
  Multiplexer #(.width(16), .enable("false")) multiplexer_1 (
    .in0(Input), .in1(adder_1_out), .out(multiplexer_1_out), .sel(INC));
  Register #(.width(16)) register_1 (.D(multiplexer_1_out), .en(multiplexer_2_out), .Q(Output), .clk(CLK), .clr(CLR));
  Multiplexer #(.enable("false")) multiplexer_2 (.in0(LOAD), .in1(INC), .out(multiplexer_2_out), .sel(INC));
endmodule

module Program_Counter_PC (
  input  [15:0] INPUT,
  input  CLK,
  input  LOAD,
  input  INC,
  input  CLR,
  output [15:0] OUTPUT
);

  Reg_16bit reg_16bit_1 (.Input(INPUT), .Output(OUTPUT), .INC(INC), .LOAD(LOAD), .CLK(CLK), .CLR(CLR));
endmodule

module Instruction_Register_IR (
  input  [15:0] INPUT,
  input  CLK,
  input  LOAD,
  input  INC,
  input  CLR,
  output [15:0] OUTPUT
);

  Reg_16bit reg_16bit_1 (.Input(INPUT), .Output(OUTPUT), .INC(INC), .LOAD(LOAD), .CLK(CLK), .CLR(CLR));
endmodule

module Address_Register_AR (
  input  [11:0] INPUT,
  input  CLK,
  input  LOAD,
  input  INC,
  input  CLR,
  output [11:0] OUTPUT
);

  Reg_12bit reg_12bit_1 (.Input(INPUT), .Output(OUTPUT), .INC(INC), .LOAD(LOAD), .CLK(CLK), .CLR(CLR));
endmodule

module Timing_Signals_Generation_Circuit (
  input  Enable,
  input  CLR,
  input  CLK,
  input  INC,
  output T0,
  output T1,
  output T2,
  output T3,
  output T4,
  output T5,
  output T6,
  output T7,
  output T8,
  output T9,
  output T10,
  output T11,
  output T12,
  output T13,
  output T14,
  output T15
);

  wire [3:0] _4_Bit_Counter_q;

  Decoder #(.select(4)) decoder_1 (
    .out0(T0), .out1(T1), .out2(T2), .out3(T3), .out4(T4), .out5(T5), .out6(T6), .out7(T7), .out8(T8),
    .out9(T9), .out10(T10), .out11(T11), .out12(T12), .out13(T13), .out14(T14), .out15(T15),
    .sel(_4_Bit_Counter_q), .en(Enable));
  Counter #(.width(4), .max('hf), .trigger("falling")) _4_Bit_Counter (
    .count(INC), .Q(_4_Bit_Counter_q), .clk(CLK), .clr(CLR));  // open: load, D, carry
endmodule

module IR_Decoding_Circuit (
  input  [15:0] IR,
  input  Enable,
  output I,
  output [7:0] D0_D7,
  output [15:0] Address
);

  wire [2:0] controlled_buffer_2_out;

  assign I = Enable ? IR[15] : 1'bz;  // Controlled_Buffer controlled_buffer_1
  assign controlled_buffer_2_out = Enable ? IR[14:12] : 3'bz;  // Controlled_Buffer controlled_buffer_2
  Decoder #(.select(3), .enable("false")) decoder_1 (
    .out0(D0_D7[0]), .out1(D0_D7[1]), .out2(D0_D7[2]), .out3(D0_D7[3]), .out4(D0_D7[4]), .out5(D0_D7[5]),
    .out6(D0_D7[6]), .out7(D0_D7[7]), .sel(controlled_buffer_2_out));
  assign Address = Enable ? {4'b0000, IR[11:0]} : 16'bz;  // Controlled_Buffer controlled_buffer_3
endmodule
