// Logisim project Control Unit - II.circ as structural Verilog: 8 circuits, main circuit MultiBus
module MultiBus (
  input  Manual_CLK,
  input  in_2
);

  wire ACE, and_1_out, ARE, Automatic_CLK_out, D0, D0_T3, D0_T4, D0_T5, D1, D1_T3, D1_T4, D1_T5, D2, D2_T3,
       D2_T4, D3, DRE, IRE, not_1_out, or_2_out, R, S0, S2, SCLR, T2, T3, T4, T5;
  wire [3:1] S;
  wire [15:0] AC_q, AR_q, DR_q, Instruction_Decoder_address, IR_q, multiplexer_1_out, multiplexer_2_out,
       n16_bit_alu_1_output, PC_output, ram_1_data;

  T_States_Generator t_states_generator_1 (
    .T0(S2), .T1(IRE), .T2(T2), .T3(T3), .T4(T4), .T5(T5), .E(in_2), .CLR(SCLR), .CLK(or_2_out));  // open: T6, T7, INR
  Clock Automatic_CLK (.out(Automatic_CLK_out));
  Multiplexer #(.width(16)) multiplexer_1 (
    .in0(Instruction_Decoder_address), .in1(PC_output), .out(multiplexer_1_out), .sel(S2), .en(in_2));
  not not_1 (not_1_out, D3);
  and and_1 (and_1_out, not_1_out, Automatic_CLK_out);
  buf or_1 (S[3], D0_T4);  // OR_Gate
  Register #(.width(16)) AR (.D(multiplexer_1_out), .en(ARE), .Q(AR_q), .clk(or_2_out));  // open: clr
  PC_with_Incrementor PC (.Input(AR_q), .Output(PC_output), .S3(IRE), .E(IRE), .CLK(or_2_out));
  or or_2 (or_2_out, and_1_out, Manual_CLK);
  or or_3 (S0, IRE, D1_T3, D0_T3);
  or or_4 (R, IRE, D1_T3, D0_T3);
  Multiplexer #(.select(2), .width(16)) multiplexer_2 (
    .in0(PC_output), .in1(ram_1_data), .in2(AC_q), .out(multiplexer_2_out), .sel({1'b0, S0}), .en(in_2));  // open: in3
  or or_5 (S[1], D1_T4, D0_T4);
  RAM #(.addrWidth(16), .dataWidth(16), .bus("separate")) ram_1 (
    .addr(AR_q), .din(AC_q), .data(ram_1_data), .str(D2_T3), .sel(in_2), .clk(or_2_out), .ld(R));  // open: clr
  Register #(.width(16)) DR (.D(multiplexer_2_out), .en(DRE), .Q(DR_q), .clk(or_2_out));  // open: clr
  _16_bit_ALU u_16_bit_alu_1 (
    .Output(n16_bit_alu_1_output), .Input_A(DR_q), .Input_B(AC_q),
    .Input_Select({1'b0, S[3], 1'b0, S[1], 1'b0}));
  Register #(.width(16)) AC (.D(n16_bit_alu_1_output), .en(ACE), .Q(AC_q), .clk(or_2_out));  // open: clr
  or or_6 (SCLR, D2_T4, D1_T5, D0_T5);
  or or_7 (ACE, D1_T4, D0_T4);
  or or_8 (DRE, D1_T3, D0_T3);
  or or_9 (ARE, S2, T2);
  Register #(.width(16)) IR (.D(multiplexer_2_out), .en(IRE), .Q(IR_q), .clk(or_2_out));  // open: clr
  Instruction_Decoder Instruction_Decoder (
    .IR(IR_q), .D0_D3({D3, D2, D1, D0}), .Address(Instruction_Decoder_address), .Enable(in_2));
  and and_2 (D0_T3, D0, T3);
  and and_3 (D0_T4, D0, T4);
  and and_4 (D0_T5, D0, T5);
  and and_5 (D1_T3, D1, T3);
  and and_6 (D1_T4, D1, T4);
  and and_7 (D1_T5, D1, T5);
  and and_8 (D2_T3, D2, T3);
  and and_9 (D2_T4, D2, T4);

  // Other names for the same wires on the sheet: E = in_2; T0 = S2; PCE = IRE; S3 = IRE; T1 = IRE; W = D2_T3

  // Notes on the sheet:
  //   D0.T4 : AC <-- DR
  //   T-States
  //   LD 0005 : 
  //   D0.T3 : DR <-- MEM[AR]
  //   SC <-- 0
  //   Control Signals
  //   ADD 0006:
  //   D1.T3 : DR <-- MEM[AR]
  //   D1.T4 : AC <-- AC + DR
  //   SC <-- 0
  //   Here , every instruction will perform same operations till T2.
  //   After T2, Each instruction perform operations according to the instruction.
  //   To use load the Memory from the following instructions, and Enable the Circuit using E pin and turn the Clock on.
  //   Load the First Operand in A that is 0005 and Second Operand in B that is 0006
  //   ST 0007:
  //   D2.T3 : MEM[AR] <-- AC
  //   SC <-- 0
  //   PROGRAM
  //   LD A
  //   ADD B
  //   ST C
  //   PROGRAM
  //   LD 0005
  //   ADD 0006
  //   ST 0007
  //   HLT
  //   T0 : AR <-- PC
  //   T1 : IR <-- MEM[AR]
  //   PC <-- PC + 1
  //   T2 : D0 ... D3
  //   OPCODES
  //   D0 - 00 - LOAD - LD
  //   D1 - 01 - ADD
  //   D2 - 10 - STORE - ST
  //   --->
  //   0005
  //   4006
  //   --->
  //   --->
  //   8007
  //   C000
  //   --->
  //   A=0005, B=0006, C=0007
  //   Decoder(IR15-IR14)
  //   AR <-- IR (0-13)
  //   INSTRUCTIONS IN HEXADECIMAL
endmodule

module _16_bit_ALU (
  input  [15:0] Input_A,
  input  [15:0] Input_B,
  input  [4:0] Input_Select,
  output [15:0] Output
);

  wire [15:0] n16_bit_au_1_output, n16_bit_lu_1_output, n16_bit_su_1_output;

  _16_bit_AU u_16_bit_au_1 (
    .Cin(Input_Select[2]), .S0(Input_Select[4]), .S1(Input_Select[3]), .Input_A(Input_A), .Input_B(Input_B),
    .Output(n16_bit_au_1_output));  // open: C_out
  _16_bit_LU u_16_bit_lu_1 (
    .S0(Input_Select[4]), .S1(Input_Select[3]), .S2(Input_Select[2]), .Input_A(Input_A), .Input_B(Input_B),
    .Output(n16_bit_lu_1_output));
  _16_bit_SU u_16_bit_su_1 (.Input(Input_A), .Output(n16_bit_su_1_output), .S(Input_Select[2]));
  Multiplexer #(.select(2), .width(16), .enable("false")) multiplexer_1 (
    .in0({16{1'b0}}), .in1(n16_bit_au_1_output), .in2(n16_bit_lu_1_output), .in3(n16_bit_su_1_output),
    .out(Output), .sel({Input_Select[0], Input_Select[1]}));

  // Other names for the same wires on the sheet: S3 = Input_Select[1]; S4 = Input_Select[0]; S2 = Input_Select[2];
  //   S1 = Input_Select[3]; S0 = Input_Select[4]

  // Notes on the sheet:
  //   S0 S1 S2 S3 S4
  //   X    X    X    0    0
  //   0    0    0    1    0
  //   0    0    1    1    0
  //   1    0    1    1    0
  //   1    0    0    1    0
  //   0    1    1    1    0
  //   1    1    0    1    0
  //   0    1    0    1    0
  //   1    1    1    1    0
  //   0    0    0    0    1
  //   1    0    0    0    1
  //   0    1    0    0    1
  //   1    1    0    0    1
  //   0    0    1    0    1
  //   1    0    1    0    1
  //   0    1    1    0    1
  //   1    1    1    0    1
  //   X    X    0    1    1
  //   X    X    1    1    1
  //   SELECT BITS     |     OPERATIONS 
  //   |
  //   |
  //   |
  //   |
  //   |
  //   |
  //   |
  //   |
  //   |
  //   |
  //   |
  //   |
  //   |
  //   |
  //   |
  //   |
  //   |
  //   |
  //   |
  //   |
  //   |
  //   |
  //   |
  //   |
  //   |
  //   |
  //   |
  //   |
  //   |
  //   |
  //   |
  //   |
  //   |
  //   |
  //   O/P
  //   0
  //   A + B
  //   A + B + 1
  //   A - B
  //   A - B - 1
  //   A + 1
  //   A - 1
  //   A
  //   A
  //   A AND B
  //   A OR B
  //   A XOR B
  //   A'
  //   Selective Set
  //   Selective Clear
  //   Selective Complement
  //   Selective Mask
  //   Arithmetic Left Shift (*2)
  //   Arithmetic Right Shift (/2)
endmodule

module _16_bit_AU (
  input  Cin,
  input  S0,
  input  S1,
  input  [15:0] Input_A,
  input  [15:0] Input_B,
  output [15:0] Output,
  output C_out
);

  wire [15:0] multiplexer_1_out, not_1_out;

  assign not_1_out = ~Input_B;  // NOT_Gate not_1, 16 bits wide
  Multiplexer #(.select(2), .width(16), .enable("false")) multiplexer_1 (
    .in0(Input_B), .in1(not_1_out), .in2({16{1'b0}}), .in3({16{1'b1}}), .out(multiplexer_1_out),
    .sel({S1, S0}));
  Adder #(.width(16)) adder_1 (.a(Input_A), .b(multiplexer_1_out), .out(Output), .cin(Cin), .cout(C_out));
endmodule

module _16_bit_LU (
  input  S0,
  input  S1,
  input  S2,
  input  [15:0] Input_A,
  input  [15:0] Input_B,
  output [15:0] Output
);

  wire [15:0] and_1_out, and_2_out, not_1_out, not_2_out, or_1_out, undriven, xor_1_out;

  assign not_1_out = ~undriven;  // NOT_Gate not_1, 16 bits wide
  assign and_1_out = undriven & Input_B;  // AND_Gate and_1, 16 bits wide
  assign or_1_out = undriven | Input_B;  // OR_Gate or_1, 16 bits wide
  assign xor_1_out = Input_B ^ undriven;  // XOR_Gate xor_1, 16 bits wide
  assign and_2_out = undriven & not_2_out;  // AND_Gate and_2, 16 bits wide
  assign not_2_out = ~Input_B;  // NOT_Gate not_2, 16 bits wide
  Multiplexer #(.select(3), .width(16), .enable("false")) multiplexer_1 (
    .in0(and_1_out), .in1(or_1_out), .in2(xor_1_out), .in3(not_1_out), .in4(or_1_out), .in5(and_2_out),
    .in6(xor_1_out), .in7(and_1_out), .out(Output), .sel({S2, S1, S0}));
endmodule

module _16_bit_SU (
  input  [15:0] Input,
  input  S,
  output [15:0] Output
);

  wire [15:0] shifter_1_out, shifter_2_out;

  Shifter #(.width(16)) shifter_1 (.in(Input), .\dist (4'b0001), .out(shifter_1_out));
  Shifter #(.width(16), .shift("lr")) shifter_2 (.in(Input), .\dist (4'b0001), .out(shifter_2_out));
  Multiplexer #(.width(16), .enable("false")) multiplexer_1 (
    .in0(shifter_1_out), .in1(shifter_2_out), .out(Output), .sel(S));
endmodule

// I.D
module Instruction_Decoder (
  input  [15:0] IR,
  input  Enable,
  output [3:0] D0_D3,
  output [15:0] Address
);

  wire [1:0] controlled_buffer_1_out;

  assign controlled_buffer_1_out = Enable ? IR[15:14] : 2'bz;  // Controlled_Buffer controlled_buffer_1
  Decoder #(.select(2), .enable("false")) decoder_1 (
    .out0(D0_D3[0]), .out1(D0_D3[1]), .out2(D0_D3[2]), .out3(D0_D3[3]), .sel(controlled_buffer_1_out));
  assign Address = Enable ? {2'b00, IR[13:0]} : 16'bz;  // Controlled_Buffer controlled_buffer_2
endmodule

module PC_with_Incrementor (
  input  [15:0] Input,
  input  S3,
  input  E,
  input  CLK,
  output [15:0] Output
);

  wire [15:0] adder_1_out, multiplexer_1_out;

  Adder #(.width(16)) adder_1 (.a(Output), .b(16'h1), .out(adder_1_out));  // open: cin, cout
  Multiplexer #(.width(16)) multiplexer_1 (.in0(Input), .in1(adder_1_out), .out(multiplexer_1_out), .sel(S3), .en(E));
  Register #(.width(16)) register_1 (.D(multiplexer_1_out), .en(E), .Q(Output), .clk(CLK));  // open: clr

  // Notes on the sheet:
  //   PC=PC+1
endmodule

// T-States
module T_States_Generator (
  input  E,
  input  CLR,
  input  CLK,
  input  INR,
  output T0,
  output T1,
  output T2,
  output T3,
  output T4,
  output T5,
  output T6,
  output T7
);

  wire [2:0] counter_1_q;

  Decoder #(.select(3)) decoder_1 (
    .out0(T0), .out1(T1), .out2(T2), .out3(T3), .out4(T4), .out5(T5), .out6(T6), .out7(T7),
    .sel(counter_1_q), .en(E));
  Counter #(.width(3), .max('h7), .trigger("falling")) counter_1 (
    .count(INR), .Q(counter_1_q), .clk(CLK), .clr(CLR));  // open: load, D, carry
endmodule
