// Logisim project 2 Stage Pipelined Processor.circ as structural Verilog: 1 circuit, main circuit 2 Stage Pipelined Processor
module _2_Stage_Pipelined_Processor (
);

  wire CLK, d_ff_1_q, d_ff_2_q, MW;
  wire [15:0] A_B_q, A_q, adder_1_out, Addr_2_q, Addr_3_q, Addr_Counter_q, Addr_q, B_q, C_next_q, C_q,
       counter_1_q, rom_1_data, rom_2_data, rom_3_data, subtractor_1_out;

  Clock clock_1 (.out(CLK));
  Counter #(.width(16), .max('hc), .ongoal("stay")) Addr_Counter (
    .Q(Addr_Counter_q), .clk(CLK));  // open: load, D, count, carry, clr
  Register #(.width(16)) Addr (.D(Addr_Counter_q), .en(1'b1), .Q(Addr_q), .clk(CLK));  // open: clr
  Register #(.width(16)) Addr_2 (.D(Addr_Counter_q), .en(1'b1), .Q(Addr_2_q), .clk(CLK));  // open: clr
  Register #(.width(16)) Addr_3 (.D(Addr_Counter_q), .en(1'b1), .Q(Addr_3_q), .clk(CLK));  // open: clr
  D_Flip_Flop d_ff_1 (.clk(CLK), .D(1'b1), .Q(d_ff_1_q));  // open: Qn, preset, en, reset
  ROM #(.addrWidth(16), .dataWidth(16)) rom_1 (.addr(Addr_q), .data(rom_1_data), .sel(1'b1));
  ROM #(.addrWidth(16), .dataWidth(16)) rom_2 (.addr(Addr_2_q), .data(rom_2_data), .sel(1'b1));
  ROM #(.addrWidth(16), .dataWidth(16)) rom_3 (.addr(Addr_3_q), .data(rom_3_data), .sel(1'b1));
  D_Flip_Flop d_ff_2 (.clk(CLK), .D(d_ff_1_q), .Q(d_ff_2_q));  // open: Qn, preset, en, reset
  Register #(.width(16)) A (.D(rom_1_data), .en(1'b1), .Q(A_q), .clk(CLK));  // open: clr
  Register #(.width(16)) B (.D(rom_2_data), .en(1'b1), .Q(B_q), .clk(CLK));  // open: clr
  Register #(.width(16)) C (.D(rom_3_data), .en(1'b1), .Q(C_q), .clk(CLK));  // open: clr
  D_Flip_Flop d_ff_3 (.clk(CLK), .D(d_ff_2_q), .Q(MW));  // open: Qn, preset, en, reset
  Adder #(.width(16)) adder_1 (.a(A_q), .b(B_q), .out(adder_1_out));  // open: cin, cout
  Register #(.width(16)) A_B (.D(adder_1_out), .en(1'b1), .Q(A_B_q), .clk(CLK));  // open: clr
  Register #(.width(16)) C_next (.D(C_q), .en(1'b1), .Q(C_next_q), .clk(CLK));  // open: clr
  Counter #(.width(16), .max('hf), .ongoal("stay")) counter_1 (
    .count(MW), .Q(counter_1_q), .clk(CLK));  // open: load, D, carry, clr
  // Probe on subtractor_1_out
  Subtractor #(.width(16)) subtractor_1 (.a(A_B_q), .b(C_next_q), .out(subtractor_1_out));  // open: bin, bout
  RAM #(.addrWidth(16), .dataWidth(16), .bus("separate")) ram_1 (
    .addr(counter_1_q), .din(subtractor_1_out), .str(MW), .sel(1'b1), .clk(CLK));  // open: data, ld, clr

  // Notes on the sheet:
  //   A
  //   B
  //   C
  //   Array of Integers
  //   contents of rom_1 (hex, n*v repeats v):
  //   1 2 3 4 5 6 7 8 9 10 11 12 a b c d
  //   contents of rom_2 (hex, n*v repeats v):
  //   154 21 5 41 7 87 712 82 914 1012 1112 122 a1 b2 c2 d3
  //   contents of rom_3 (hex, n*v repeats v):
  //   6 9 4 5 7 14 45 24 123 12 45 145 a b c d
  //   D
  //   D [ i ] = ( A [ i ] + B [ i ] ) - C [ i ]
endmodule
