// Logisim project 4 Core Parallel Processor.circ as structural Verilog: 2 circuits, main circuit 4 Core Parallel Processor
module _4_Core_Parallel_Processor (
);

  wire and_1_out, and_3_out, C1, C2, C3, C4, CLK, CLK_Enable, clock_1_out, d_ff_1_q, d_ff_3_q, d_ff_4_q,
       decoder_1_out0, decoder_1_out1, decoder_1_out2, decoder_1_out3, MW, RESET, ROM_SEL;
  wire [1:0] counter_2_q_2;
  wire [3:0] counter_1_q;
  wire [15:0] Address_Counter_q, C1_Out, C2_Out, C3_Out, C4_Out, core_1_a_2, core_1_b_2, core_1_c_2,
       core_2_a_2, core_2_b_2, core_2_c_2, core_3_a_2, core_3_b_2, core_3_c_2, core_4_a_2, core_4_b_2,
       core_4_c_2, counter_2_q, multiplexer_1_out, pull_resistor_1_node, pull_resistor_2_node, rom_3_data,
       Total_Cycle_Count_q;

  Clock clock_1 (.out(clock_1_out));
  Counter #(.width(16), .max('hffff)) Total_Cycle_Count (
    .Q(Total_Cycle_Count_q), .clk(CLK));  // open: load, D, count, carry, clr
  // Probe on Total_Cycle_Count_q
  Counter #(.width(16), .max('hc)) Address_Counter (
    .Q(Address_Counter_q), .clk(CLK));  // open: load, D, count, carry, clr
  and and_1 (and_1_out, Address_Counter_q[2], Address_Counter_q[3]);
  and and_2 (CLK, clock_1_out, CLK_Enable);
  D_Flip_Flop d_ff_1 (.clk(and_1_out), .D(1'b1), .Q(d_ff_1_q), .Qn(ROM_SEL));  // open: preset, en, reset
  Counter #(.width(4), .max('hb)) counter_1 (
    .Q(counter_1_q), .clk(CLK), .clr(d_ff_4_q));  // open: load, D, count, carry
  and and_3 (and_3_out, ~counter_1_q[0], counter_1_q[1], ~counter_1_q[2], ~counter_1_q[3], d_ff_1_q);  // AND_Gate
  Pull_Resistor pull_resistor_1 (.node(pull_resistor_1_node));
  ROM #(.addrWidth(16), .dataWidth(16)) rom_1 (.addr(Address_Counter_q), .data(pull_resistor_1_node));  // open: sel
  Pull_Resistor pull_resistor_2 (.node(pull_resistor_2_node));
  ROM #(.addrWidth(16), .dataWidth(16)) rom_2 (.addr(Address_Counter_q), .data(pull_resistor_2_node));  // open: sel
  ROM #(.addrWidth(16), .dataWidth(16)) rom_3 (.addr(Address_Counter_q), .data(rom_3_data));  // open: sel
  Pull_Resistor pull_resistor_3 (.node(rom_3_data));
  Decoder #(.select(2), .enable("false")) decoder_1 (
    .out0(decoder_1_out0), .out1(decoder_1_out1), .out2(decoder_1_out2), .out3(decoder_1_out3),
    .sel(counter_1_q[1:0]));
  D_Flip_Flop d_ff_2 (.clk(and_3_out), .D(1'b1), .Q(MW));  // open: Qn, preset, en, reset
  // Probe on core_1_c_2
  // Probe on core_1_b_2
  // Probe on core_1_a_2
  // Probe on core_2_c_2
  // Probe on core_2_b_2
  // Probe on core_2_a_2
  nor nor_1 (RESET, ROM_SEL, MW);
  // Probe on C1_Out
  Core core_1 (
    .in_4(CLK), .in_5(C1), .A(pull_resistor_1_node), .B(pull_resistor_2_node), .C(rom_3_data),
    .D__A_B__C(C1_Out), .A_2(core_1_a_2), .B_2(core_1_b_2), .C_2(core_1_c_2));
  // Probe on C3_Out
  Core core_2 (
    .in_4(CLK), .in_5(C3), .A(pull_resistor_1_node), .B(pull_resistor_2_node), .C(rom_3_data),
    .D__A_B__C(C3_Out), .A_2(core_2_a_2), .B_2(core_2_b_2), .C_2(core_2_c_2));
  or or_1 (C1, decoder_1_out0, RESET);
  or or_2 (C2, decoder_1_out1, RESET);
  or or_3 (C3, RESET, decoder_1_out2);
  or or_4 (C4, RESET, decoder_1_out3);
  D_Flip_Flop d_ff_3 (.clk(CLK), .D(RESET), .Q(d_ff_3_q), .reset(d_ff_4_q));  // open: Qn, preset, en
  // Probe on core_3_b_2
  // Probe on core_3_a_2
  // Probe on core_4_b_2
  // Probe on core_4_a_2
  D_Flip_Flop d_ff_4 (.clk(CLK), .D(d_ff_3_q), .Q(d_ff_4_q), .reset(d_ff_4_q));  // open: Qn, preset, en
  // Probe on core_3_c_2
  Core core_3 (
    .in_4(CLK), .in_5(C2), .A(pull_resistor_1_node), .B(pull_resistor_2_node), .C(rom_3_data),
    .D__A_B__C(C2_Out), .A_2(core_3_a_2), .B_2(core_3_b_2), .C_2(core_3_c_2));
  // Probe on core_4_c_2
  Core core_4 (
    .in_4(CLK), .in_5(C4), .A(pull_resistor_1_node), .B(pull_resistor_2_node), .C(rom_3_data),
    .D__A_B__C(C4_Out), .A_2(core_4_a_2), .B_2(core_4_b_2), .C_2(core_4_c_2));
  Multiplexer #(.select(2), .width(16), .enable("false")) multiplexer_1 (
    .in0(C1_Out), .in1(C2_Out), .in2(C3_Out), .in3(C4_Out), .out(multiplexer_1_out), .sel(counter_1_q[1:0]));
  Counter #(.width(16), .max('hffff)) counter_2 (
    .count(MW), .Q({counter_2_q[15:4], counter_2_q_2, counter_2_q[1:0]}), .clk(CLK));  // open: load, D, carry, clr
  // Probe on C2_Out
  // Probe on C4_Out
  nand nand_1 (CLK_Enable, counter_2_q_2[0], counter_2_q_2[1]);
  RAM #(.addrWidth(16), .dataWidth(16), .bus("separate")) ram_1 (
    .addr({counter_2_q[15:4], counter_2_q_2, counter_2_q[1:0]}), .din(multiplexer_1_out), .str(MW),
    .sel(1'b1), .clk(CLK));  // open: data, ld, clr

  // Notes on the sheet:
  //   A
  //   B
  //   C
  //   Array of Integers
  //   contents of rom_1 (hex, n*v repeats v):
  //   1 2 3 4 5 6 7 8 9 10 11 12
  //   contents of rom_2 (hex, n*v repeats v):
  //   12 34 56 67 78 89 90 1 21 32 43 54
  //   contents of rom_3 (hex, n*v repeats v):
  //   11 22 33 19 28 37 45 61 32 43 28 39
  //   D
  //   D[ i ] = ( A[ i ] + B[ i ] ) - C[ i ]
endmodule

module Core (
  input  [15:0] A,
  input  [15:0] B,
  input  [15:0] C,
  input  in_4,
  input  in_5,
  output [15:0] A_2,
  output [15:0] B_2,
  output [15:0] C_2,
  output [15:0] D__A_B__C
);

  wire [15:0] A_2_q, A_3_q, A_B_q, adder_1_out, B_2_q, B_3_q, C_2_q, C_3_q, C_next_q, subtractor_1_out;

  Register #(.width(16)) u_A (.D(A), .en(in_5), .Q(A_2), .clk(in_4));  // open: clr
  Register #(.width(16)) u_B (.D(B), .en(in_5), .Q(B_2), .clk(in_4));  // open: clr
  Register #(.width(16)) u_C (.D(C), .en(in_5), .Q(C_2), .clk(in_4));  // open: clr
  Register #(.width(16)) u_A_2 (.D(A_2), .en(in_5), .Q(A_2_q), .clk(in_4));  // open: clr
  Register #(.width(16)) u_B_2 (.D(B_2), .en(in_5), .Q(B_2_q), .clk(in_4));  // open: clr
  Register #(.width(16)) u_C_2 (.D(C_2), .en(in_5), .Q(C_2_q), .clk(in_4));  // open: clr
  Register #(.width(16)) A_3 (.D(A_2_q), .en(in_5), .Q(A_3_q), .clk(in_4));  // open: clr
  Register #(.width(16)) B_3 (.D(B_2_q), .en(in_5), .Q(B_3_q), .clk(in_4));  // open: clr
  Register #(.width(16)) C_3 (.D(C_2_q), .en(in_5), .Q(C_3_q), .clk(in_4));  // open: clr
  Adder #(.width(16)) adder_1 (.a(A_3_q), .b(B_3_q), .out(adder_1_out));  // open: cin, cout
  Register #(.width(16)) A_B (.D(adder_1_out), .en(in_5), .Q(A_B_q), .clk(in_4));  // open: clr
  Register #(.width(16)) C_next (.D(C_3_q), .en(in_5), .Q(C_next_q), .clk(in_4));  // open: clr
  Subtractor #(.width(16)) subtractor_1 (.a(A_B_q), .b(C_next_q), .out(subtractor_1_out));  // open: bin, bout
  Register #(.width(16)) D (.D(subtractor_1_out), .en(in_5), .Q(D__A_B__C), .clk(in_4));  // open: clr

  // Other names for the same wires on the sheet: CLK = in_4; LD = in_5
endmodule
