// Logisim project 64 Bit Hierarchical CLA Short.circ as structural Verilog: 8 circuits, main circuit 1 Bit Full Adder
module _1_Bit_Full_Adder (
  input  A,
  input  B,
  input  Cin,
  output P,
  output G,
  output Cout
);

  wire AND_2_out;

  xor XOR (P, A, B);
  and AND (G, A, B);
  and AND_2 (AND_2_out, P, Cin);
  or OR (Cout, G, AND_2_out);
endmodule

module _4_bit_CLG (
  input  A3,
  input  B3,
  input  A2,
  input  B2,
  input  A1,
  input  B1,
  input  A0,
  input  B0,
  input  C0,
  output C4,
  output P,
  output G,
  output C3,
  output C2,
  output C1,
  output C0_2,
  output P3,
  output P2,
  output P1,
  output P0
);

  wire AND_2_out, AND_3_out, AND_4_out, n1_bit_full_adder_1_g, n1_bit_full_adder_2_g, n1_bit_full_adder_3_g,
       n1_bit_full_adder_4_g;

  and AND (P, P3, P2, P1, P0);
  or OR (G, n1_bit_full_adder_1_g, AND_2_out, AND_3_out, AND_4_out);
  _1_Bit_Full_Adder u_1_bit_full_adder_1 (.A(A3), .B(B3), .Cin(C3), .P(P3), .G(n1_bit_full_adder_1_g), .Cout(C4));
  and AND_2 (AND_2_out, P3, n1_bit_full_adder_2_g);
  _1_Bit_Full_Adder u_1_bit_full_adder_2 (.A(A2), .B(B2), .Cin(C2), .P(P2), .G(n1_bit_full_adder_2_g), .Cout(C3));
  _1_Bit_Full_Adder u_1_bit_full_adder_3 (.A(A1), .B(B1), .Cin(C1), .P(P1), .G(n1_bit_full_adder_3_g), .Cout(C2));
  and AND_3 (AND_3_out, P3, P2, n1_bit_full_adder_3_g);
  _1_Bit_Full_Adder u_1_bit_full_adder_4 (.A(A0), .B(B0), .Cin(C0), .P(P0), .G(n1_bit_full_adder_4_g), .Cout(C1));
  and AND_4 (AND_4_out, P3, P2, P1, n1_bit_full_adder_4_g);

  assign C0_2 = C0;
endmodule

module _1_bit_GP_CLG (
  input  G,
  input  P,
  input  Cin,
  output Cout
);

  wire AND_out;

  and AND (AND_out, P, Cin);
  or OR (Cout, G, AND_out);
endmodule

module _4_bit_GP_CLG (
  input  C0,
  input  G3,
  input  P3,
  input  G2,
  input  P2,
  input  G1,
  input  P1,
  input  G0,
  input  P0,
  output C16,
  output C12,
  output C8,
  output C4
);

  _1_bit_GP_CLG u_1_bit_gp_clg_1 (.G(G3), .P(P3), .Cin(C12), .Cout(C16));
  _1_bit_GP_CLG u_1_bit_gp_clg_2 (.G(G2), .P(P2), .Cin(C8), .Cout(C12));
  _1_bit_GP_CLG u_1_bit_gp_clg_3 (.G(G1), .P(P1), .Cin(C4), .Cout(C8));
  _1_bit_GP_CLG u_1_bit_gp_clg_4 (.G(G0), .P(P0), .Cin(C0), .Cout(C4));
endmodule

module _4_bit_GP_CLA (
  input  B3,
  input  A3,
  input  B2,
  input  A2,
  input  B1,
  input  A1,
  input  B0,
  input  A0,
  input  C0,
  output P,
  output G,
  output S3,
  output S2,
  output S1,
  output S0
);

  wire n4_bit_clg_1_c0_2, n4_bit_clg_1_c1, n4_bit_clg_1_c2, n4_bit_clg_1_c3, n4_bit_clg_1_p0,
       n4_bit_clg_1_p1, n4_bit_clg_1_p2, n4_bit_clg_1_p3;

  _4_bit_CLG u_4_bit_clg_1 (
    .P(P), .G(G), .C3(n4_bit_clg_1_c3), .C2(n4_bit_clg_1_c2), .C1(n4_bit_clg_1_c1), .C0_2(n4_bit_clg_1_c0_2),
    .P3(n4_bit_clg_1_p3), .P2(n4_bit_clg_1_p2), .P1(n4_bit_clg_1_p1), .P0(n4_bit_clg_1_p0), .A3(A3), .B3(B3),
    .A2(A2), .B2(B2), .A1(A1), .B1(B1), .A0(A0), .B0(B0), .C0(C0));  // open: C4
  xor xor_1 (S3, n4_bit_clg_1_p3, n4_bit_clg_1_c3);
  xor xor_2 (S2, n4_bit_clg_1_p2, n4_bit_clg_1_c2);
  xor xor_3 (S0, n4_bit_clg_1_p0, n4_bit_clg_1_c0_2);
  xor xor_4 (S1, n4_bit_clg_1_p1, n4_bit_clg_1_c1);
endmodule

module _4_bit_GP___CLG (
  input  C0,
  input  G3,
  input  P3,
  input  G2,
  input  P2,
  input  G1,
  input  P1,
  input  G0,
  input  P0,
  output C16,
  output C12,
  output C8,
  output C4,
  output G,
  output P
);

  wire AND_2_out, AND_3_out, AND_4_out;

  and AND (P, P3, P2, P1, P0);
  or OR (G, G3, AND_2_out, AND_3_out, AND_4_out);
  and AND_2 (AND_2_out, P3, G2);
  _4_bit_GP_CLG u_4_bit_gp_clg_1 (
    .C16(C16), .C0(C0), .G3(G3), .P3(P3), .C12(C12), .G2(G2), .P2(P2), .C8(C8), .G1(G1), .P1(P1), .C4(C4),
    .G0(G0), .P0(P0));
  and AND_3 (AND_3_out, P3, P2, G1);
  and AND_4 (AND_4_out, P3, P2, P1, G0);
endmodule

module _16_bit_GP_CLG (
  input  [15:0] A0_15,
  input  [15:0] B0_15,
  input  C0,
  output G,
  output P,
  output [15:0] S0_15
);

  wire n4_bit_gp_cla_1_g, n4_bit_gp_cla_1_p, n4_bit_gp_cla_2_g, n4_bit_gp_cla_2_p, n4_bit_gp_cla_3_g,
       n4_bit_gp_cla_3_p, n4_bit_gp_cla_4_g, n4_bit_gp_cla_4_p, n4_bit_gp_clg_1_c4, n4_bit_gp_clg_1_c8,
       n4_bit_gp_clg_1_c12;

  _4_bit_GP_CLA u_4_bit_gp_cla_1 (
    .B3(B0_15[15]), .A3(A0_15[15]), .B2(B0_15[14]), .B1(B0_15[13]), .A1(A0_15[13]), .B0(B0_15[12]),
    .A0(A0_15[12]), .C0(n4_bit_gp_clg_1_c12), .P(n4_bit_gp_cla_1_p), .G(n4_bit_gp_cla_1_g), .S3(S0_15[15]),
    .S2(S0_15[14]), .S1(S0_15[13]), .S0(S0_15[12]), .A2(A0_15[14]));
  _4_bit_GP_CLA u_4_bit_gp_cla_2 (
    .B3(B0_15[11]), .A3(A0_15[11]), .B2(B0_15[10]), .B1(B0_15[9]), .A1(A0_15[9]), .B0(B0_15[8]),
    .A0(A0_15[8]), .C0(n4_bit_gp_clg_1_c8), .P(n4_bit_gp_cla_2_p), .G(n4_bit_gp_cla_2_g), .S3(S0_15[11]),
    .S2(S0_15[10]), .S1(S0_15[9]), .S0(S0_15[8]), .A2(A0_15[10]));
  _4_bit_GP_CLA u_4_bit_gp_cla_3 (
    .B3(B0_15[7]), .A3(A0_15[7]), .B2(B0_15[6]), .B1(B0_15[5]), .A1(A0_15[5]), .B0(B0_15[4]), .A0(A0_15[4]),
    .C0(n4_bit_gp_clg_1_c4), .P(n4_bit_gp_cla_3_p), .G(n4_bit_gp_cla_3_g), .S3(S0_15[7]), .S2(S0_15[6]),
    .S1(S0_15[5]), .S0(S0_15[4]), .A2(A0_15[6]));
  _4_bit_GP___CLG u_4_bit_gp_clg_1 (
    .C0(C0), .G(G), .P(P), .P3(n4_bit_gp_cla_1_p), .C12(n4_bit_gp_clg_1_c12), .G2(n4_bit_gp_cla_2_g),
    .P2(n4_bit_gp_cla_2_p), .C8(n4_bit_gp_clg_1_c8), .G1(n4_bit_gp_cla_3_g), .P1(n4_bit_gp_cla_3_p),
    .C4(n4_bit_gp_clg_1_c4), .G0(n4_bit_gp_cla_4_g), .P0(n4_bit_gp_cla_4_p), .G3(n4_bit_gp_cla_1_g));  // open: C16
  _4_bit_GP_CLA u_4_bit_gp_cla_4 (
    .B3(B0_15[3]), .A3(A0_15[3]), .B2(B0_15[2]), .B1(B0_15[1]), .A1(A0_15[1]), .B0(B0_15[0]), .A0(A0_15[0]),
    .C0(C0), .P(n4_bit_gp_cla_4_p), .G(n4_bit_gp_cla_4_g), .S3(S0_15[3]), .S2(S0_15[2]), .S1(S0_15[1]),
    .S0(S0_15[0]), .A2(A0_15[2]));
endmodule

module _64_bit_CLA (
  input  [15:0] A63_48,
  input  [15:0] B63_48,
  input  [15:0] A47_32,
  input  [15:0] B47_32,
  input  [15:0] A31_16,
  input  [15:0] B31_16,
  input  [15:0] A15_0,
  input  [15:0] B15_0,
  input  C0,
  output [15:0] S63_48,
  output [15:0] S47_32,
  output [15:0] S31_16,
  output [15:0] S15_0,
  output C16,
  output G,
  output P
);

  wire n4_bit_gp_clg_1_c4, n4_bit_gp_clg_1_c8, n4_bit_gp_clg_1_c12, n16_bit_gp_clg_1_g, n16_bit_gp_clg_1_p,
       n16_bit_gp_clg_2_g, n16_bit_gp_clg_2_p, n16_bit_gp_clg_3_g, n16_bit_gp_clg_3_p, n16_bit_gp_clg_4_g,
       n16_bit_gp_clg_4_p;

  _16_bit_GP_CLG u_16_bit_gp_clg_1 (
    .C0(n4_bit_gp_clg_1_c12), .G(n16_bit_gp_clg_1_g), .P(n16_bit_gp_clg_1_p), .S0_15(S63_48), .A0_15(B63_48),
    .B0_15(A63_48));
  _16_bit_GP_CLG u_16_bit_gp_clg_2 (
    .C0(n4_bit_gp_clg_1_c8), .G(n16_bit_gp_clg_2_g), .P(n16_bit_gp_clg_2_p), .S0_15(S47_32), .A0_15(B47_32),
    .B0_15(A47_32));
  _4_bit_GP___CLG u_4_bit_gp_clg_1 (
    .C16(C16), .C0(C0), .G(G), .P(P), .P3(n16_bit_gp_clg_1_p), .C12(n4_bit_gp_clg_1_c12),
    .G2(n16_bit_gp_clg_2_g), .P2(n16_bit_gp_clg_2_p), .C8(n4_bit_gp_clg_1_c8), .G1(n16_bit_gp_clg_3_g),
    .P1(n16_bit_gp_clg_3_p), .C4(n4_bit_gp_clg_1_c4), .G0(n16_bit_gp_clg_4_g), .P0(n16_bit_gp_clg_4_p),
    .G3(n16_bit_gp_clg_1_g));
  _16_bit_GP_CLG u_16_bit_gp_clg_3 (
    .C0(n4_bit_gp_clg_1_c4), .G(n16_bit_gp_clg_3_g), .P(n16_bit_gp_clg_3_p), .S0_15(S31_16), .A0_15(B31_16),
    .B0_15(A31_16));
  _16_bit_GP_CLG u_16_bit_gp_clg_4 (
    .C0(C0), .G(n16_bit_gp_clg_4_g), .P(n16_bit_gp_clg_4_p), .S0_15(S15_0), .A0_15(B15_0), .B0_15(A15_0));
endmodule
