// Logisim project CLA.circ as structural Verilog
module Carry_Look_Ahead_Generator (
  input  C0,
  input  G0,
  input  G1,
  input  G2,
  input  G3,
  input  P0,
  input  P1,
  input  P2,
  input  P3,
  output C0_2,
  output C1,
  output C2,
  output C3,
  output C4,
  output P0_2,
  output P1_2,
  output P2_2,
  output P3_2
);

  wire and_1_out, and_2_out, and_3_out, and_4_out, and_5_out, and_6_out, and_7_out, and_8_out, and_9_out,
       or_2_out;

  and and_1 (and_1_out, P0, C0);
  and and_2 (and_2_out, P2, P1, P0, C0);
  and and_3 (and_3_out, P3, P2, P1, P0, C0);
  or or_1 (C1, and_1_out, G0);
  or or_2 (or_2_out, and_1_out, G0);
  and and_4 (and_4_out, P1, P2, G0);
  and and_5 (and_5_out, or_2_out, P1);
  and and_6 (and_6_out, G1, P2);
  and and_7 (and_7_out, P3, P2, P1, G0);
  and and_8 (and_8_out, G1, P2, P3);
  and and_9 (and_9_out, P2, P3);
  or or_3 (C2, and_5_out, G1);
  or or_4 (C3, and_2_out, and_4_out, and_6_out, G2);
  or or_5 (C4, and_3_out, and_7_out, and_8_out, and_9_out, G3);

  assign C0_2 = C0;
  assign P0_2 = P0;
  assign P1_2 = P1;
  assign P2_2 = P2;
  assign P3_2 = P3;
endmodule

module G_and_P_Generator (
  input  A0,
  input  B0,
  input  A1,
  input  B1,
  input  A2,
  input  B2,
  input  A3,
  input  B3,
  output P0,
  output G0,
  output P1,
  output G1,
  output P2,
  output G2,
  output P3,
  output G3
);

  GP gp_1 (.A(A0), .B(B0), .P(P0), .G(G0));
  GP gp_2 (.A(A1), .B(B1), .P(P1), .G(G1));
  GP gp_3 (.A(A2), .B(B2), .P(P2), .G(G2));
  GP gp_4 (.A(A3), .B(B3), .P(P3), .G(G3));

  // Notes on the sheet:
  //   G and P Generator
endmodule

module _4_bit_CLA (
  input  B3,
  input  A3,
  input  B2,
  input  A2,
  input  B1,
  input  A1,
  input  B0,
  input  A0,
  input  C0,
  output C4,
  output S3,
  output S2,
  output S1,
  output S0
);

  wire carry_look_ahead_generator_1_c0_2, carry_look_ahead_generator_1_c1, carry_look_ahead_generator_1_c2,
       carry_look_ahead_generator_1_c3, carry_look_ahead_generator_1_p0_2, carry_look_ahead_generator_1_p1_2,
       carry_look_ahead_generator_1_p2_2, carry_look_ahead_generator_1_p3_2, g_and_p_generator_1_g0,
       g_and_p_generator_1_g1, g_and_p_generator_1_g2, g_and_p_generator_1_g3, g_and_p_generator_1_p0,
       g_and_p_generator_1_p1, g_and_p_generator_1_p2, g_and_p_generator_1_p3;

  xor XOR (S3, carry_look_ahead_generator_1_p3_2, carry_look_ahead_generator_1_c3);
  xor XOR_2 (S2, carry_look_ahead_generator_1_p2_2, carry_look_ahead_generator_1_c2);
  G_and_P_Generator g_and_p_generator_1 (
    .A0(A0), .B0(B0), .A1(A1), .B1(B1), .A2(A2), .B2(B2), .A3(A3), .B3(B3), .G0(g_and_p_generator_1_g0),
    .G1(g_and_p_generator_1_g1), .P2(g_and_p_generator_1_p2), .G2(g_and_p_generator_1_g2),
    .P1(g_and_p_generator_1_p1), .P0(g_and_p_generator_1_p0), .G3(g_and_p_generator_1_g3),
    .P3(g_and_p_generator_1_p3));
  Carry_Look_Ahead_Generator carry_look_ahead_generator_1 (
    .C0(C0), .G1(g_and_p_generator_1_g1), .G2(g_and_p_generator_1_g2), .G3(g_and_p_generator_1_g3),
    .P0(g_and_p_generator_1_p0), .P1(g_and_p_generator_1_p1), .P2(g_and_p_generator_1_p2),
    .G0(g_and_p_generator_1_g0), .P3(g_and_p_generator_1_p3), .C1(carry_look_ahead_generator_1_c1), .C4(C4),
    .C2(carry_look_ahead_generator_1_c2), .C3(carry_look_ahead_generator_1_c3),
    .P0_2(carry_look_ahead_generator_1_p0_2), .P1_2(carry_look_ahead_generator_1_p1_2),
    .P2_2(carry_look_ahead_generator_1_p2_2), .P3_2(carry_look_ahead_generator_1_p3_2),
    .C0_2(carry_look_ahead_generator_1_c0_2));
  xor XOR_3 (S1, carry_look_ahead_generator_1_p1_2, carry_look_ahead_generator_1_c1);
  xor XOR_4 (S0, carry_look_ahead_generator_1_p0_2, carry_look_ahead_generator_1_c0_2);
endmodule

module _16_bit_CLA (
  input  C0,
  input  B15,
  input  A15,
  input  B14,
  input  A14,
  input  B13,
  input  A13,
  input  B12,
  input  A12,
  input  B11,
  input  A11,
  input  B10,
  input  A10,
  input  B9,
  input  A9,
  input  B8,
  input  A8,
  input  B7,
  input  A7,
  input  B6,
  input  A6,
  input  B5,
  input  A5,
  input  B4,
  input  A4,
  input  B3,
  input  A3,
  input  B2,
  input  A2,
  input  B1,
  input  A1,
  input  B0,
  input  A0,
  output C16,
  output S15,
  output S14,
  output S13,
  output S12,
  output S11,
  output S10,
  output S9,
  output S8,
  output S7,
  output S6,
  output S5,
  output S4,
  output S3,
  output S2,
  output S1,
  output S0
);

  wire n4_bit_clg_1_c0_2, n4_bit_clg_1_c1, n4_bit_clg_1_c2, n4_bit_clg_1_c3, n4_bit_clg_1_g, n4_bit_clg_1_p,
       n4_bit_clg_1_p0, n4_bit_clg_1_p1, n4_bit_clg_1_p2, n4_bit_clg_1_p3, n4_bit_clg_2_c0_2,
       n4_bit_clg_2_c1, n4_bit_clg_2_c2, n4_bit_clg_2_c3, n4_bit_clg_2_g, n4_bit_clg_2_p, n4_bit_clg_2_p0,
       n4_bit_clg_2_p1, n4_bit_clg_2_p2, n4_bit_clg_2_p3, n4_bit_clg_3_c0_2, n4_bit_clg_3_c1,
       n4_bit_clg_3_c2, n4_bit_clg_3_c3, n4_bit_clg_3_g, n4_bit_clg_3_p, n4_bit_clg_3_p0, n4_bit_clg_3_p1,
       n4_bit_clg_3_p2, n4_bit_clg_3_p3, n4_bit_clg_4_c0_2, n4_bit_clg_4_c1, n4_bit_clg_4_c2,
       n4_bit_clg_4_c3, n4_bit_clg_4_g, n4_bit_clg_4_p, n4_bit_clg_4_p0, n4_bit_clg_4_p1, n4_bit_clg_4_p2,
       n4_bit_clg_4_p3, n4_bit_gp_clg_1_c4, n4_bit_gp_clg_1_c8, n4_bit_gp_clg_1_c12;

  _4_bit_CLG u_4_bit_clg_1 (
    .P(n4_bit_clg_1_p), .G(n4_bit_clg_1_g), .C3(n4_bit_clg_1_c3), .C2(n4_bit_clg_1_c2), .C1(n4_bit_clg_1_c1),
    .C0_2(n4_bit_clg_1_c0_2), .P3(n4_bit_clg_1_p3), .P2(n4_bit_clg_1_p2), .P1(n4_bit_clg_1_p1),
    .P0(n4_bit_clg_1_p0), .A3(A15), .B3(B15), .A2(A14), .B2(B14), .A1(A13), .B1(B13), .A0(A12), .B0(B12),
    .C0(n4_bit_gp_clg_1_c12));  // open: C4
  Small_XOR small_xor_1 (.A(n4_bit_clg_1_c1), .B(n4_bit_clg_1_p1), .S(S13));
  Small_XOR small_xor_2 (.A(n4_bit_clg_1_c2), .B(n4_bit_clg_1_p2), .S(S14));
  Small_XOR small_xor_3 (.A(n4_bit_clg_1_c3), .B(n4_bit_clg_1_p3), .S(S15));
  Small_XOR small_xor_4 (.A(n4_bit_clg_1_c0_2), .B(n4_bit_clg_1_p0), .S(S12));
  _4_bit_CLG u_4_bit_clg_2 (
    .P(n4_bit_clg_2_p), .G(n4_bit_clg_2_g), .C3(n4_bit_clg_2_c3), .C2(n4_bit_clg_2_c2), .C1(n4_bit_clg_2_c1),
    .C0_2(n4_bit_clg_2_c0_2), .P3(n4_bit_clg_2_p3), .P2(n4_bit_clg_2_p2), .P1(n4_bit_clg_2_p1),
    .P0(n4_bit_clg_2_p0), .A3(A11), .B3(B11), .A2(A10), .B2(B10), .A1(A9), .B1(B9), .A0(A8), .B0(B8),
    .C0(n4_bit_gp_clg_1_c8));  // open: C4
  Small_XOR small_xor_5 (.A(n4_bit_clg_2_c3), .B(n4_bit_clg_2_p3), .S(S11));
  Small_XOR small_xor_6 (.A(n4_bit_clg_2_c2), .B(n4_bit_clg_2_p2), .S(S10));
  Small_XOR small_xor_7 (.A(n4_bit_clg_2_c1), .B(n4_bit_clg_2_p1), .S(S9));
  Small_XOR small_xor_8 (.A(n4_bit_clg_2_c0_2), .B(n4_bit_clg_2_p0), .S(S8));
  _4_bit_GP_CLG u_4_bit_gp_clg_1 (
    .C16(C16), .C0(C0), .G3(n4_bit_clg_1_g), .P3(n4_bit_clg_1_p), .C12(n4_bit_gp_clg_1_c12),
    .G2(n4_bit_clg_2_g), .P2(n4_bit_clg_2_p), .C8(n4_bit_gp_clg_1_c8), .G1(n4_bit_clg_3_g),
    .P1(n4_bit_clg_3_p), .C4(n4_bit_gp_clg_1_c4), .G0(n4_bit_clg_4_g), .P0(n4_bit_clg_4_p));
  _4_bit_CLG u_4_bit_clg_3 (
    .P(n4_bit_clg_3_p), .G(n4_bit_clg_3_g), .C3(n4_bit_clg_3_c3), .C2(n4_bit_clg_3_c2), .C1(n4_bit_clg_3_c1),
    .C0_2(n4_bit_clg_3_c0_2), .P3(n4_bit_clg_3_p3), .P2(n4_bit_clg_3_p2), .P1(n4_bit_clg_3_p1),
    .P0(n4_bit_clg_3_p0), .A3(A7), .B3(B7), .A2(A6), .B2(B6), .A1(A5), .B1(B5), .A0(A4), .B0(B4),
    .C0(n4_bit_gp_clg_1_c4));  // open: C4
  Small_XOR small_xor_9 (.A(n4_bit_clg_3_c2), .B(n4_bit_clg_3_p2), .S(S6));
  Small_XOR small_xor_10 (.A(n4_bit_clg_3_c3), .B(n4_bit_clg_3_p3), .S(S7));
  Small_XOR small_xor_11 (.A(n4_bit_clg_3_c1), .B(n4_bit_clg_3_p1), .S(S5));
  Small_XOR small_xor_12 (.A(n4_bit_clg_3_c0_2), .B(n4_bit_clg_3_p0), .S(S4));
  _4_bit_CLG u_4_bit_clg_4 (
    .P(n4_bit_clg_4_p), .G(n4_bit_clg_4_g), .C3(n4_bit_clg_4_c3), .C2(n4_bit_clg_4_c2), .C1(n4_bit_clg_4_c1),
    .C0_2(n4_bit_clg_4_c0_2), .P3(n4_bit_clg_4_p3), .P2(n4_bit_clg_4_p2), .P1(n4_bit_clg_4_p1),
    .P0(n4_bit_clg_4_p0), .A3(A3), .B3(B3), .A2(A2), .B2(B2), .A1(A1), .B1(B1), .A0(A0), .B0(B0), .C0(C0));  // open: C4
  Small_XOR small_xor_13 (.A(n4_bit_clg_4_c2), .B(n4_bit_clg_4_p2), .S(S2));
  Small_XOR small_xor_14 (.A(n4_bit_clg_4_c3), .B(n4_bit_clg_4_p3), .S(S3));
  Small_XOR small_xor_15 (.A(n4_bit_clg_4_c1), .B(n4_bit_clg_4_p1), .S(S1));
  Small_XOR small_xor_16 (.A(n4_bit_clg_4_c0_2), .B(n4_bit_clg_4_p0), .S(S0));
endmodule

module _4_bit_CLG (
  input  A3,
  input  B3,
  input  A2,
  input  B2,
  input  A1,
  input  B1,
  input  A0,
  input  B0,
  input  C0,
  output C4,
  output P,
  output G,
  output C3,
  output C2,
  output C1,
  output C0_2,
  output P3,
  output P2,
  output P1,
  output P0
);

  wire AND_2_out, AND_3_out, AND_4_out, n1_bit_full_adder_1_g, n1_bit_full_adder_2_g, n1_bit_full_adder_3_g,
       n1_bit_full_adder_4_g;

  and AND (P, P3, P2, P1, P0);
  or OR (G, n1_bit_full_adder_1_g, AND_2_out, AND_3_out, AND_4_out);
  _1_bit_Full_Adder u_1_bit_full_adder_1 (.A(A3), .B(B3), .Cin(C3), .P(P3), .G(n1_bit_full_adder_1_g), .Cout(C4));
  and AND_2 (AND_2_out, P3, n1_bit_full_adder_2_g);
  _1_bit_Full_Adder u_1_bit_full_adder_2 (.A(A2), .B(B2), .Cin(C2), .P(P2), .G(n1_bit_full_adder_2_g), .Cout(C3));
  _1_bit_Full_Adder u_1_bit_full_adder_3 (.A(A1), .B(B1), .Cin(C1), .P(P1), .G(n1_bit_full_adder_3_g), .Cout(C2));
  and AND_3 (AND_3_out, P3, P2, n1_bit_full_adder_3_g);
  _1_bit_Full_Adder u_1_bit_full_adder_4 (.A(A0), .B(B0), .Cin(C0), .P(P0), .G(n1_bit_full_adder_4_g), .Cout(C1));
  and AND_4 (AND_4_out, P3, P2, P1, n1_bit_full_adder_4_g);

  assign C0_2 = C0;
endmodule

module GP (
  input  A,
  input  B,
  output P,
  output G
);

  xor XOR (P, A, B);
  and AND (G, A, B);
endmodule

// 1 Bit Full Adder
module _1_bit_Full_Adder (
  input  A,
  input  B,
  input  Cin,
  output P,
  output G,
  output Cout
);

  wire and_2_out;

  xor XOR (P, A, B);
  and AND (G, A, B);
  and and_2 (and_2_out, P, Cin);
  or or_1 (Cout, G, and_2_out);
endmodule

module _4_bit_GP_CLG (
  input  C0,
  input  G3,
  input  P3,
  input  G2,
  input  P2,
  input  G1,
  input  P1,
  input  G0,
  input  P0,
  output C16,
  output C12,
  output C8,
  output C4
);

  _1_bit_GP_CLG u_1_bit_gp_clg_1 (.G(G3), .P(P3), .Cin(C12), .Cout(C16));
  _1_bit_GP_CLG u_1_bit_gp_clg_2 (.G(G2), .P(P2), .Cin(C8), .Cout(C12));
  _1_bit_GP_CLG u_1_bit_gp_clg_3 (.G(G1), .P(P1), .Cin(C4), .Cout(C8));
  _1_bit_GP_CLG u_1_bit_gp_clg_4 (.G(G0), .P(P0), .Cin(C0), .Cout(C4));
endmodule

module _1_bit_GP_CLG (
  input  G,
  input  P,
  input  Cin,
  output Cout
);

  wire AND_out;

  and AND (AND_out, P, Cin);
  or OR (Cout, G, AND_out);
endmodule

// XOR
module Small_XOR (
  input  A,
  input  B,
  output S
);

  xor XOR (S, A, B);
endmodule

module _64_bit_CLA (
  input  B63,
  input  A63,
  input  B62,
  input  A62,
  input  B61,
  input  A61,
  input  B60,
  input  A60,
  input  B59,
  input  A59,
  input  B58,
  input  A58,
  input  B57,
  input  A57,
  input  B56,
  input  A56,
  input  B55,
  input  A55,
  input  B54,
  input  A54,
  input  B53,
  input  A53,
  input  B52,
  input  A52,
  input  B51,
  input  A51,
  input  B50,
  input  A50,
  input  B49,
  input  A49,
  input  B48,
  input  A48,
  input  B47,
  input  A47,
  input  B46,
  input  A46,
  input  B45,
  input  A45,
  input  B44,
  input  A44,
  input  B43,
  input  A43,
  input  B42,
  input  A42,
  input  B41,
  input  A41,
  input  B40,
  input  A40,
  input  B39,
  input  A39,
  input  B38,
  input  A38,
  input  B37,
  input  A37,
  input  B36,
  input  A36,
  input  B35,
  input  A35,
  input  B34,
  input  A34,
  input  B33,
  input  A33,
  input  B32,
  input  A32,
  input  B31,
  input  A31,
  input  B30,
  input  A30,
  input  B29,
  input  A29,
  input  B28,
  input  A28,
  input  B27,
  input  A27,
  input  B26,
  input  A26,
  input  B25,
  input  A25,
  input  B24,
  input  A24,
  input  B23,
  input  A23,
  input  B22,
  input  A22,
  input  B21,
  input  A21,
  input  B20,
  input  A20,
  input  B19,
  input  A19,
  input  B18,
  input  A18,
  input  B17,
  input  A17,
  input  B16,
  input  A16,
  input  B15,
  input  A15,
  input  B14,
  input  A14,
  input  B13,
  input  A13,
  input  B12,
  input  A12,
  input  B11,
  input  A11,
  input  B10,
  input  A10,
  input  B9,
  input  A9,
  input  B8,
  input  A8,
  input  B7,
  input  A7,
  input  B6,
  input  A6,
  input  B5,
  input  A5,
  input  B4,
  input  A4,
  input  B3,
  input  A3,
  input  B2,
  input  A2,
  input  B1,
  input  A1,
  input  B0,
  input  A0,
  input  C0,
  output S63,
  output S62,
  output S61,
  output S60,
  output S59,
  output S58,
  output S57,
  output S56,
  output S55,
  output S54,
  output S53,
  output S52,
  output S51,
  output S50,
  output S49,
  output S48,
  output S47,
  output S46,
  output S45,
  output S44,
  output S43,
  output S42,
  output S41,
  output S40,
  output S39,
  output S38,
  output S37,
  output S36,
  output S35,
  output S34,
  output S33,
  output S32,
  output S31,
  output S30,
  output S29,
  output S28,
  output S27,
  output S26,
  output S25,
  output S24,
  output S23,
  output S22,
  output S21,
  output S20,
  output S19,
  output S18,
  output S17,
  output S16,
  output S15,
  output S14,
  output S13,
  output S12,
  output S11,
  output S10,
  output S9,
  output S8,
  output S7,
  output S6,
  output S5,
  output S4,
  output S3,
  output S2,
  output S1,
  output S0,
  output C16,
  output G,
  output P
);

  wire n4_bit_gp_clg_1_c4, n4_bit_gp_clg_1_c8, n4_bit_gp_clg_1_c12, n16_bit_gp_clg_1_g, n16_bit_gp_clg_1_p,
       n16_bit_gp_clg_2_g, n16_bit_gp_clg_2_p, n16_bit_gp_clg_3_g, n16_bit_gp_clg_3_p, n16_bit_gp_clg_4_g,
       n16_bit_gp_clg_4_p;

  _16_bit_GP_CLG u_16_bit_gp_clg_1 (
    .C0(n4_bit_gp_clg_1_c12), .B15(B63), .A15(A63), .B14(B62), .A14(A62), .B13(B61), .A13(A61), .B12(B60),
    .A12(A60), .B11(B59), .A11(A59), .B10(B58), .A10(A58), .B9(B57), .A9(A57), .B8(B56), .A8(A56), .B7(B55),
    .A7(A55), .B6(B54), .A6(A54), .B5(B53), .A5(A53), .B4(B52), .A4(A52), .B3(B51), .A3(A51), .B2(B50),
    .A2(A50), .B1(B49), .A1(A49), .B0(B48), .A0(A48), .S15(S63), .S14(S62), .S13(S61), .S12(S60),
    .G(n16_bit_gp_clg_1_g), .P(n16_bit_gp_clg_1_p), .S11(S59), .S10(S58), .S9(S57), .S8(S56), .S7(S55),
    .S6(S54), .S5(S53), .S4(S52), .S3(S51), .S2(S50), .S1(S49), .S0(S48));
  _16_bit_GP_CLG u_16_bit_gp_clg_2 (
    .C0(n4_bit_gp_clg_1_c8), .B15(B47), .A15(A47), .B14(B46), .A14(A46), .B13(B45), .A13(A45), .B12(B44),
    .A12(A44), .B11(B43), .A11(A43), .B10(B42), .A10(A42), .B9(B41), .A9(A41), .B8(B40), .A8(A40), .B7(B39),
    .A7(A39), .B6(B38), .A6(A38), .B5(B37), .A5(A37), .B4(B36), .A4(A36), .B3(B35), .A3(A35), .B2(B34),
    .A2(A34), .B1(B33), .A1(A33), .B0(B32), .A0(A32), .S15(S47), .S14(S46), .S13(S45), .S12(S44),
    .G(n16_bit_gp_clg_2_g), .P(n16_bit_gp_clg_2_p), .S11(S43), .S10(S42), .S9(S41), .S8(S40), .S7(S39),
    .S6(S38), .S5(S37), .S4(S36), .S3(S35), .S2(S34), .S1(S33), .S0(S32));
  _4_bit_GP___CLG u_4_bit_gp_clg_1 (
    .C16(C16), .C0(C0), .G(G), .P(P), .P3(n16_bit_gp_clg_1_p), .C12(n4_bit_gp_clg_1_c12),
    .G2(n16_bit_gp_clg_2_g), .P2(n16_bit_gp_clg_2_p), .C8(n4_bit_gp_clg_1_c8), .G1(n16_bit_gp_clg_3_g),
    .P1(n16_bit_gp_clg_3_p), .C4(n4_bit_gp_clg_1_c4), .G0(n16_bit_gp_clg_4_g), .P0(n16_bit_gp_clg_4_p),
    .G3(n16_bit_gp_clg_1_g));
  _16_bit_GP_CLG u_16_bit_gp_clg_3 (
    .C0(n4_bit_gp_clg_1_c4), .B15(B31), .A15(A31), .B14(B30), .A14(A30), .B13(B29), .A13(A29), .B12(B28),
    .A12(A28), .B11(B27), .A11(A27), .B10(B26), .A10(A26), .B9(B25), .A9(A25), .B8(B24), .A8(A24), .B7(B23),
    .A7(A23), .B6(B22), .A6(A22), .B5(B21), .A5(A21), .B4(B20), .A4(A20), .B3(B19), .A3(A19), .B2(B18),
    .A2(A18), .B1(B17), .A1(A17), .B0(B16), .A0(A16), .S15(S31), .S14(S30), .S13(S29), .S12(S28),
    .G(n16_bit_gp_clg_3_g), .P(n16_bit_gp_clg_3_p), .S11(S27), .S10(S26), .S9(S25), .S8(S24), .S7(S23),
    .S6(S22), .S5(S21), .S4(S20), .S3(S19), .S2(S18), .S1(S17), .S0(S16));
  _16_bit_GP_CLG u_16_bit_gp_clg_4 (
    .C0(C0), .B15(B15), .A15(A15), .B14(B14), .A14(A14), .B13(B13), .A13(A13), .B12(B12), .A12(A12),
    .B11(B11), .A11(A11), .B10(B10), .A10(A10), .B9(B9), .A9(A9), .B8(B8), .A8(A8), .B7(B7), .A7(A7),
    .B6(B6), .A6(A6), .B5(B5), .A5(A5), .B4(B4), .A4(A4), .B3(B3), .A3(A3), .B2(B2), .A2(A2), .B1(B1),
    .A1(A1), .B0(B0), .A0(A0), .S15(S15), .S14(S14), .S13(S13), .S12(S12), .G(n16_bit_gp_clg_4_g),
    .P(n16_bit_gp_clg_4_p), .S11(S11), .S10(S10), .S9(S9), .S8(S8), .S7(S7), .S6(S6), .S5(S5), .S4(S4),
    .S3(S3), .S2(S2), .S1(S1), .S0(S0));
endmodule

module _16_bit_CLG (
  input  B15,
  input  A15,
  input  B14,
  input  A14,
  input  B13,
  input  A13,
  input  B12,
  input  A12,
  input  B11,
  input  A11,
  input  B10,
  input  A10,
  input  B9,
  input  A9,
  input  B8,
  input  A8,
  input  B7,
  input  A7,
  input  B6,
  input  A6,
  input  B5,
  input  A5,
  input  B4,
  input  A4,
  input  B3,
  input  A3,
  input  B2,
  input  A2,
  input  B1,
  input  A1,
  input  B0,
  input  A0,
  output out_33,
  output out_34,
  output out_35,
  output out_36,
  output out_37,
  output out_38,
  output out_39,
  output out_40,
  output out_41,
  output out_42,
  output out_43,
  output out_44,
  output out_45,
  output out_46,
  output out_47,
  output out_48,
  output out_49,
  output out_50,
  output out_51,
  output out_52,
  output out_53,
  output out_54,
  output out_55,
  output out_56,
  output out_57,
  output out_58,
  output out_59,
  output out_60,
  output out_61,
  output out_62,
  output out_63,
  output out_64
);

  // _4_bit_CLG 4_bit_clg_1: pin names not known; wires that end beside it: B15, A15, out_33, B14, out_34, out_35, A14, out_36, B13, out_37, out_38, A13, out_39, out_40, B12, A12
  // _4_bit_CLG 4_bit_clg_2: pin names not known; wires that end beside it: B11, A11, out_41, B10, out_42, out_43, A10, out_44, B9, out_45, out_46, A9, out_47, out_48, B8, A8
  // _4_bit_CLG 4_bit_clg_3: pin names not known; wires that end beside it: B7, A7, out_49, B6, out_50, out_51, A6, out_52, B5, out_53, out_54, A5, out_55, out_56, B4, A4
  // _4_bit_CLG 4_bit_clg_4: pin names not known; wires that end beside it: B3, A3, out_57, B2, out_58, out_59, A2, out_60, B1, out_61, out_62, A1, out_63, out_64, B0, A0
endmodule

module _4_bit_GP_CLA (
  input  B3,
  input  A3,
  input  B2,
  input  A2,
  input  B1,
  input  A1,
  input  B0,
  input  A0,
  input  C0,
  output P,
  output G,
  output S3,
  output S2,
  output S1,
  output S0
);

  wire n4_bit_clg_1_c0_2, n4_bit_clg_1_c1, n4_bit_clg_1_c2, n4_bit_clg_1_c3, n4_bit_clg_1_p0,
       n4_bit_clg_1_p1, n4_bit_clg_1_p2, n4_bit_clg_1_p3;

  _4_bit_CLG u_4_bit_clg_1 (
    .P(P), .G(G), .C3(n4_bit_clg_1_c3), .C2(n4_bit_clg_1_c2), .C1(n4_bit_clg_1_c1), .C0_2(n4_bit_clg_1_c0_2),
    .P3(n4_bit_clg_1_p3), .P2(n4_bit_clg_1_p2), .P1(n4_bit_clg_1_p1), .P0(n4_bit_clg_1_p0), .A3(A3), .B3(B3),
    .A2(A2), .B2(B2), .A1(A1), .B1(B1), .A0(A0), .B0(B0), .C0(C0));  // open: C4
  Small_XOR small_xor_1 (.A(n4_bit_clg_1_c3), .B(n4_bit_clg_1_p3), .S(S3));
  Small_XOR small_xor_2 (.A(n4_bit_clg_1_c2), .B(n4_bit_clg_1_p2), .S(S2));
  Small_XOR small_xor_3 (.A(n4_bit_clg_1_c1), .B(n4_bit_clg_1_p1), .S(S1));
  Small_XOR small_xor_4 (.A(n4_bit_clg_1_c0_2), .B(n4_bit_clg_1_p0), .S(S0));
endmodule

module _16_bit_GP_CLG (
  input  B15,
  input  A15,
  input  B14,
  input  A14,
  input  B13,
  input  A13,
  input  B12,
  input  A12,
  input  B11,
  input  A11,
  input  B10,
  input  A10,
  input  B9,
  input  A9,
  input  B8,
  input  A8,
  input  B7,
  input  A7,
  input  B6,
  input  A6,
  input  B5,
  input  A5,
  input  B4,
  input  A4,
  input  B3,
  input  A3,
  input  B2,
  input  A2,
  input  B1,
  input  A1,
  input  B0,
  input  A0,
  input  C0,
  output S15,
  output S14,
  output S13,
  output S12,
  output S11,
  output S10,
  output S9,
  output S8,
  output S7,
  output S6,
  output S5,
  output S4,
  output S3,
  output S2,
  output S1,
  output S0,
  output G,
  output P
);

  wire n4_bit_gp_cla_1_g, n4_bit_gp_cla_1_p, n4_bit_gp_cla_2_g, n4_bit_gp_cla_2_p, n4_bit_gp_cla_3_g,
       n4_bit_gp_cla_3_p, n4_bit_gp_cla_4_g, n4_bit_gp_cla_4_p, n4_bit_gp_clg_1_c4, n4_bit_gp_clg_1_c8,
       n4_bit_gp_clg_1_c12;

  _4_bit_GP_CLA u_4_bit_gp_cla_1 (
    .B3(B15), .A3(A15), .B2(B14), .A2(A14), .B1(B13), .A1(A13), .B0(B12), .A0(A12), .C0(n4_bit_gp_clg_1_c12),
    .P(n4_bit_gp_cla_1_p), .G(n4_bit_gp_cla_1_g), .S3(S15), .S2(S14), .S1(S13), .S0(S12));
  _4_bit_GP_CLA u_4_bit_gp_cla_2 (
    .B3(B11), .A3(A11), .B2(B10), .A2(A10), .B1(B9), .A1(A9), .B0(B8), .A0(A8), .C0(n4_bit_gp_clg_1_c8),
    .P(n4_bit_gp_cla_2_p), .G(n4_bit_gp_cla_2_g), .S3(S11), .S2(S10), .S1(S9), .S0(S8));
  _4_bit_GP_CLA u_4_bit_gp_cla_3 (
    .B3(B7), .A3(A7), .B2(B6), .A2(A6), .B1(B5), .A1(A5), .B0(B4), .A0(A4), .C0(n4_bit_gp_clg_1_c4),
    .P(n4_bit_gp_cla_3_p), .G(n4_bit_gp_cla_3_g), .S3(S7), .S2(S6), .S1(S5), .S0(S4));
  _4_bit_GP___CLG u_4_bit_gp_clg_1 (
    .C0(C0), .G(G), .P(P), .P3(n4_bit_gp_cla_1_p), .C12(n4_bit_gp_clg_1_c12), .G2(n4_bit_gp_cla_2_g),
    .P2(n4_bit_gp_cla_2_p), .C8(n4_bit_gp_clg_1_c8), .G1(n4_bit_gp_cla_3_g), .P1(n4_bit_gp_cla_3_p),
    .C4(n4_bit_gp_clg_1_c4), .G0(n4_bit_gp_cla_4_g), .P0(n4_bit_gp_cla_4_p), .G3(n4_bit_gp_cla_1_g));  // open: C16
  _4_bit_GP_CLA u_4_bit_gp_cla_4 (
    .B3(B3), .A3(A3), .B2(B2), .A2(A2), .B1(B1), .A1(A1), .B0(B0), .A0(A0), .C0(C0), .P(n4_bit_gp_cla_4_p),
    .G(n4_bit_gp_cla_4_g), .S3(S3), .S2(S2), .S1(S1), .S0(S0));
endmodule

module _4_bit_GP___CLG (
  input  C0,
  input  G3,
  input  P3,
  input  G2,
  input  P2,
  input  G1,
  input  P1,
  input  G0,
  input  P0,
  output C16,
  output C12,
  output C8,
  output C4,
  output G,
  output P
);

  wire AND_2_out, AND_3_out, AND_4_out;

  and AND (P, P3, P2, P1, P0);
  or OR (G, G3, AND_2_out, AND_3_out, AND_4_out);
  and AND_2 (AND_2_out, P3, G2);
  _4_bit_GP_CLG u_4_bit_gp_clg_1 (
    .C16(C16), .C0(C0), .G3(G3), .P3(P3), .C12(C12), .G2(G2), .P2(P2), .C8(C8), .G1(G1), .P1(P1), .C4(C4),
    .G0(G0), .P0(P0));
  and AND_3 (AND_3_out, P3, P2, G1);
  and AND_4 (AND_4_out, P3, P2, P1, G0);
endmodule
