// Logisim project CSA.circ as structural Verilog: 5 circuits, main circuit 7 8-bit Numbers CSA
// F.A
module Full_Adder (
  input  Cin,
  input  A,
  input  B,
  output S,
  output Cout
);

  Adder #(.width(1)) adder_1 (.a(A), .b(B), .out(S), .cin(Cin), .cout(Cout));
endmodule

// 1-bit CSA
module _3_1_bit_Numbers_CSA (
  input  C,
  input  A,
  input  B,
  output S,
  output Cout
);

  Adder #(.width(1)) adder_1 (.a(A), .b(B), .out(S), .cin(C), .cout(Cout));
endmodule

module _3_8_bit_Numbers_CSA (
  input  A7,
  input  B7,
  input  C7,
  input  A6,
  input  B6,
  input  C6,
  input  A5,
  input  B5,
  input  C5,
  input  A4,
  input  B4,
  input  C4,
  input  A3,
  input  B3,
  input  C3,
  input  A2,
  input  B2,
  input  C2,
  input  A1,
  input  B1,
  input  C1,
  input  A0,
  input  B0,
  input  C0,
  output Co8,
  output Co8_prime,
  output S7_prime,
  output S6_prime,
  output S5_prime,
  output S4_prime,
  output S3_prime,
  output S2_prime,
  output S1_prime,
  output S0_prime
);

  wire full_adder_2_cout, full_adder_3_cout, full_adder_4_cout, full_adder_5_cout, full_adder_6_cout,
       full_adder_7_cout, full_adder_8_cout, n3_1_bit_numbers_csa_1_s, n3_1_bit_numbers_csa_2_cout,
       n3_1_bit_numbers_csa_2_s, n3_1_bit_numbers_csa_3_cout, n3_1_bit_numbers_csa_3_s,
       n3_1_bit_numbers_csa_4_cout, n3_1_bit_numbers_csa_4_s, n3_1_bit_numbers_csa_5_cout,
       n3_1_bit_numbers_csa_5_s, n3_1_bit_numbers_csa_6_cout, n3_1_bit_numbers_csa_6_s,
       n3_1_bit_numbers_csa_7_cout, n3_1_bit_numbers_csa_7_s, n3_1_bit_numbers_csa_8_cout,
       n3_1_bit_numbers_csa_8_s;

  _3_1_bit_Numbers_CSA u_3_1_bit_numbers_csa_1 (.A(A7), .B(B7), .S(n3_1_bit_numbers_csa_1_s), .C(C7), .Cout(Co8));
  Full_Adder full_adder_1 (
    .A(n3_1_bit_numbers_csa_1_s), .B(n3_1_bit_numbers_csa_2_cout), .S(S7_prime), .Cin(full_adder_2_cout),
    .Cout(Co8_prime));
  _3_1_bit_Numbers_CSA u_3_1_bit_numbers_csa_2 (
    .A(A6), .B(B6), .S(n3_1_bit_numbers_csa_2_s), .C(C6), .Cout(n3_1_bit_numbers_csa_2_cout));
  Full_Adder full_adder_2 (
    .A(n3_1_bit_numbers_csa_2_s), .B(n3_1_bit_numbers_csa_3_cout), .S(S6_prime), .Cin(full_adder_3_cout),
    .Cout(full_adder_2_cout));
  _3_1_bit_Numbers_CSA u_3_1_bit_numbers_csa_3 (
    .A(A5), .B(B5), .S(n3_1_bit_numbers_csa_3_s), .C(C5), .Cout(n3_1_bit_numbers_csa_3_cout));
  Full_Adder full_adder_3 (
    .A(n3_1_bit_numbers_csa_3_s), .B(n3_1_bit_numbers_csa_4_cout), .S(S5_prime), .Cin(full_adder_4_cout),
    .Cout(full_adder_3_cout));
  _3_1_bit_Numbers_CSA u_3_1_bit_numbers_csa_4 (
    .A(A4), .B(B4), .S(n3_1_bit_numbers_csa_4_s), .C(C4), .Cout(n3_1_bit_numbers_csa_4_cout));
  Full_Adder full_adder_4 (
    .A(n3_1_bit_numbers_csa_4_s), .B(n3_1_bit_numbers_csa_5_cout), .S(S4_prime), .Cin(full_adder_5_cout),
    .Cout(full_adder_4_cout));
  _3_1_bit_Numbers_CSA u_3_1_bit_numbers_csa_5 (
    .A(A3), .B(B3), .S(n3_1_bit_numbers_csa_5_s), .C(C3), .Cout(n3_1_bit_numbers_csa_5_cout));
  Full_Adder full_adder_5 (
    .A(n3_1_bit_numbers_csa_5_s), .B(n3_1_bit_numbers_csa_6_cout), .S(S3_prime), .Cin(full_adder_6_cout),
    .Cout(full_adder_5_cout));
  _3_1_bit_Numbers_CSA u_3_1_bit_numbers_csa_6 (
    .A(A2), .B(B2), .S(n3_1_bit_numbers_csa_6_s), .C(C2), .Cout(n3_1_bit_numbers_csa_6_cout));
  Full_Adder full_adder_6 (
    .A(n3_1_bit_numbers_csa_6_s), .B(n3_1_bit_numbers_csa_7_cout), .S(S2_prime), .Cin(full_adder_7_cout),
    .Cout(full_adder_6_cout));
  _3_1_bit_Numbers_CSA u_3_1_bit_numbers_csa_7 (
    .A(A1), .B(B1), .S(n3_1_bit_numbers_csa_7_s), .C(C1), .Cout(n3_1_bit_numbers_csa_7_cout));
  Full_Adder full_adder_7 (
    .A(n3_1_bit_numbers_csa_7_s), .B(n3_1_bit_numbers_csa_8_cout), .S(S1_prime), .Cin(full_adder_8_cout),
    .Cout(full_adder_7_cout));
  _3_1_bit_Numbers_CSA u_3_1_bit_numbers_csa_8 (
    .A(A0), .B(B0), .S(n3_1_bit_numbers_csa_8_s), .C(C0), .Cout(n3_1_bit_numbers_csa_8_cout));
  Full_Adder full_adder_8 (.A(n3_1_bit_numbers_csa_8_s), .B(1'b0), .S(S0_prime), .Cin(1'b0), .Cout(full_adder_8_cout));

  // Notes on the sheet:
  //   S7
  //   S6
  //   Co7
  //   Co7'
  //   Co6
  //   Co6'
  //   S5
  //   Co5
  //   Co5'
  //   S4
  //   Co4
  //   Co4'
  //   S3
  //   S2
  //   Co3
  //   Co3'
  //   Co2
  //   Co2'
  //   S1
  //   Co1
  //   Co1'
  //   S0
endmodule

// 8-bit CSA
module _3_8_bit_Numbers_CSA_with_Carry (
  input  [7:0] C0_7,
  input  [7:0] B0_7,
  input  [7:0] A0_7,
  output [7:0] S0_7,
  output [7:0] Co1_8
);

  _3_1_bit_Numbers_CSA u_3_1_bit_numbers_csa_1 (.A(A0_7[7]), .B(B0_7[7]), .S(S0_7[7]), .C(C0_7[7]), .Cout(Co1_8[7]));
  _3_1_bit_Numbers_CSA u_3_1_bit_numbers_csa_2 (.A(A0_7[6]), .B(B0_7[6]), .S(S0_7[6]), .C(C0_7[6]), .Cout(Co1_8[6]));
  _3_1_bit_Numbers_CSA u_3_1_bit_numbers_csa_3 (.A(A0_7[5]), .B(B0_7[5]), .S(S0_7[5]), .C(C0_7[5]), .Cout(Co1_8[5]));
  _3_1_bit_Numbers_CSA u_3_1_bit_numbers_csa_4 (.A(A0_7[4]), .B(B0_7[4]), .S(S0_7[4]), .C(C0_7[4]), .Cout(Co1_8[4]));
  _3_1_bit_Numbers_CSA u_3_1_bit_numbers_csa_5 (.A(A0_7[3]), .B(B0_7[3]), .S(S0_7[3]), .C(C0_7[3]), .Cout(Co1_8[3]));
  _3_1_bit_Numbers_CSA u_3_1_bit_numbers_csa_6 (.A(A0_7[2]), .B(B0_7[2]), .S(S0_7[2]), .C(C0_7[2]), .Cout(Co1_8[2]));
  _3_1_bit_Numbers_CSA u_3_1_bit_numbers_csa_7 (.A(A0_7[1]), .B(B0_7[1]), .S(S0_7[1]), .C(C0_7[1]), .Cout(Co1_8[1]));
  _3_1_bit_Numbers_CSA u_3_1_bit_numbers_csa_8 (.A(A0_7[0]), .B(B0_7[0]), .S(S0_7[0]), .C(C0_7[0]), .Cout(Co1_8[0]));
endmodule

module _7_8_bit_Numbers_CSA (
  input  [7:0] A0_7,
  input  [7:0] B0_7,
  input  [7:0] C0_7,
  input  [7:0] D0_7,
  input  [7:0] E0_7,
  input  [7:0] F0_7,
  input  [7:0] G0_7,
  output S0,
  output S1,
  output S2,
  output [7:0] C4_11,
  output [7:0] S3_10,
  output [2:0] S2_0
);

  wire [6:0] n3_8_bit_numbers_csa_with_carry_3_co1_8, n3_8_bit_numbers_csa_with_carry_6_s0_7,
       n3_8_bit_numbers_csa_with_carry_9_s0_7, n3_8_bit_numbers_csa_with_carry_10_co1_8_2;
  wire [7:0] n3_8_bit_numbers_csa_with_carry_1_co1_8, n3_8_bit_numbers_csa_with_carry_1_s0_7,
       n3_8_bit_numbers_csa_with_carry_2_s0_7, n3_8_bit_numbers_csa_with_carry_3_s0_7,
       n3_8_bit_numbers_csa_with_carry_4_co1_8, n3_8_bit_numbers_csa_with_carry_4_s0_7,
       n3_8_bit_numbers_csa_with_carry_5_co1_8, n3_8_bit_numbers_csa_with_carry_6_co1_8,
       n3_8_bit_numbers_csa_with_carry_8_co1_8, n3_8_bit_numbers_csa_with_carry_8_s0_7,
       n3_8_bit_numbers_csa_with_carry_9_co1_8, n3_8_bit_numbers_csa_with_carry_10_s0_7;
  wire [7:1] n3_8_bit_numbers_csa_with_carry_2_co1_8_2, n3_8_bit_numbers_csa_with_carry_5_s0_7;
  wire [7:7] n3_8_bit_numbers_csa_with_carry_2_co1_8, n3_8_bit_numbers_csa_with_carry_3_co1_8_2,
       n3_8_bit_numbers_csa_with_carry_10_co1_8;

  _3_8_bit_Numbers_CSA_with_Carry u_3_8_bit_numbers_csa_with_carry_1 (
    .C0_7(C0_7), .B0_7(B0_7), .A0_7(A0_7), .S0_7(n3_8_bit_numbers_csa_with_carry_1_s0_7),
    .Co1_8(n3_8_bit_numbers_csa_with_carry_1_co1_8));
  _3_8_bit_Numbers_CSA_with_Carry u_3_8_bit_numbers_csa_with_carry_2 (
    .C0_7({n3_8_bit_numbers_csa_with_carry_10_co1_8[7], {7{1'b0}}}),
    .B0_7(n3_8_bit_numbers_csa_with_carry_8_co1_8),
    .A0_7({n3_8_bit_numbers_csa_with_carry_1_co1_8[7], {7{1'b0}}}),
    .S0_7(n3_8_bit_numbers_csa_with_carry_2_s0_7),
    .Co1_8({n3_8_bit_numbers_csa_with_carry_2_co1_8[7], n3_8_bit_numbers_csa_with_carry_2_co1_8_2}));
  _3_8_bit_Numbers_CSA_with_Carry u_3_8_bit_numbers_csa_with_carry_3 (
    .C0_7(n3_8_bit_numbers_csa_with_carry_5_co1_8),
    .B0_7({n3_8_bit_numbers_csa_with_carry_4_co1_8[7], {7{1'b0}}}),
    .A0_7({n3_8_bit_numbers_csa_with_carry_2_co1_8[7], {7{1'b0}}}),
    .S0_7(n3_8_bit_numbers_csa_with_carry_3_s0_7),
    .Co1_8({n3_8_bit_numbers_csa_with_carry_3_co1_8_2[7], n3_8_bit_numbers_csa_with_carry_3_co1_8}));
  _3_8_bit_Numbers_CSA_with_Carry u_3_8_bit_numbers_csa_with_carry_4 (
    .C0_7(n3_8_bit_numbers_csa_with_carry_9_co1_8), .B0_7(n3_8_bit_numbers_csa_with_carry_2_s0_7),
    .A0_7({n3_8_bit_numbers_csa_with_carry_2_co1_8_2, 1'b0}), .S0_7(n3_8_bit_numbers_csa_with_carry_4_s0_7),
    .Co1_8(n3_8_bit_numbers_csa_with_carry_4_co1_8));
  _3_8_bit_Numbers_CSA_with_Carry u_3_8_bit_numbers_csa_with_carry_5 (
    .C0_7({1'b0, n3_8_bit_numbers_csa_with_carry_9_s0_7}), .B0_7(n3_8_bit_numbers_csa_with_carry_4_s0_7),
    .A0_7({n3_8_bit_numbers_csa_with_carry_4_co1_8[6:0], 1'b0}),
    .S0_7({n3_8_bit_numbers_csa_with_carry_5_s0_7, S1}), .Co1_8(n3_8_bit_numbers_csa_with_carry_5_co1_8));
  _3_8_bit_Numbers_CSA_with_Carry u_3_8_bit_numbers_csa_with_carry_6 (
    .C0_7({1'b0, n3_8_bit_numbers_csa_with_carry_5_s0_7}), .B0_7(n3_8_bit_numbers_csa_with_carry_3_s0_7),
    .A0_7({n3_8_bit_numbers_csa_with_carry_3_co1_8, 1'b0}),
    .S0_7({n3_8_bit_numbers_csa_with_carry_6_s0_7, S2}), .Co1_8(n3_8_bit_numbers_csa_with_carry_6_co1_8));
  _3_8_bit_Numbers_CSA_with_Carry u_3_8_bit_numbers_csa_with_carry_7 (
    .C0_7({1'b0, n3_8_bit_numbers_csa_with_carry_6_s0_7}), .B0_7(n3_8_bit_numbers_csa_with_carry_6_co1_8),
    .A0_7({n3_8_bit_numbers_csa_with_carry_3_co1_8_2[7], {7{1'b0}}}), .S0_7(S3_10), .Co1_8(C4_11));
  _3_8_bit_Numbers_CSA_with_Carry u_3_8_bit_numbers_csa_with_carry_8 (
    .C0_7(n3_8_bit_numbers_csa_with_carry_10_s0_7), .B0_7(n3_8_bit_numbers_csa_with_carry_1_s0_7),
    .A0_7({n3_8_bit_numbers_csa_with_carry_1_co1_8[6:0], 1'b0}),
    .S0_7(n3_8_bit_numbers_csa_with_carry_8_s0_7), .Co1_8(n3_8_bit_numbers_csa_with_carry_8_co1_8));
  _3_8_bit_Numbers_CSA_with_Carry u_3_8_bit_numbers_csa_with_carry_9 (
    .C0_7(G0_7), .B0_7(n3_8_bit_numbers_csa_with_carry_8_s0_7),
    .A0_7({n3_8_bit_numbers_csa_with_carry_10_co1_8_2, 1'b0}),
    .S0_7({n3_8_bit_numbers_csa_with_carry_9_s0_7, S0}), .Co1_8(n3_8_bit_numbers_csa_with_carry_9_co1_8));
  _3_8_bit_Numbers_CSA_with_Carry u_3_8_bit_numbers_csa_with_carry_10 (
    .C0_7(F0_7), .B0_7(E0_7), .A0_7(D0_7), .S0_7(n3_8_bit_numbers_csa_with_carry_10_s0_7),
    .Co1_8({n3_8_bit_numbers_csa_with_carry_10_co1_8[7], n3_8_bit_numbers_csa_with_carry_10_co1_8_2}));

  assign S2_0 = {S2, S1, S0};

  // Notes on the sheet:
  //   C10
  //   C8
  //   C9
  //   C9
  //   C2 -C9
  //   C2 -C9
  //   C3-C10
  //   S1-S8
  //   S2-S9
  //   S1-S8
  //   C8
endmodule
