// Logisim project Comparator,MUX,Arithmetic Circuit and CSA.circ as structural Verilog: 19 circuits, main circuit 1-bit Comparator
module _1_bit_Comparator (
  input  A,
  input  B,
  output A_B,
  output A_B_2,
  output A_B_3
);

  wire not_1_out, not_2_out;

  not not_1 (not_1_out, A);
  not not_2 (not_2_out, B);
  and and_1 (A_B, not_1_out, B);
  and and_2 (A_B_3, A, not_2_out);
  nor nor_1 (A_B_2, A_B, A_B_3);
endmodule

module _2_bit_Comparator (
  input  A1,
  input  B1,
  input  A0,
  input  B0,
  output A_B,
  output A_B_2,
  output A_B_3
);

  wire and_2_out, and_3_out, n1_bit_comparator_1_a_b, n1_bit_comparator_1_a_b_2, n1_bit_comparator_1_a_b_3,
       n1_bit_comparator_2_a_b, n1_bit_comparator_2_a_b_2, n1_bit_comparator_2_a_b_3;

  _1_bit_Comparator u_1_bit_comparator_1 (
    .A(A1), .B(B1), .A_B(n1_bit_comparator_1_a_b), .A_B_2(n1_bit_comparator_1_a_b_2),
    .A_B_3(n1_bit_comparator_1_a_b_3));
  _1_bit_Comparator u_1_bit_comparator_2 (
    .A(A0), .B(B0), .A_B(n1_bit_comparator_2_a_b), .A_B_2(n1_bit_comparator_2_a_b_2),
    .A_B_3(n1_bit_comparator_2_a_b_3));
  and and_1 (A_B_2, n1_bit_comparator_1_a_b_2, n1_bit_comparator_2_a_b_2);
  and and_2 (and_2_out, n1_bit_comparator_1_a_b_2, n1_bit_comparator_2_a_b_3);
  and and_3 (and_3_out, n1_bit_comparator_1_a_b_2, n1_bit_comparator_2_a_b);
  or or_1 (A_B, n1_bit_comparator_1_a_b, and_3_out);
  or or_2 (A_B_3, n1_bit_comparator_1_a_b_3, and_2_out);
endmodule

module _2_bit_Cascading_Comparator (
  input  A_B,
  input  A_B_2,
  input  A_B_3,
  input  A1,
  input  A0,
  input  B1,
  input  B0,
  output A_B_4,
  output A_B_5,
  output A_B_6
);

  wire and_2_out, and_3_out, n2_bit_comparator_1_a_b, n2_bit_comparator_1_a_b_2, n2_bit_comparator_1_a_b_3;

  _2_bit_Comparator u_2_bit_comparator_1 (
    .A1(A1), .B1(B1), .A0(A0), .B0(B0), .A_B(n2_bit_comparator_1_a_b), .A_B_2(n2_bit_comparator_1_a_b_2),
    .A_B_3(n2_bit_comparator_1_a_b_3));
  and and_1 (A_B_5, A_B_2, n2_bit_comparator_1_a_b_2);
  and and_2 (and_2_out, A_B_2, n2_bit_comparator_1_a_b_3);
  and and_3 (and_3_out, A_B_2, n2_bit_comparator_1_a_b);
  or or_1 (A_B_4, A_B, and_3_out);
  or or_2 (A_B_6, A_B_3, and_2_out);
endmodule

module _4_bit_Comparator (
  input  [3:0] A0_3,
  input  [3:0] B0_3,
  output A_B,
  output A_B_2,
  output A_B_3
);

  wire and_2_out, and_3_out, n2_bit_comparator_1_a_b, n2_bit_comparator_1_a_b_2, n2_bit_comparator_1_a_b_3,
       n2_bit_comparator_2_a_b, n2_bit_comparator_2_a_b_2, n2_bit_comparator_2_a_b_3;

  _2_bit_Comparator u_2_bit_comparator_1 (
    .A1(A0_3[3]), .B1(B0_3[3]), .A0(A0_3[2]), .B0(B0_3[2]), .A_B(n2_bit_comparator_1_a_b),
    .A_B_2(n2_bit_comparator_1_a_b_2), .A_B_3(n2_bit_comparator_1_a_b_3));
  _2_bit_Comparator u_2_bit_comparator_2 (
    .A1(A0_3[1]), .B1(B0_3[1]), .A0(A0_3[0]), .B0(B0_3[0]), .A_B(n2_bit_comparator_2_a_b),
    .A_B_2(n2_bit_comparator_2_a_b_2), .A_B_3(n2_bit_comparator_2_a_b_3));
  and and_1 (A_B_2, n2_bit_comparator_1_a_b_2, n2_bit_comparator_2_a_b_2);
  and and_2 (and_2_out, n2_bit_comparator_1_a_b_2, n2_bit_comparator_2_a_b);
  and and_3 (and_3_out, n2_bit_comparator_1_a_b_2, n2_bit_comparator_2_a_b_3);
  or or_1 (A_B, n2_bit_comparator_1_a_b, and_2_out);
  or or_2 (A_B_3, n2_bit_comparator_1_a_b_3, and_3_out);
endmodule

module _4_bit_Cascading_Comparator (
  input  A_B,
  input  A_B_2,
  input  A_B_3,
  input  [3:0] A0_3,
  input  [3:0] B0_3,
  output A_B_4,
  output A_B_5,
  output A_B_6
);

  wire n2_bit_cascading_comparator_1_a_b_4, n2_bit_cascading_comparator_1_a_b_5,
       n2_bit_cascading_comparator_1_a_b_6;

  _2_bit_Cascading_Comparator u_2_bit_cascading_comparator_1 (
    .A_B(A_B), .A_B_2(A_B_2), .A_B_3(A_B_3), .A1(A0_3[3]), .A0(A0_3[2]), .B1(B0_3[3]), .B0(B0_3[2]),
    .A_B_4(n2_bit_cascading_comparator_1_a_b_4), .A_B_5(n2_bit_cascading_comparator_1_a_b_5),
    .A_B_6(n2_bit_cascading_comparator_1_a_b_6));
  _2_bit_Cascading_Comparator u_2_bit_cascading_comparator_2 (
    .A_B(n2_bit_cascading_comparator_1_a_b_4), .A_B_2(n2_bit_cascading_comparator_1_a_b_5),
    .A_B_3(n2_bit_cascading_comparator_1_a_b_6), .A1(A0_3[1]), .A0(A0_3[0]), .B1(B0_3[1]), .B0(B0_3[0]),
    .A_B_4(A_B_4), .A_B_5(A_B_5), .A_B_6(A_B_6));
endmodule

module _8_bit_Comparator (
  input  [7:0] A0_7,
  input  [7:0] B0_7,
  output A_B,
  output A_B_2,
  output A_B_3
);

  wire and_2_out, and_3_out, n4_bit_comparator_1_a_b, n4_bit_comparator_1_a_b_2, n4_bit_comparator_1_a_b_3,
       n4_bit_comparator_2_a_b, n4_bit_comparator_2_a_b_2, n4_bit_comparator_2_a_b_3;

  _4_bit_Comparator u_4_bit_comparator_1 (
    .A0_3(A0_7[7:4]), .B0_3(B0_7[7:4]), .A_B(n4_bit_comparator_1_a_b), .A_B_2(n4_bit_comparator_1_a_b_2),
    .A_B_3(n4_bit_comparator_1_a_b_3));
  _4_bit_Comparator u_4_bit_comparator_2 (
    .A0_3(A0_7[7:4]), .B0_3(B0_7[7:4]), .A_B(n4_bit_comparator_2_a_b), .A_B_2(n4_bit_comparator_2_a_b_2),
    .A_B_3(n4_bit_comparator_2_a_b_3));
  and and_1 (A_B_2, n4_bit_comparator_1_a_b_2, n4_bit_comparator_2_a_b_2);
  and and_2 (and_2_out, n4_bit_comparator_1_a_b_2, n4_bit_comparator_2_a_b_3);
  and and_3 (and_3_out, n4_bit_comparator_1_a_b_2, n4_bit_comparator_2_a_b);
  or or_1 (A_B, n4_bit_comparator_1_a_b, and_3_out);
  or or_2 (A_B_3, n4_bit_comparator_1_a_b_3, and_2_out);
endmodule

module _8_bit_Cascading_Comparator (
  input  A_B,
  input  A_B_2,
  input  A_B_3,
  input  [7:0] A0_7,
  input  [7:0] B0_7,
  output A_B_4,
  output A_B_5,
  output A_B_6
);

  wire n4_bit_cascading_comparator_1_a_b_4, n4_bit_cascading_comparator_1_a_b_5,
       n4_bit_cascading_comparator_1_a_b_6;

  _4_bit_Cascading_Comparator u_4_bit_cascading_comparator_1 (
    .A_B(A_B), .A_B_2(A_B_2), .A_B_3(A_B_3), .A0_3(A0_7[7:4]), .B0_3(B0_7[7:4]),
    .A_B_4(n4_bit_cascading_comparator_1_a_b_4), .A_B_5(n4_bit_cascading_comparator_1_a_b_5),
    .A_B_6(n4_bit_cascading_comparator_1_a_b_6));
  _4_bit_Cascading_Comparator u_4_bit_cascading_comparator_2 (
    .A_B(n4_bit_cascading_comparator_1_a_b_4), .A_B_2(n4_bit_cascading_comparator_1_a_b_5),
    .A_B_3(n4_bit_cascading_comparator_1_a_b_6), .A0_3(A0_7[3:0]), .B0_3(B0_7[3:0]), .A_B_4(A_B_4),
    .A_B_5(A_B_5), .A_B_6(A_B_6));
endmodule

module _16_bit_Comparator (
  input  [15:0] A0_15,
  input  [15:0] B0_15,
  output A_B,
  output A_B_2,
  output A_B_3
);

  wire and_2_out, and_3_out, n8_bit_comparator_1_a_b, n8_bit_comparator_1_a_b_2, n8_bit_comparator_1_a_b_3,
       n8_bit_comparator_2_a_b, n8_bit_comparator_2_a_b_2, n8_bit_comparator_2_a_b_3;

  _8_bit_Comparator u_8_bit_comparator_1 (
    .A0_7({A0_15[8], A0_15[9], A0_15[10], A0_15[11], A0_15[12], A0_15[13], A0_15[14], A0_15[15]}),
    .B0_7({B0_15[8], B0_15[9], B0_15[10], B0_15[11], B0_15[12], B0_15[13], B0_15[14], B0_15[15]}),
    .A_B(n8_bit_comparator_1_a_b), .A_B_2(n8_bit_comparator_1_a_b_2), .A_B_3(n8_bit_comparator_1_a_b_3));
  _8_bit_Comparator u_8_bit_comparator_2 (
    .A0_7(A0_15[7:0]),
    .B0_7({B0_15[0], B0_15[1], B0_15[2], B0_15[3], B0_15[4], B0_15[5], B0_15[6], B0_15[7]}),
    .A_B(n8_bit_comparator_2_a_b), .A_B_2(n8_bit_comparator_2_a_b_2), .A_B_3(n8_bit_comparator_2_a_b_3));
  and and_1 (A_B_2, n8_bit_comparator_1_a_b_2, n8_bit_comparator_2_a_b_2);
  and and_2 (and_2_out, n8_bit_comparator_1_a_b_2, n8_bit_comparator_2_a_b_3);
  and and_3 (and_3_out, n8_bit_comparator_1_a_b_2, n8_bit_comparator_2_a_b);
  or or_1 (A_B, n8_bit_comparator_1_a_b, and_3_out);
  or or_2 (A_B_3, n8_bit_comparator_1_a_b_3, and_2_out);
endmodule

module _16_bit_Cascading_Comparator (
  input  A_B,
  input  A_B_2,
  input  A_B_3,
  input  [15:0] A0_7,
  input  [15:0] B0_7,
  output A_B_4,
  output A_B_5,
  output A_B_6
);

  wire n8_bit_cascading_comparator_1_a_b_4, n8_bit_cascading_comparator_1_a_b_5,
       n8_bit_cascading_comparator_1_a_b_6;

  _8_bit_Cascading_Comparator u_8_bit_cascading_comparator_1 (
    .A_B(A_B), .A_B_2(A_B_2), .A_B_3(A_B_3), .A0_7(A0_7[15:8]), .B0_7(B0_7[15:8]),
    .A_B_4(n8_bit_cascading_comparator_1_a_b_4), .A_B_5(n8_bit_cascading_comparator_1_a_b_5),
    .A_B_6(n8_bit_cascading_comparator_1_a_b_6));
  _8_bit_Cascading_Comparator u_8_bit_cascading_comparator_2 (
    .A_B(n8_bit_cascading_comparator_1_a_b_4), .A_B_2(n8_bit_cascading_comparator_1_a_b_5),
    .A_B_3(n8_bit_cascading_comparator_1_a_b_6), .A0_7(A0_7[7:0]), .B0_7(B0_7[7:0]), .A_B_4(A_B_4),
    .A_B_5(A_B_5), .A_B_6(A_B_6));
endmodule

module _2_1_MUX (
  input  S0,
  input  i0,
  input  i1,
  output Y
);

  wire and_1_out, and_2_out, not_1_out;

  not not_1 (not_1_out, S0);
  and and_1 (and_1_out, i0, not_1_out);
  and and_2 (and_2_out, S0, i1);
  or or_1 (Y, and_1_out, and_2_out);
endmodule

module _2_1_MUX_as_NOT_Gate (
  input  X,
  output X_prime
);

  _2_1_MUX u_2_1_mux_1 (.i0(1'b1), .i1(1'b0), .Y(X_prime), .S0(X));
endmodule

module _2_1_MUX_as_AND_Gate (
  input  y,
  input  x,
  output R_x_y
);

  _2_1_MUX u_2_1_mux_1 (.i0(1'b0), .i1(y), .Y(R_x_y), .S0(x));
endmodule

// 4:1 MUX
module _4_1_Cascading_MUX (
  input  i0,
  input  i1,
  input  i2,
  input  i3,
  input  S1,
  input  S0,
  output Y
);

  wire n2_1_mux_1_y, n2_1_mux_2_y;

  _2_1_MUX u_2_1_mux_1 (.i0(i0), .i1(i1), .Y(n2_1_mux_1_y), .S0(S0));
  _2_1_MUX u_2_1_mux_2 (.i0(i2), .i1(i3), .Y(n2_1_mux_2_y), .S0(S0));
  _2_1_MUX u_2_1_mux_3 (.i0(n2_1_mux_1_y), .i1(n2_1_mux_2_y), .Y(Y), .S0(S1));
endmodule

module Arithmetic_Circuit_using_Adder_and_MUX (
  input  Cin,
  input  S1,
  input  S0,
  input  A0,
  input  B0,
  input  A1,
  input  B1,
  input  A2,
  input  B2,
  input  A3,
  input  B3,
  output R0,
  output R1,
  output R2,
  output R3,
  output C4
);

  wire adder_1_cout, adder_2_cout, adder_3_cout, n4_1_cascading_mux_1_y, n4_1_cascading_mux_2_y,
       n4_1_cascading_mux_3_y, n4_1_cascading_mux_4_y, not_1_out, not_2_out, not_3_out, not_4_out;

  not not_1 (not_1_out, B0);
  not not_2 (not_2_out, B1);
  not not_3 (not_3_out, B2);
  not not_4 (not_4_out, B3);
  _4_1_Cascading_MUX u_4_1_cascading_mux_1 (
    .i0(B0), .i1(not_1_out), .i2(1'b0), .i3(1'b1), .Y(n4_1_cascading_mux_1_y), .S0(S0), .S1(S1));
  _4_1_Cascading_MUX u_4_1_cascading_mux_2 (
    .i0(B1), .i1(not_2_out), .i2(1'b0), .i3(1'b1), .Y(n4_1_cascading_mux_2_y), .S0(S0), .S1(S1));
  _4_1_Cascading_MUX u_4_1_cascading_mux_3 (
    .i0(B2), .i1(not_3_out), .i2(1'b0), .i3(1'b1), .Y(n4_1_cascading_mux_3_y), .S0(S0), .S1(S1));
  _4_1_Cascading_MUX u_4_1_cascading_mux_4 (
    .i0(B3), .i1(not_4_out), .i2(1'b0), .i3(1'b1), .Y(n4_1_cascading_mux_4_y), .S0(S0), .S1(S1));
  Adder #(.width(1)) adder_1 (.a(A0), .b(n4_1_cascading_mux_1_y), .out(R0), .cin(Cin), .cout(adder_1_cout));
  Adder #(.width(1)) adder_2 (.a(A1), .b(n4_1_cascading_mux_2_y), .out(R1), .cin(adder_1_cout), .cout(adder_2_cout));
  Adder #(.width(1)) adder_3 (.a(A2), .b(n4_1_cascading_mux_3_y), .out(R2), .cin(adder_2_cout), .cout(adder_3_cout));
  Adder #(.width(1)) adder_4 (.a(A3), .b(n4_1_cascading_mux_4_y), .out(R3), .cin(adder_3_cout), .cout(C4));

  // Notes on the sheet:
  //   Control Signals
  //   Data Signals
endmodule

// F.A
module Full_Adder (
  input  Cin,
  input  A,
  input  B,
  output S,
  output Cout
);

  Adder #(.width(1)) adder_1 (.a(A), .b(B), .out(S), .cin(Cin), .cout(Cout));
endmodule

// 1-bit CSA
module _3_1_bit_Numbers_CSA (
  input  C,
  input  A,
  input  B,
  output S,
  output Cout
);

  Adder #(.width(1)) adder_1 (.a(A), .b(B), .out(S), .cin(C), .cout(Cout));
endmodule

module _3_8_bit_Numbers_CSA (
  input  A7,
  input  B7,
  input  C7,
  input  A6,
  input  B6,
  input  C6,
  input  A5,
  input  B5,
  input  C5,
  input  A4,
  input  B4,
  input  C4,
  input  A3,
  input  B3,
  input  C3,
  input  A2,
  input  B2,
  input  C2,
  input  A1,
  input  B1,
  input  C1,
  input  A0,
  input  B0,
  input  C0,
  output Co8,
  output Co8_prime,
  output S7_prime,
  output S6_prime,
  output S5_prime,
  output S4_prime,
  output S3_prime,
  output S2_prime,
  output S1_prime,
  output S0_prime
);

  wire full_adder_2_cout, full_adder_3_cout, full_adder_4_cout, full_adder_5_cout, full_adder_6_cout,
       full_adder_7_cout, full_adder_8_cout, n3_1_bit_numbers_csa_1_s, n3_1_bit_numbers_csa_2_cout,
       n3_1_bit_numbers_csa_2_s, n3_1_bit_numbers_csa_3_cout, n3_1_bit_numbers_csa_3_s,
       n3_1_bit_numbers_csa_4_cout, n3_1_bit_numbers_csa_4_s, n3_1_bit_numbers_csa_5_cout,
       n3_1_bit_numbers_csa_5_s, n3_1_bit_numbers_csa_6_cout, n3_1_bit_numbers_csa_6_s,
       n3_1_bit_numbers_csa_7_cout, n3_1_bit_numbers_csa_7_s, n3_1_bit_numbers_csa_8_cout,
       n3_1_bit_numbers_csa_8_s;

  _3_1_bit_Numbers_CSA u_3_1_bit_numbers_csa_1 (.A(A7), .B(B7), .S(n3_1_bit_numbers_csa_1_s), .C(C7), .Cout(Co8));
  Full_Adder full_adder_1 (
    .A(n3_1_bit_numbers_csa_1_s), .B(n3_1_bit_numbers_csa_2_cout), .S(S7_prime), .Cin(full_adder_2_cout),
    .Cout(Co8_prime));
  _3_1_bit_Numbers_CSA u_3_1_bit_numbers_csa_2 (
    .A(A6), .B(B6), .S(n3_1_bit_numbers_csa_2_s), .C(C6), .Cout(n3_1_bit_numbers_csa_2_cout));
  Full_Adder full_adder_2 (
    .A(n3_1_bit_numbers_csa_2_s), .B(n3_1_bit_numbers_csa_3_cout), .S(S6_prime), .Cin(full_adder_3_cout),
    .Cout(full_adder_2_cout));
  _3_1_bit_Numbers_CSA u_3_1_bit_numbers_csa_3 (
    .A(A5), .B(B5), .S(n3_1_bit_numbers_csa_3_s), .C(C5), .Cout(n3_1_bit_numbers_csa_3_cout));
  Full_Adder full_adder_3 (
    .A(n3_1_bit_numbers_csa_3_s), .B(n3_1_bit_numbers_csa_4_cout), .S(S5_prime), .Cin(full_adder_4_cout),
    .Cout(full_adder_3_cout));
  _3_1_bit_Numbers_CSA u_3_1_bit_numbers_csa_4 (
    .A(A4), .B(A4), .S(n3_1_bit_numbers_csa_4_s), .C(C4), .Cout(n3_1_bit_numbers_csa_4_cout));
  Full_Adder full_adder_4 (
    .A(n3_1_bit_numbers_csa_4_s), .B(n3_1_bit_numbers_csa_5_cout), .S(S4_prime), .Cin(full_adder_5_cout),
    .Cout(full_adder_4_cout));
  _3_1_bit_Numbers_CSA u_3_1_bit_numbers_csa_5 (
    .A(A3), .B(B3), .S(n3_1_bit_numbers_csa_5_s), .C(C3), .Cout(n3_1_bit_numbers_csa_5_cout));
  Full_Adder full_adder_5 (
    .A(n3_1_bit_numbers_csa_5_s), .B(n3_1_bit_numbers_csa_6_cout), .S(S3_prime), .Cin(full_adder_6_cout),
    .Cout(full_adder_5_cout));
  _3_1_bit_Numbers_CSA u_3_1_bit_numbers_csa_6 (
    .A(A2), .B(B2), .S(n3_1_bit_numbers_csa_6_s), .C(C2), .Cout(n3_1_bit_numbers_csa_6_cout));
  Full_Adder full_adder_6 (
    .A(n3_1_bit_numbers_csa_6_s), .B(n3_1_bit_numbers_csa_7_cout), .S(S2_prime), .Cin(full_adder_7_cout),
    .Cout(full_adder_6_cout));
  _3_1_bit_Numbers_CSA u_3_1_bit_numbers_csa_7 (
    .A(A1), .B(B1), .S(n3_1_bit_numbers_csa_7_s), .C(C1), .Cout(n3_1_bit_numbers_csa_7_cout));
  Full_Adder full_adder_7 (
    .A(n3_1_bit_numbers_csa_7_s), .B(n3_1_bit_numbers_csa_8_cout), .S(S1_prime), .Cin(full_adder_8_cout),
    .Cout(full_adder_7_cout));
  _3_1_bit_Numbers_CSA u_3_1_bit_numbers_csa_8 (
    .A(A0), .B(B0), .S(n3_1_bit_numbers_csa_8_s), .C(C0), .Cout(n3_1_bit_numbers_csa_8_cout));
  Full_Adder full_adder_8 (.A(n3_1_bit_numbers_csa_8_s), .B(1'b0), .S(S0_prime), .Cin(1'b0), .Cout(full_adder_8_cout));

  assign B4 = A4;

  // Notes on the sheet:
  //   S7
  //   S6
  //   Co7
  //   Co7'
  //   Co6
  //   Co6'
  //   S5
  //   Co5
  //   Co5'
  //   S4
  //   Co4
  //   Co4'
  //   S3
  //   S2
  //   Co3
  //   Co3'
  //   Co2
  //   Co2'
  //   S1
  //   Co1
  //   Co1'
  //   S0
endmodule

// 8-bit CSA
module _3_8_bit_Numbers_CSA_with_Carry (
  input  [7:0] C0_7,
  input  [7:0] B0_7,
  input  [7:0] A0_7,
  output [7:0] S0_7,
  output [7:0] Co1_8
);

  _3_1_bit_Numbers_CSA u_3_1_bit_numbers_csa_1 (.A(A0_7[7]), .B(B0_7[7]), .S(S0_7[7]), .C(C0_7[7]), .Cout(Co1_8[7]));
  _3_1_bit_Numbers_CSA u_3_1_bit_numbers_csa_2 (.A(A0_7[6]), .B(B0_7[6]), .S(S0_7[6]), .C(C0_7[6]), .Cout(Co1_8[6]));
  _3_1_bit_Numbers_CSA u_3_1_bit_numbers_csa_3 (.A(A0_7[5]), .B(B0_7[5]), .S(S0_7[5]), .C(C0_7[5]), .Cout(Co1_8[5]));
  _3_1_bit_Numbers_CSA u_3_1_bit_numbers_csa_4 (.A(A0_7[4]), .B(B0_7[4]), .S(S0_7[4]), .C(C0_7[4]), .Cout(Co1_8[4]));
  _3_1_bit_Numbers_CSA u_3_1_bit_numbers_csa_5 (.A(A0_7[3]), .B(B0_7[3]), .S(S0_7[3]), .C(C0_7[3]), .Cout(Co1_8[3]));
  _3_1_bit_Numbers_CSA u_3_1_bit_numbers_csa_6 (.A(A0_7[2]), .B(B0_7[2]), .S(S0_7[2]), .C(C0_7[2]), .Cout(Co1_8[2]));
  _3_1_bit_Numbers_CSA u_3_1_bit_numbers_csa_7 (.A(A0_7[1]), .B(B0_7[1]), .S(S0_7[1]), .C(C0_7[1]), .Cout(Co1_8[1]));
  _3_1_bit_Numbers_CSA u_3_1_bit_numbers_csa_8 (.A(A0_7[0]), .B(B0_7[0]), .S(S0_7[0]), .C(C0_7[0]), .Cout(Co1_8[0]));
endmodule

module _7_8_bit_Numbers_CSA (
  input  [7:0] A0_7,
  input  [7:0] B0_7,
  input  [7:0] C0_7,
  input  [7:0] D0_7,
  input  [7:0] E0_7,
  input  [7:0] F0_7,
  input  [7:0] G0_7,
  output S0,
  output [7:0] C1_8,
  output [7:0] S1_8
);

  wire [6:0] n3_8_bit_numbers_csa_with_carry_6_s0_7;
  wire [7:0] n3_8_bit_numbers_csa_with_carry_1_co1_8, n3_8_bit_numbers_csa_with_carry_1_s0_7,
       n3_8_bit_numbers_csa_with_carry_2_co1_8, n3_8_bit_numbers_csa_with_carry_2_s0_7,
       n3_8_bit_numbers_csa_with_carry_3_co1_8, n3_8_bit_numbers_csa_with_carry_3_s0_7,
       n3_8_bit_numbers_csa_with_carry_5_co1_8, n3_8_bit_numbers_csa_with_carry_5_s0_7,
       n3_8_bit_numbers_csa_with_carry_6_co1_8, n3_8_bit_numbers_csa_with_carry_7_s0_7;
  wire [7:1] n3_8_bit_numbers_csa_with_carry_7_co1_8_2;
  wire [7:7] n3_8_bit_numbers_csa_with_carry_7_co1_8;

  _3_8_bit_Numbers_CSA_with_Carry u_3_8_bit_numbers_csa_with_carry_1 (
    .C0_7(C0_7), .B0_7(B0_7), .A0_7(A0_7), .S0_7(n3_8_bit_numbers_csa_with_carry_1_s0_7),
    .Co1_8(n3_8_bit_numbers_csa_with_carry_1_co1_8));
  _3_8_bit_Numbers_CSA_with_Carry u_3_8_bit_numbers_csa_with_carry_2 (
    .C0_7({n3_8_bit_numbers_csa_with_carry_7_co1_8[7], {7{1'b0}}}),
    .B0_7(n3_8_bit_numbers_csa_with_carry_5_co1_8),
    .A0_7({n3_8_bit_numbers_csa_with_carry_1_co1_8[7], {7{1'b0}}}),
    .S0_7(n3_8_bit_numbers_csa_with_carry_2_s0_7), .Co1_8(n3_8_bit_numbers_csa_with_carry_2_co1_8));
  _3_8_bit_Numbers_CSA_with_Carry u_3_8_bit_numbers_csa_with_carry_3 (
    .C0_7(n3_8_bit_numbers_csa_with_carry_6_co1_8), .B0_7(n3_8_bit_numbers_csa_with_carry_2_s0_7),
    .A0_7(n3_8_bit_numbers_csa_with_carry_2_co1_8), .S0_7(n3_8_bit_numbers_csa_with_carry_3_s0_7),
    .Co1_8(n3_8_bit_numbers_csa_with_carry_3_co1_8));
  _3_8_bit_Numbers_CSA_with_Carry u_3_8_bit_numbers_csa_with_carry_4 (
    .C0_7({1'b0, n3_8_bit_numbers_csa_with_carry_6_s0_7}), .B0_7(n3_8_bit_numbers_csa_with_carry_3_s0_7),
    .A0_7(n3_8_bit_numbers_csa_with_carry_3_co1_8), .S0_7(S1_8), .Co1_8(C1_8));
  _3_8_bit_Numbers_CSA_with_Carry u_3_8_bit_numbers_csa_with_carry_5 (
    .C0_7(n3_8_bit_numbers_csa_with_carry_7_s0_7), .B0_7(n3_8_bit_numbers_csa_with_carry_1_s0_7),
    .A0_7({n3_8_bit_numbers_csa_with_carry_1_co1_8[6:0], 1'b0}),
    .S0_7(n3_8_bit_numbers_csa_with_carry_5_s0_7), .Co1_8(n3_8_bit_numbers_csa_with_carry_5_co1_8));
  _3_8_bit_Numbers_CSA_with_Carry u_3_8_bit_numbers_csa_with_carry_6 (
    .C0_7(G0_7), .B0_7(n3_8_bit_numbers_csa_with_carry_5_s0_7),
    .A0_7({n3_8_bit_numbers_csa_with_carry_7_co1_8_2, 1'b0}),
    .S0_7({n3_8_bit_numbers_csa_with_carry_6_s0_7, S0}), .Co1_8(n3_8_bit_numbers_csa_with_carry_6_co1_8));
  _3_8_bit_Numbers_CSA_with_Carry u_3_8_bit_numbers_csa_with_carry_7 (
    .C0_7(F0_7), .B0_7(E0_7), .A0_7(D0_7), .S0_7(n3_8_bit_numbers_csa_with_carry_7_s0_7),
    .Co1_8({n3_8_bit_numbers_csa_with_carry_7_co1_8[7], n3_8_bit_numbers_csa_with_carry_7_co1_8_2}));

  // Notes on the sheet:
  //   C8
  //   C8
endmodule
