// Logisim project Comparator.circ as structural Verilog: 9 circuits, main circuit 1-bit Comparator
module _1_bit_Comparator (
  input  A,
  input  B,
  output A_B,
  output A_B_2,
  output A_B_3
);

  wire not_1_out, not_2_out;

  not not_1 (not_1_out, A);
  not not_2 (not_2_out, B);
  and AND (A_B, not_1_out, B);
  and AND_2 (A_B_3, A, not_2_out);
  nor NOR (A_B_2, A_B, A_B_3);
endmodule

module _2_bit_Comparator (
  input  A1,
  input  B1,
  input  A0,
  input  B0,
  output A_B,
  output A_B_2,
  output A_B_3
);

  wire and_2_out, and_3_out, n1_bit_comparator_1_a_b, n1_bit_comparator_1_a_b_2, n1_bit_comparator_1_a_b_3,
       n1_bit_comparator_2_a_b, n1_bit_comparator_2_a_b_2, n1_bit_comparator_2_a_b_3;

  _1_bit_Comparator u_1_bit_comparator_1 (
    .A(A1), .B(B1), .A_B(n1_bit_comparator_1_a_b), .A_B_2(n1_bit_comparator_1_a_b_2),
    .A_B_3(n1_bit_comparator_1_a_b_3));
  _1_bit_Comparator u_1_bit_comparator_2 (
    .A(A0), .B(B0), .A_B(n1_bit_comparator_2_a_b), .A_B_2(n1_bit_comparator_2_a_b_2),
    .A_B_3(n1_bit_comparator_2_a_b_3));
  and and_1 (A_B_2, n1_bit_comparator_1_a_b_2, n1_bit_comparator_2_a_b_2);
  and and_2 (and_2_out, n1_bit_comparator_1_a_b_2, n1_bit_comparator_2_a_b_3);
  and and_3 (and_3_out, n1_bit_comparator_1_a_b_2, n1_bit_comparator_2_a_b);
  or or_1 (A_B, n1_bit_comparator_1_a_b, and_3_out);
  or or_2 (A_B_3, n1_bit_comparator_1_a_b_3, and_2_out);
endmodule

// 2-bit CC
module _2_bit_Cascading_Comparator (
  input  A_B,
  input  A_B_2,
  input  A_B_3,
  input  A1,
  input  A0,
  input  B1,
  input  B0,
  output A_B_4,
  output A_B_5,
  output A_B_6
);

  wire and_2_out, and_3_out, n2_bit_comparator_1_a_b, n2_bit_comparator_1_a_b_2, n2_bit_comparator_1_a_b_3;

  _2_bit_Comparator u_2_bit_comparator_1 (
    .A1(A1), .B1(B1), .A0(A0), .B0(B0), .A_B(n2_bit_comparator_1_a_b), .A_B_2(n2_bit_comparator_1_a_b_2),
    .A_B_3(n2_bit_comparator_1_a_b_3));
  and and_1 (A_B_5, A_B_2, n2_bit_comparator_1_a_b_2);
  and and_2 (and_2_out, A_B_2, n2_bit_comparator_1_a_b_3);
  and and_3 (and_3_out, A_B_2, n2_bit_comparator_1_a_b);
  or or_1 (A_B_4, A_B, and_3_out);
  or or_2 (A_B_6, A_B_3, and_2_out);
endmodule

module _4_bit_Comparator (
  input  [3:0] A0_3,
  input  [3:0] B0_3,
  output A_B,
  output A_B_2,
  output A_B_3
);

  wire and_2_out, and_3_out, n2_bit_comparator_1_a_b, n2_bit_comparator_1_a_b_2, n2_bit_comparator_1_a_b_3,
       n2_bit_comparator_2_a_b, n2_bit_comparator_2_a_b_2, n2_bit_comparator_2_a_b_3;

  _2_bit_Comparator u_2_bit_comparator_1 (
    .A1(A0_3[3]), .B1(B0_3[3]), .A0(A0_3[2]), .B0(B0_3[2]), .A_B(n2_bit_comparator_1_a_b),
    .A_B_2(n2_bit_comparator_1_a_b_2), .A_B_3(n2_bit_comparator_1_a_b_3));
  _2_bit_Comparator u_2_bit_comparator_2 (
    .A1(A0_3[1]), .B1(B0_3[1]), .A0(A0_3[0]), .B0(B0_3[0]), .A_B(n2_bit_comparator_2_a_b),
    .A_B_2(n2_bit_comparator_2_a_b_2), .A_B_3(n2_bit_comparator_2_a_b_3));
  and and_1 (A_B_2, n2_bit_comparator_1_a_b_2, n2_bit_comparator_2_a_b_2);
  and and_2 (and_2_out, n2_bit_comparator_1_a_b_2, n2_bit_comparator_2_a_b);
  and and_3 (and_3_out, n2_bit_comparator_1_a_b_2, n2_bit_comparator_2_a_b_3);
  or or_1 (A_B, n2_bit_comparator_1_a_b, and_2_out);
  or or_2 (A_B_3, n2_bit_comparator_1_a_b_3, and_3_out);
endmodule

module _4_bit_Cascading_Comparator (
  input  A_B,
  input  A_B_2,
  input  A_B_3,
  input  [3:0] A0_3,
  input  [3:0] B0_3,
  output A_B_4,
  output A_B_5,
  output A_B_6
);

  wire n2_bit_cascading_comparator_1_a_b_4, n2_bit_cascading_comparator_1_a_b_5,
       n2_bit_cascading_comparator_1_a_b_6;

  _2_bit_Cascading_Comparator u_2_bit_cascading_comparator_1 (
    .A_B(A_B), .A_B_2(A_B_2), .A_B_3(A_B_3), .A1(A0_3[3]), .A0(A0_3[2]), .B1(B0_3[3]), .B0(B0_3[2]),
    .A_B_4(n2_bit_cascading_comparator_1_a_b_4), .A_B_5(n2_bit_cascading_comparator_1_a_b_5),
    .A_B_6(n2_bit_cascading_comparator_1_a_b_6));
  _2_bit_Cascading_Comparator u_2_bit_cascading_comparator_2 (
    .A_B(n2_bit_cascading_comparator_1_a_b_4), .A_B_2(n2_bit_cascading_comparator_1_a_b_5),
    .A_B_3(n2_bit_cascading_comparator_1_a_b_6), .A1(A0_3[1]), .A0(A0_3[0]), .B1(B0_3[1]), .B0(B0_3[0]),
    .A_B_4(A_B_4), .A_B_5(A_B_5), .A_B_6(A_B_6));
endmodule

module _8_bit_Comparator (
  input  [7:0] A0_7,
  input  [7:0] B0_7,
  output A_B,
  output A_B_2,
  output A_B_3
);

  wire and_2_out, and_3_out, n4_bit_comparator_1_a_b, n4_bit_comparator_1_a_b_2, n4_bit_comparator_1_a_b_3,
       n4_bit_comparator_2_a_b, n4_bit_comparator_2_a_b_2, n4_bit_comparator_2_a_b_3;

  _4_bit_Comparator u_4_bit_comparator_1 (
    .A0_3(A0_7[7:4]), .B0_3(B0_7[7:4]), .A_B(n4_bit_comparator_1_a_b), .A_B_2(n4_bit_comparator_1_a_b_2),
    .A_B_3(n4_bit_comparator_1_a_b_3));
  _4_bit_Comparator u_4_bit_comparator_2 (
    .A0_3(A0_7[3:0]), .B0_3(B0_7[3:0]), .A_B(n4_bit_comparator_2_a_b), .A_B_2(n4_bit_comparator_2_a_b_2),
    .A_B_3(n4_bit_comparator_2_a_b_3));
  and and_1 (A_B_2, n4_bit_comparator_1_a_b_2, n4_bit_comparator_2_a_b_2);
  and and_2 (and_2_out, n4_bit_comparator_1_a_b_2, n4_bit_comparator_2_a_b_3);
  and and_3 (and_3_out, n4_bit_comparator_1_a_b_2, n4_bit_comparator_2_a_b);
  or or_1 (A_B, n4_bit_comparator_1_a_b, and_3_out);
  or or_2 (A_B_3, n4_bit_comparator_1_a_b_3, and_2_out);
endmodule

module _8_bit_Cascading_Comparator (
  input  A_B,
  input  A_B_2,
  input  A_B_3,
  input  [7:0] A0_7,
  input  [7:0] B0_7,
  output A_B_4,
  output A_B_5,
  output A_B_6
);

  wire n4_bit_cascading_comparator_1_a_b_4, n4_bit_cascading_comparator_1_a_b_5,
       n4_bit_cascading_comparator_1_a_b_6;

  _4_bit_Cascading_Comparator u_4_bit_cascading_comparator_1 (
    .A_B(A_B), .A_B_2(A_B_2), .A_B_3(A_B_3), .A0_3(A0_7[7:4]), .B0_3(B0_7[7:4]),
    .A_B_4(n4_bit_cascading_comparator_1_a_b_4), .A_B_5(n4_bit_cascading_comparator_1_a_b_5),
    .A_B_6(n4_bit_cascading_comparator_1_a_b_6));
  _4_bit_Cascading_Comparator u_4_bit_cascading_comparator_2 (
    .A_B(n4_bit_cascading_comparator_1_a_b_4), .A_B_2(n4_bit_cascading_comparator_1_a_b_5),
    .A_B_3(n4_bit_cascading_comparator_1_a_b_6), .A0_3(A0_7[3:0]), .B0_3(B0_7[3:0]), .A_B_4(A_B_4),
    .A_B_5(A_B_5), .A_B_6(A_B_6));
endmodule

module _16_bit_Comparator (
  input  [15:0] A0_15,
  input  [15:0] B0_15,
  output A_B,
  output A_B_2,
  output A_B_3
);

  wire and_2_out, and_3_out, n8_bit_comparator_1_a_b, n8_bit_comparator_1_a_b_2, n8_bit_comparator_1_a_b_3,
       n8_bit_comparator_2_a_b, n8_bit_comparator_2_a_b_2, n8_bit_comparator_2_a_b_3;

  _8_bit_Comparator u_8_bit_comparator_1 (
    .A0_7({A0_15[8], A0_15[9], A0_15[10], A0_15[11], A0_15[12], A0_15[13], A0_15[14], A0_15[15]}),
    .B0_7({B0_15[8], B0_15[9], B0_15[10], B0_15[11], B0_15[12], B0_15[13], B0_15[14], B0_15[15]}),
    .A_B(n8_bit_comparator_1_a_b), .A_B_2(n8_bit_comparator_1_a_b_2), .A_B_3(n8_bit_comparator_1_a_b_3));
  _8_bit_Comparator u_8_bit_comparator_2 (
    .A0_7({A0_15[0], A0_15[1], A0_15[2], A0_15[3], A0_15[4], A0_15[5], A0_15[6], A0_15[7]}),
    .B0_7({B0_15[0], B0_15[1], B0_15[2], B0_15[3], B0_15[4], B0_15[5], B0_15[6], B0_15[7]}),
    .A_B(n8_bit_comparator_2_a_b), .A_B_2(n8_bit_comparator_2_a_b_2), .A_B_3(n8_bit_comparator_2_a_b_3));
  and and_1 (A_B_2, n8_bit_comparator_1_a_b_2, n8_bit_comparator_2_a_b_2);
  and and_2 (and_2_out, n8_bit_comparator_1_a_b_2, n8_bit_comparator_2_a_b);
  and and_3 (and_3_out, n8_bit_comparator_1_a_b_2, n8_bit_comparator_2_a_b_3);
  or or_1 (A_B, n8_bit_comparator_1_a_b, and_2_out);
  or or_2 (A_B_3, n8_bit_comparator_1_a_b_3, and_3_out);
endmodule

module _16_bit_Cascading_Comparator (
  input  A_B,
  input  A_B_2,
  input  A_B_3,
  input  [15:0] A0_15,
  input  [15:0] B0_15,
  output A_B_4,
  output A_B_5,
  output A_B_6
);

  wire n8_bit_cascading_comparator_1_a_b_4, n8_bit_cascading_comparator_1_a_b_5,
       n8_bit_cascading_comparator_1_a_b_6;

  _8_bit_Cascading_Comparator u_8_bit_cascading_comparator_1 (
    .A_B(A_B), .A_B_2(A_B_2), .A_B_3(A_B_3), .A0_7(A0_15[15:8]), .B0_7(B0_15[15:8]),
    .A_B_4(n8_bit_cascading_comparator_1_a_b_4), .A_B_5(n8_bit_cascading_comparator_1_a_b_5),
    .A_B_6(n8_bit_cascading_comparator_1_a_b_6));
  _8_bit_Cascading_Comparator u_8_bit_cascading_comparator_2 (
    .A_B(n8_bit_cascading_comparator_1_a_b_4), .A_B_2(n8_bit_cascading_comparator_1_a_b_5),
    .A_B_3(n8_bit_cascading_comparator_1_a_b_6), .A0_7(A0_15[7:0]), .B0_7(B0_15[7:0]), .A_B_4(A_B_4),
    .A_B_5(A_B_5), .A_B_6(A_B_6));
endmodule
