// Logisim project DeMux.circ as structural Verilog: 7 circuits, main circuit 1:2 DeMUX
module _1_2_DeMUX (
  input  i0,
  input  S0,
  output y0,
  output y1
);

  wire not_1_out;

  not not_1 (not_1_out, S0);
  and and_1 (y0, i0, not_1_out);
  and and_2 (y1, i0, S0);
endmodule

module _1_4_DeMux (
  input  i0,
  input  S1,
  input  S0,
  output y0,
  output y1,
  output y2,
  output y3
);

  wire not_1_out, not_2_out;

  not not_1 (not_1_out, S1);
  not not_2 (not_2_out, S0);
  and and_1 (y0, i0, not_2_out, not_1_out);
  and and_2 (y1, i0, not_1_out, S0);
  and and_3 (y2, i0, S1, not_2_out);
  and and_4 (y3, i0, S1, S0);
endmodule

module _1_4_Cascading_DeMux (
  input  i0,
  input  S1,
  input  S0,
  output y0,
  output y1,
  output y2,
  output y3
);

  wire n1_2_demux_1_y0, n1_2_demux_1_y1;

  _1_2_DeMUX u_1_2_demux_1 (.i0(i0), .y0(n1_2_demux_1_y0), .y1(n1_2_demux_1_y1), .S0(S1));
  _1_2_DeMUX u_1_2_demux_2 (.i0(n1_2_demux_1_y0), .y0(y0), .y1(y1), .S0(S0));
  _1_2_DeMUX u_1_2_demux_3 (.i0(n1_2_demux_1_y1), .y0(y2), .y1(y3), .S0(S0));
endmodule

// 1:8 DeMux
module _1_8_Cascading_DeMux (
  input  i0,
  input  S2,
  input  S1,
  input  S0,
  output y0,
  output y1,
  output y2,
  output y3,
  output y4,
  output y5,
  output y6,
  output y7
);

  wire n1_2_demux_1_y0, n1_2_demux_1_y1;

  _1_2_DeMUX u_1_2_demux_1 (.i0(i0), .y0(n1_2_demux_1_y0), .y1(n1_2_demux_1_y1), .S0(S2));
  _1_4_DeMux u_1_4_demux_1 (.i0(n1_2_demux_1_y0), .y0(y0), .y1(y1), .y2(y2), .y3(y3), .S1(S1), .S0(S0));
  _1_4_DeMux u_1_4_demux_2 (.i0(n1_2_demux_1_y1), .y0(y4), .y1(y5), .y2(y6), .y3(y7), .S1(S1), .S0(S0));
endmodule

// 1:16 DeMux
module _1_16_Cascading_DeMux (
  input  i0,
  input  S3,
  input  S2,
  input  S1,
  input  S0,
  output [7:0] y0_y7,
  output [7:0] y8_y15
);

  wire n1_2_demux_1_y0, n1_2_demux_1_y1;

  _1_2_DeMUX u_1_2_demux_1 (.i0(i0), .y0(n1_2_demux_1_y0), .y1(n1_2_demux_1_y1), .S0(S3));
  _1_8_Cascading_DeMux u_1_8_cascading_demux_1 (
    .i0(n1_2_demux_1_y0), .y0(y0_y7[0]), .y1(y0_y7[1]), .y2(y0_y7[2]), .y3(y0_y7[3]), .y4(y0_y7[4]),
    .y5(y0_y7[5]), .y6(y0_y7[6]), .y7(y0_y7[7]), .S2(S2), .S1(S1), .S0(S0));
  _1_8_Cascading_DeMux u_1_8_cascading_demux_2 (
    .i0(n1_2_demux_1_y1), .y0(y8_y15[0]), .y1(y8_y15[1]), .y2(y8_y15[2]), .y3(y8_y15[3]), .y4(y8_y15[4]),
    .y5(y8_y15[5]), .y6(y8_y15[6]), .y7(y8_y15[7]), .S2(S2), .S1(S1), .S0(S0));
endmodule

// 1:32 DeMux
module _1_32_Cascading_DeMux (
  input  i0,
  input  S4,
  input  S3,
  input  S2,
  input  S1,
  input  S0,
  output [15:0] y0_y15,
  output [15:0] y16_y31
);

  wire n1_2_demux_1_y0, n1_2_demux_1_y1;

  _1_2_DeMUX u_1_2_demux_1 (.i0(i0), .y0(n1_2_demux_1_y0), .y1(n1_2_demux_1_y1), .S0(S4));
  _1_16_Cascading_DeMux u_1_16_cascading_demux_1 (
    .i0(n1_2_demux_1_y0), .y0_y7(y0_y15[7:0]), .y8_y15(y0_y15[15:8]), .S3(S3), .S2(S2), .S1(S1), .S0(S0));
  _1_16_Cascading_DeMux u_1_16_cascading_demux_2 (
    .i0(n1_2_demux_1_y1), .y0_y7(y16_y31[7:0]), .y8_y15(y16_y31[15:8]), .S3(S3), .S2(S2), .S1(S1), .S0(S0));
endmodule

module _1_64_Cascading_DeMux (
  input  i0,
  input  S5,
  input  S4,
  input  S3,
  input  S2,
  input  S1,
  input  S0,
  output [31:0] y0_y31,
  output [31:0] y32_y63
);

  wire n1_2_demux_1_y0, n1_2_demux_1_y1;

  _1_2_DeMUX u_1_2_demux_1 (.i0(i0), .y0(n1_2_demux_1_y0), .y1(n1_2_demux_1_y1), .S0(S5));
  _1_32_Cascading_DeMux u_1_32_cascading_demux_1 (
    .i0(n1_2_demux_1_y0), .y0_y15(y0_y31[15:0]), .y16_y31(y0_y31[31:16]), .S4(S4), .S3(S3), .S2(S2), .S1(S1),
    .S0(S0));
  _1_32_Cascading_DeMux u_1_32_cascading_demux_2 (
    .i0(n1_2_demux_1_y1), .y0_y15(y32_y63[15:0]), .y16_y31(y32_y63[31:16]), .S4(S4), .S3(S3), .S2(S2),
    .S1(S1), .S0(S0));
endmodule
