// Logisim project Decoder.circ as structural Verilog: 5 circuits, main circuit 1:2 Decoder
module _1_2_Decoder (
  input  C,
  input  Enable,
  output y1,
  output y0
);

  wire not_1_out;

  not not_1 (not_1_out, C);
  and and_1 (y1, Enable, C);
  and and_2 (y0, Enable, not_1_out);
endmodule

module _2_4_Decoder (
  input  Enable,
  input  C1,
  input  C0,
  output y0,
  output y1,
  output y2,
  output y3
);

  wire not_1_out, not_2_out;

  not not_1 (not_1_out, C1);
  not not_2 (not_2_out, C0);
  and and_1 (y0, Enable, not_2_out, not_1_out);
  and and_2 (y1, Enable, C0, not_1_out);
  and and_3 (y2, Enable, C1, not_2_out);
  and and_4 (y3, Enable, C1, C0);
endmodule

// 2:4 Decoder
module _2_4_Cascading_Decoder (
  input  Enable,
  input  C1,
  input  C0,
  output y0,
  output y1,
  output y2,
  output y3
);

  wire n1_2_decoder_1_y0, n1_2_decoder_1_y1;

  _1_2_Decoder u_1_2_decoder_1 (.y1(n1_2_decoder_1_y1), .y0(n1_2_decoder_1_y0), .C(C1), .Enable(Enable));
  _1_2_Decoder u_1_2_decoder_2 (.y1(y1), .y0(y0), .C(C0), .Enable(n1_2_decoder_1_y0));
  _1_2_Decoder u_1_2_decoder_3 (.y1(y3), .y0(y2), .C(C0), .Enable(n1_2_decoder_1_y1));
endmodule

module _3_8_Cascading_Decoder (
  input  Enable,
  input  C1,
  input  C2,
  input  C0,
  output y0,
  output y1,
  output y2,
  output y3,
  output y4,
  output y5,
  output y6,
  output y7
);

  wire n1_2_decoder_1_y0, n1_2_decoder_1_y1;

  _1_2_Decoder u_1_2_decoder_1 (.y1(n1_2_decoder_1_y1), .y0(n1_2_decoder_1_y0), .C(C2), .Enable(Enable));
  _2_4_Cascading_Decoder u_2_4_cascading_decoder_1 (
    .C1(C1), .C0(C0), .y0(y0), .y1(y1), .y2(y2), .y3(y3), .Enable(n1_2_decoder_1_y0));
  _2_4_Cascading_Decoder u_2_4_cascading_decoder_2 (
    .C1(C1), .C0(C0), .y0(y4), .y1(y5), .y2(y6), .y3(y7), .Enable(n1_2_decoder_1_y1));
endmodule

module _4_16_Cascading_Decoder (
  input  C1,
  input  C0,
  input  Enable,
  input  C3,
  input  C2,
  output y0,
  output y1,
  output y2,
  output y3,
  output y4,
  output y5,
  output y6,
  output y7,
  output y8,
  output y9,
  output y10,
  output y11,
  output y12,
  output y13,
  output y14,
  output y15
);

  wire n2_4_cascading_decoder_1_y0, n2_4_cascading_decoder_1_y1, n2_4_cascading_decoder_1_y2,
       n2_4_cascading_decoder_1_y3;

  _2_4_Cascading_Decoder u_2_4_cascading_decoder_1 (
    .C1(C3), .C0(C2), .y0(n2_4_cascading_decoder_1_y0), .y1(n2_4_cascading_decoder_1_y1),
    .y2(n2_4_cascading_decoder_1_y2), .y3(n2_4_cascading_decoder_1_y3), .Enable(Enable));
  _2_4_Cascading_Decoder u_2_4_cascading_decoder_2 (
    .C1(C1), .C0(C0), .y0(y0), .y1(y1), .y2(y2), .y3(y3), .Enable(n2_4_cascading_decoder_1_y0));
  _2_4_Cascading_Decoder u_2_4_cascading_decoder_3 (
    .C1(C1), .C0(C0), .y0(y4), .y1(y5), .y2(y6), .y3(y7), .Enable(n2_4_cascading_decoder_1_y1));
  _2_4_Cascading_Decoder u_2_4_cascading_decoder_4 (
    .C1(C1), .C0(C0), .y0(y8), .y1(y9), .y2(y10), .y3(y11), .Enable(n2_4_cascading_decoder_1_y2));
  _2_4_Cascading_Decoder u_2_4_cascading_decoder_5 (
    .C1(C1), .C0(C0), .y0(y12), .y1(y13), .y2(y14), .y3(y15), .Enable(n2_4_cascading_decoder_1_y3));
endmodule
