// Logisim project Encoder.circ as structural Verilog: 2 circuits, main circuit 2:1 Encoder
module _2_1_Encoder (
  input  Enable,
  input  i0,
  input  i1,
  output out_4
);

  wire and_1_out, and_2_out, not_1_out;

  not not_1 (not_1_out, i0);
  and and_1 (and_1_out, not_1_out, Enable);
  and and_2 (and_2_out, Enable, i1);
  or or_1 (out_4, and_1_out, and_2_out);
endmodule

module _4_2_Encoder (
  input  i0,
  input  i1,
  input  i2,
  input  i3,
  output C0,
  output C1
);

  or or_1 (C0, i1, i3);
  or or_2 (C1, i2, i3);
endmodule
