// Logisim project Gates.circ as structural Verilog: 1 circuit, main circuit main
module main (
  input  in_1,
  input  in_2,
  input  in_3,
  input  in_4,
  input  in_5,
  input  in_6,
  input  in_7,
  input  in_8,
  input  in_9,
  input  in_10,
  input  in_11
);

  wire AND_out, pull_resistor_1_node, pull_resistor_2_node, pull_resistor_3_node, transistor_1_out,
       transistor_2_out, transistor_3_out, transistor_5_out, transistor_6_out;

  Transistor #(.\type ("n")) transistor_1 (.in(in_1), .out(transistor_1_out), .gate(in_2));
  Transistor #(.\type ("n")) transistor_2 (.in(transistor_1_out), .out(transistor_2_out), .gate(in_5));
  Pull_Resistor pull_resistor_1 (.node(pull_resistor_1_node));
  Transistor transistor_3 (.in(in_6), .out(transistor_3_out), .gate(in_8));
  LED led_1 (.in(transistor_2_out));
  Transistor transistor_4 (.in(in_6), .out(transistor_3_out), .gate(in_10));
  Pull_Resistor pull_resistor_2 (.node(pull_resistor_2_node));
  LED led_2 (.in(transistor_3_out));
  Transistor transistor_5 (.in(pull_resistor_3_node), .out(transistor_5_out), .gate(in_9));
  Transistor transistor_6 (.in(transistor_5_out), .out(transistor_6_out), .gate(in_11));
  and AND (AND_out, in_3, in_4);
  Pull_Resistor pull_resistor_3 (.node(pull_resistor_3_node));
  LED led_3 (.in(pull_resistor_3_node));
  LED led_4 (.in(AND_out));
  // also tied to GND on the sheet: {pull_resistor_1_node, pull_resistor_2_node, transistor_6_out}

  // Notes on the sheet:
  //   AND GATE USING TRANSISTOR
  //   OR GATE USING TRANSISTOR
  //   AND GATE
endmodule
