// Logisim project MUX and Arithmetic Circuit.circ as structural Verilog: 9 circuits, main circuit 2:1 MUX
module _2_1_MUX (
  input  S0,
  input  i0,
  input  i1,
  output Y
);

  wire AND_2_out, AND_out, NOT_out;

  not NOT (NOT_out, S0);
  and AND (AND_out, i0, NOT_out);
  and AND_2 (AND_2_out, S0, i1);
  or OR (Y, AND_out, AND_2_out);
endmodule

module _2_1_MUX_as_NOT_Gate (
  input  X,
  output X_prime
);

  _2_1_MUX u_2_1_mux_1 (.i0(1'b1), .i1(1'b0), .Y(X_prime), .S0(X));

  // Notes on the sheet:
  //   CONSTANT
  //   INPUT
  //   OUTPUT
endmodule

module _2_1_MUX_as_AND_Gate (
  input  Y,
  input  X,
  output R_X_Y
);

  _2_1_MUX u_2_1_mux_1 (.i0(1'b0), .i1(Y), .Y(R_X_Y), .S0(X));

  // Notes on the sheet:
  //   CONSTANT
  //   INPUT Y
  //   INPUT X
  //   OUTPUT X.Y
endmodule

// 4:1 MUX
module _4_1_Cascading_MUX (
  input  i0,
  input  i1,
  input  i2,
  input  i3,
  input  S0,
  input  S1,
  output Y
);

  wire n2_1_mux_1_y, n2_1_mux_2_y;

  _2_1_MUX u_2_1_mux_1 (.i0(i0), .i1(i1), .Y(n2_1_mux_1_y), .S0(S0));
  _2_1_MUX u_2_1_mux_2 (.i0(i2), .i1(i3), .Y(n2_1_mux_2_y), .S0(S0));
  _2_1_MUX u_2_1_mux_3 (.i0(n2_1_mux_1_y), .i1(n2_1_mux_2_y), .Y(Y), .S0(S1));
endmodule

// 8:1 MUX
module _8_1_Cascading_MUX (
  input  i0,
  input  i1,
  input  i2,
  input  i3,
  input  i4,
  input  i5,
  input  i6,
  input  i7,
  input  S0,
  input  S1,
  input  S2,
  output Y
);

  wire n4_1_cascading_mux_1_y, n4_1_cascading_mux_2_y;

  _4_1_Cascading_MUX u_4_1_cascading_mux_1 (
    .i0(i0), .i1(i1), .i2(i2), .i3(i3), .Y(n4_1_cascading_mux_1_y), .S0(S0), .S1(S1));
  _4_1_Cascading_MUX u_4_1_cascading_mux_2 (
    .i0(i4), .i1(i5), .i2(i6), .i3(i7), .Y(n4_1_cascading_mux_2_y), .S0(S0), .S1(S1));
  _2_1_MUX u_2_1_mux_1 (.i0(n4_1_cascading_mux_1_y), .i1(n4_1_cascading_mux_2_y), .Y(Y), .S0(S2));
endmodule

// 16:1 MUX
module _16_1_Cascading_MUX (
  input  [7:0] i7_0,
  input  [7:0] i15_8,
  input  S0,
  input  S1,
  input  S2,
  input  S3,
  output Y
);

  wire n8_1_cascading_mux_1_y, n8_1_cascading_mux_2_y;

  _8_1_Cascading_MUX u_8_1_cascading_mux_1 (
    .i0(i7_0[0]), .i1(i7_0[1]), .i2(i7_0[2]), .i3(i7_0[3]), .i4(i7_0[4]), .i5(i7_0[5]), .i6(i7_0[6]),
    .i7(i7_0[7]), .S0(S0), .S1(S1), .S2(S2), .Y(n8_1_cascading_mux_1_y));
  _8_1_Cascading_MUX u_8_1_cascading_mux_2 (
    .i0(i15_8[0]), .i1(i15_8[1]), .i2(i15_8[2]), .i3(i15_8[3]), .i4(i15_8[4]), .i5(i15_8[5]), .i6(i15_8[6]),
    .i7(i15_8[7]), .S0(S0), .S1(S1), .S2(S2), .Y(n8_1_cascading_mux_2_y));
  _2_1_MUX u_2_1_mux_1 (.i0(n8_1_cascading_mux_1_y), .i1(n8_1_cascading_mux_2_y), .Y(Y), .S0(S3));
endmodule

// 32:1 MUX
module _32_1_Cascading_MUX (
  input  [15:0] i15_0,
  input  [15:0] i31_16,
  input  S4,
  input  S0,
  input  S1,
  input  S2,
  input  S3,
  output Y
);

  wire n16_1_cascading_mux_1_y, n16_1_cascading_mux_2_y;

  _16_1_Cascading_MUX u_16_1_cascading_mux_1 (
    .i7_0(i15_0[7:0]), .i15_8(i15_0[15:8]), .Y(n16_1_cascading_mux_1_y), .S0(S0), .S1(S1), .S2(S2), .S3(S3));
  _16_1_Cascading_MUX u_16_1_cascading_mux_2 (
    .i7_0(i31_16[7:0]), .i15_8(i31_16[15:8]), .Y(n16_1_cascading_mux_2_y), .S0(S0), .S1(S1), .S2(S2), .S3(S3));
  _2_1_MUX u_2_1_mux_1 (.i0(n16_1_cascading_mux_1_y), .i1(n16_1_cascading_mux_2_y), .Y(Y), .S0(S4));
endmodule

module _64_1_Cascading_MUX (
  input  [31:0] i31_0,
  input  [31:0] i63_32,
  input  S0,
  input  S1,
  input  S2,
  input  S3,
  input  S4,
  input  S5,
  output Y
);

  wire n32_1_cascading_mux_1_y, n32_1_cascading_mux_2_y;

  _32_1_Cascading_MUX u_32_1_cascading_mux_1 (
    .i15_0(i31_0[15:0]), .i31_16(i31_0[31:16]), .S0(S0), .S1(S1), .S2(S2), .S3(S3), .S4(S4),
    .Y(n32_1_cascading_mux_1_y));
  _32_1_Cascading_MUX u_32_1_cascading_mux_2 (
    .i15_0(i63_32[15:0]), .i31_16(i63_32[31:16]), .S0(S0), .S1(S1), .S2(S2), .S3(S3), .S4(S4),
    .Y(n32_1_cascading_mux_2_y));
  _2_1_MUX u_2_1_mux_1 (.i0(n32_1_cascading_mux_1_y), .i1(n32_1_cascading_mux_2_y), .Y(Y), .S0(S5));
endmodule

module _4_bit_Arithmetic_Circuit_using_Adder_and_4_1_MUX (
  input  Cin,
  input  S1,
  input  S0,
  input  A0,
  input  B0,
  input  A1,
  input  B1,
  input  A2,
  input  B2,
  input  A3,
  input  B3,
  output R0,
  output R1,
  output R2,
  output R3,
  output C4
);

  wire adder_1_cout, adder_2_cout, adder_3_cout, n4_1_cascading_mux_1_y, n4_1_cascading_mux_2_y,
       n4_1_cascading_mux_3_y, n4_1_cascading_mux_4_y, not_1_out, not_2_out, not_3_out, not_4_out;

  not not_1 (not_1_out, B0);
  not not_2 (not_2_out, B1);
  not not_3 (not_3_out, B2);
  not not_4 (not_4_out, B3);
  _4_1_Cascading_MUX u_4_1_cascading_mux_1 (
    .i0(B0), .i1(not_1_out), .i2(1'b0), .i3(1'b1), .Y(n4_1_cascading_mux_1_y), .S0(S0), .S1(S1));
  _4_1_Cascading_MUX u_4_1_cascading_mux_2 (
    .i0(B1), .i1(not_2_out), .i2(1'b0), .i3(1'b1), .Y(n4_1_cascading_mux_2_y), .S0(S0), .S1(S1));
  _4_1_Cascading_MUX u_4_1_cascading_mux_3 (
    .i0(B2), .i1(not_3_out), .i2(1'b0), .i3(1'b1), .Y(n4_1_cascading_mux_3_y), .S0(S0), .S1(S1));
  _4_1_Cascading_MUX u_4_1_cascading_mux_4 (
    .i0(B3), .i1(not_4_out), .i2(1'b0), .i3(1'b1), .Y(n4_1_cascading_mux_4_y), .S0(S0), .S1(S1));
  Adder #(.width(1)) adder_1 (.a(A0), .b(n4_1_cascading_mux_1_y), .out(R0), .cin(Cin), .cout(adder_1_cout));
  Adder #(.width(1)) adder_2 (.a(A1), .b(n4_1_cascading_mux_2_y), .out(R1), .cin(adder_1_cout), .cout(adder_2_cout));
  Adder #(.width(1)) adder_3 (.a(A2), .b(n4_1_cascading_mux_3_y), .out(R2), .cin(adder_2_cout), .cout(adder_3_cout));
  Adder #(.width(1)) adder_4 (.a(A3), .b(n4_1_cascading_mux_4_y), .out(R3), .cin(adder_3_cout), .cout(C4));

  // Notes on the sheet:
  //   Control Signals
  //   Data Signals
endmodule
