// Logisim project NAND.circ as structural Verilog: 1 circuit, main circuit main
module main (
  input  A,
  input  B,
  input  C,
  input  D,
  input  A_2,
  input  B_2,
  input  C_2
);

  wire nand_1_out, nand_2_out, nand_3_out, nand_4_out, nand_5_out, nand_6_out, nand_7_out, nand_8_out;

  nand nand_1 (nand_1_out, A, B);
  nand nand_2 (nand_2_out, C, D);
  nand nand_3 (nand_3_out, A_2, B_2);
  nand nand_4 (nand_4_out, nand_1_out, nand_1_out);
  nand nand_5 (nand_5_out, nand_2_out, nand_2_out);
  nand nand_6 (nand_6_out, nand_3_out, nand_3_out);
  nand nand_7 (nand_7_out, nand_6_out, C_2);
  LED led_1 (.in(nand_8_out));
  nand nand_8 (nand_8_out, nand_4_out, nand_5_out);
  LED led_2 (.in(nand_7_out));

  // Notes on the sheet:
  //   (AB)'
  //   (AB)'
  //   (CD)'
  //   4 INPUT NAND USING 2 INPUT NAND
  //   3 INPUT NAND USING 2 INPUT NAND
  //   AB
  //   CD
  //   AB
  //   (ABCD)'
  //   (ABC)'
endmodule
