// Logisim project Arkopravo Saha 64 bit HCLA.circ as structural Verilog: 9 circuits, main circuit 1-bit GP generator and full adder
module _1_bit_GP_generator_and_full_adder (
  input  A_i,
  input  B_i,
  input  C_in,
  output C_out,
  output Propagator,
  output Generator,
  output S_i
);

  wire and_1_out;

  or or_1 (C_out, and_1_out, Generator);
  and and_1 (and_1_out, C_in, Propagator);
  and and_2 (Generator, A_i, B_i);
  xor xor_1 (Propagator, A_i, B_i);
  xor xor_2 (S_i, Propagator, C_in);
endmodule

module _4_bit_ripple_circuit (
  input  A3,
  input  A2,
  input  A1,
  input  A0,
  input  B3,
  input  B2,
  input  B1,
  input  B0,
  input  External_C_in,
  output S4,
  output S3,
  output S2,
  output S1,
  output S0
);

  wire n1_bit_gp_generator_and_full_adder_2_c_out, n1_bit_gp_generator_and_full_adder_3_c_out,
       n1_bit_gp_generator_and_full_adder_4_c_out;

  _1_bit_GP_generator_and_full_adder u_1_bit_gp_generator_and_full_adder_1 (
    .C_out(S4), .A_i(A3), .B_i(B3), .S_i(S3), .C_in(n1_bit_gp_generator_and_full_adder_2_c_out));  // open: Generator, Propagator
  _1_bit_GP_generator_and_full_adder u_1_bit_gp_generator_and_full_adder_2 (
    .C_out(n1_bit_gp_generator_and_full_adder_2_c_out), .A_i(A2), .B_i(B2), .S_i(S2),
    .C_in(n1_bit_gp_generator_and_full_adder_3_c_out));  // open: Generator, Propagator
  _1_bit_GP_generator_and_full_adder u_1_bit_gp_generator_and_full_adder_3 (
    .C_out(n1_bit_gp_generator_and_full_adder_3_c_out), .A_i(A1), .B_i(B1), .S_i(S1),
    .C_in(n1_bit_gp_generator_and_full_adder_4_c_out));  // open: Generator, Propagator
  _1_bit_GP_generator_and_full_adder u_1_bit_gp_generator_and_full_adder_4 (
    .C_out(n1_bit_gp_generator_and_full_adder_4_c_out), .A_i(A0), .B_i(B0), .S_i(S0), .C_in(External_C_in));  // open: Generator, Propagator
endmodule

module _16_bit_ripple_circuit__view (
  input  in_1,
  input  in_2,
  input  in_3,
  input  in_4,
  input  in_5,
  input  in_6,
  input  in_7,
  input  in_8,
  input  in_9,
  input  in_10,
  input  in_11,
  input  in_12,
  input  in_13,
  input  in_14,
  input  in_15,
  input  in_16,
  input  in_17,
  input  in_18,
  input  in_19,
  input  in_20,
  input  in_21,
  input  in_22,
  input  in_23,
  input  in_24,
  input  in_25,
  input  in_26,
  input  in_27,
  input  in_28,
  input  in_29,
  input  in_30,
  input  in_31,
  input  in_32,
  input  External_Carry_in,
  output out_34,
  output out_35,
  output out_36,
  output out_37,
  output out_38,
  output out_39,
  output out_40,
  output out_41,
  output out_42,
  output out_43,
  output out_44,
  output out_45,
  output out_46,
  output out_47,
  output out_48,
  output out_49,
  output out_50
);

  wire n4_bit_ripple_circuit_2_s4, n4_bit_ripple_circuit_3_s4, n4_bit_ripple_circuit_4_s4;

  _4_bit_ripple_circuit u_4_bit_ripple_circuit_1 (
    .A3(in_1), .A2(in_2), .A1(in_3), .A0(in_4), .B3(in_17), .B2(in_18), .B1(in_19), .B0(in_20),
    .External_C_in(n4_bit_ripple_circuit_2_s4), .S4(out_34), .S3(out_35), .S2(out_36), .S1(out_37),
    .S0(out_38));
  _4_bit_ripple_circuit u_4_bit_ripple_circuit_2 (
    .A3(in_5), .A2(in_6), .A1(in_7), .A0(in_8), .B3(in_21), .B2(in_22), .B1(in_23), .B0(in_24),
    .External_C_in(n4_bit_ripple_circuit_3_s4), .S4(n4_bit_ripple_circuit_2_s4), .S3(out_39), .S2(out_40),
    .S1(out_41), .S0(out_42));
  _4_bit_ripple_circuit u_4_bit_ripple_circuit_3 (
    .A3(in_9), .A2(in_10), .A1(in_11), .A0(in_12), .B3(in_25), .B2(in_26), .B1(in_27), .B0(in_28),
    .External_C_in(n4_bit_ripple_circuit_4_s4), .S4(n4_bit_ripple_circuit_3_s4), .S3(out_43), .S2(out_44),
    .S1(out_45), .S0(out_46));
  _4_bit_ripple_circuit u_4_bit_ripple_circuit_4 (
    .A3(in_13), .A2(in_14), .A1(in_15), .A0(in_16), .B3(in_29), .B2(in_30), .B1(in_31), .B0(in_32),
    .External_C_in(External_Carry_in), .S4(n4_bit_ripple_circuit_4_s4), .S3(out_47), .S2(out_48),
    .S1(out_49), .S0(out_50));

  // Notes on the sheet:
  //   First Number A
  //   Second Number B
  //   Sum = 
endmodule

module _4_bit_GP_Generator (
  input  [3:0] A_0_3,
  input  [3:0] B_0_3,
  output [3:0] P_0_3,
  output [3:0] G_0_3,
  output Group_P,
  output Group_G
);

  wire and_1_out, and_2_out, and_3_out;

  and and_1 (and_1_out, G_0_3[2], P_0_3[3]);
  and and_2 (and_2_out, G_0_3[1], P_0_3[3], P_0_3[2]);
  or or_1 (Group_G, G_0_3[3], and_1_out, and_2_out, and_3_out);
  and and_3 (and_3_out, G_0_3[0], P_0_3[3], P_0_3[2], P_0_3[1]);
  _1_bit_GP_generator_and_full_adder u_1_bit_gp_generator_and_full_adder_1 (
    .A_i(A_0_3[3]), .B_i(B_0_3[3]), .Generator(G_0_3[3]), .Propagator(P_0_3[3]));  // open: C_out, S_i, C_in
  _1_bit_GP_generator_and_full_adder u_1_bit_gp_generator_and_full_adder_2 (
    .A_i(A_0_3[2]), .B_i(B_0_3[2]), .Generator(G_0_3[2]), .Propagator(P_0_3[2]));  // open: C_out, S_i, C_in
  _1_bit_GP_generator_and_full_adder u_1_bit_gp_generator_and_full_adder_3 (
    .A_i(A_0_3[1]), .B_i(B_0_3[1]), .Generator(G_0_3[1]), .Propagator(P_0_3[1]));  // open: C_out, S_i, C_in
  and and_4 (Group_P, P_0_3[3], P_0_3[2], P_0_3[1], P_0_3[0]);
  _1_bit_GP_generator_and_full_adder u_1_bit_gp_generator_and_full_adder_4 (
    .A_i(A_0_3[0]), .B_i(B_0_3[0]), .Generator(G_0_3[0]), .Propagator(P_0_3[0]));  // open: C_out, S_i, C_in
endmodule

module _1_bit_Sum_and_Carry_Generator (
  input  G,
  input  P,
  input  C_in,
  output C_out,
  output S
);

  wire and_1_out;

  or or_1 (C_out, G, and_1_out);
  and and_1 (and_1_out, P, C_in);
  xor xor_1 (S, P, C_in);
endmodule

module _4_bit_Sum_and_Carry_Generator (
  input  [3:0] P_0_3,
  input  [3:0] G_0_3,
  input  C_in_0,
  output [3:0] C_out_0_3,
  output [3:0] S_0_3
);

  _1_bit_Sum_and_Carry_Generator u_1_bit_sum_and_carry_generator_1 (
    .G(G_0_3[3]), .P(P_0_3[3]), .C_in(C_out_0_3[2]), .C_out(C_out_0_3[3]), .S(S_0_3[3]));
  _1_bit_Sum_and_Carry_Generator u_1_bit_sum_and_carry_generator_2 (
    .G(G_0_3[2]), .P(P_0_3[2]), .C_in(C_out_0_3[1]), .C_out(C_out_0_3[2]), .S(S_0_3[2]));
  _1_bit_Sum_and_Carry_Generator u_1_bit_sum_and_carry_generator_3 (
    .G(G_0_3[1]), .P(P_0_3[1]), .C_in(C_out_0_3[0]), .C_out(C_out_0_3[1]), .S(S_0_3[1]));
  _1_bit_Sum_and_Carry_Generator u_1_bit_sum_and_carry_generator_4 (
    .G(G_0_3[0]), .P(P_0_3[0]), .C_in(C_in_0), .C_out(C_out_0_3[0]), .S(S_0_3[0]));
endmodule

module Heirarchical_16_Bit_Look_Ahead_Circuit__view (
  input  [3:0] in_1,
  input  [3:0] in_2,
  input  [3:0] in_3,
  input  [3:0] in_4,
  input  [3:0] in_5,
  input  [3:0] in_6,
  input  [3:0] in_7,
  input  [3:0] in_8,
  input  External_Carry_in,
  output out_10,
  output [3:0] out_11,
  output [3:0] out_12,
  output [3:0] out_13,
  output [3:0] out_14
);

  wire [2:0] n4_bit_sum_and_carry_generator_2_c_out_0_3;
  wire [3:0] n4_bit_gp_generator_1_g_0_3, n4_bit_gp_generator_1_p_0_3, n4_bit_gp_generator_2_g_0_3,
       n4_bit_gp_generator_2_p_0_3, n4_bit_gp_generator_3_g_0_3, n4_bit_gp_generator_3_p_0_3,
       n4_bit_gp_generator_4_g_0_3, n4_bit_gp_generator_4_group_g, n4_bit_gp_generator_4_group_p,
       n4_bit_gp_generator_4_p_0_3;

  _4_bit_GP_Generator u_4_bit_gp_generator_1 (
    .A_0_3(in_1), .B_0_3(in_5), .Group_G(n4_bit_gp_generator_4_group_g[3]),
    .Group_P(n4_bit_gp_generator_4_group_p[3]), .P_0_3(n4_bit_gp_generator_1_p_0_3),
    .G_0_3(n4_bit_gp_generator_1_g_0_3));
  _4_bit_Sum_and_Carry_Generator u_4_bit_sum_and_carry_generator_1 (
    .P_0_3(n4_bit_gp_generator_1_p_0_3), .G_0_3(n4_bit_gp_generator_1_g_0_3),
    .C_in_0(n4_bit_sum_and_carry_generator_2_c_out_0_3[2]), .S_0_3(out_11));  // open: C_out_0_3
  _4_bit_GP_Generator u_4_bit_gp_generator_2 (
    .A_0_3(in_2), .B_0_3(in_6), .Group_G(n4_bit_gp_generator_4_group_g[2]),
    .Group_P(n4_bit_gp_generator_4_group_p[2]), .P_0_3(n4_bit_gp_generator_2_p_0_3),
    .G_0_3(n4_bit_gp_generator_2_g_0_3));
  _4_bit_Sum_and_Carry_Generator u_4_bit_sum_and_carry_generator_2 (
    .P_0_3(n4_bit_gp_generator_4_group_p), .G_0_3(n4_bit_gp_generator_4_group_g), .C_in_0(External_Carry_in),
    .C_out_0_3({out_10, n4_bit_sum_and_carry_generator_2_c_out_0_3}));  // open: S_0_3
  _4_bit_Sum_and_Carry_Generator u_4_bit_sum_and_carry_generator_3 (
    .P_0_3(n4_bit_gp_generator_2_p_0_3), .G_0_3(n4_bit_gp_generator_2_g_0_3),
    .C_in_0(n4_bit_sum_and_carry_generator_2_c_out_0_3[1]), .S_0_3(out_12));  // open: C_out_0_3
  _4_bit_GP_Generator u_4_bit_gp_generator_3 (
    .A_0_3(in_3), .B_0_3(in_7), .Group_G(n4_bit_gp_generator_4_group_g[1]),
    .Group_P(n4_bit_gp_generator_4_group_p[1]), .P_0_3(n4_bit_gp_generator_3_p_0_3),
    .G_0_3(n4_bit_gp_generator_3_g_0_3));
  _4_bit_Sum_and_Carry_Generator u_4_bit_sum_and_carry_generator_4 (
    .P_0_3(n4_bit_gp_generator_3_p_0_3), .G_0_3(n4_bit_gp_generator_3_g_0_3),
    .C_in_0(n4_bit_sum_and_carry_generator_2_c_out_0_3[0]), .S_0_3(out_13));  // open: C_out_0_3
  _4_bit_GP_Generator u_4_bit_gp_generator_4 (
    .A_0_3(in_4), .B_0_3(in_8), .Group_G(n4_bit_gp_generator_4_group_g[0]),
    .Group_P(n4_bit_gp_generator_4_group_p[0]), .P_0_3(n4_bit_gp_generator_4_p_0_3),
    .G_0_3(n4_bit_gp_generator_4_g_0_3));
  _4_bit_Sum_and_Carry_Generator u_4_bit_sum_and_carry_generator_5 (
    .P_0_3(n4_bit_gp_generator_4_p_0_3), .G_0_3(n4_bit_gp_generator_4_g_0_3), .C_in_0(External_Carry_in),
    .S_0_3(out_14));  // open: C_out_0_3

  // Notes on the sheet:
  //   First Number A
  //   Second Number B
  //   Sum = 
endmodule

module Hierarchy_16_bit_level (
  input  [15:0] A_0_15,
  input  [15:0] B_0_15,
  input  External_Carry_in,
  output [15:0] S_0_15,
  output Group_G,
  output Group_P
);

  wire and_1_out, and_2_out, and_3_out;
  wire [3:0] n4_bit_gp_generator_1_g_0_3, n4_bit_gp_generator_1_p_0_3, n4_bit_gp_generator_2_g_0_3,
       n4_bit_gp_generator_2_p_0_3, n4_bit_gp_generator_3_g_0_3, n4_bit_gp_generator_3_p_0_3,
       n4_bit_gp_generator_4_g_0_3, n4_bit_gp_generator_4_group_g, n4_bit_gp_generator_4_group_p,
       n4_bit_gp_generator_4_p_0_3, n4_bit_sum_and_carry_generator_3_c_out_0_3;

  and and_1 (and_1_out, n4_bit_gp_generator_4_group_g[2], n4_bit_gp_generator_4_group_p[3]);
  or or_1 (Group_G, n4_bit_gp_generator_4_group_g[3], and_1_out, and_2_out, and_3_out);
  and and_2 (and_2_out, n4_bit_gp_generator_4_group_g[1], n4_bit_gp_generator_4_group_p[3], n4_bit_gp_generator_4_group_p[2]);
  and and_3 (and_3_out, n4_bit_gp_generator_4_group_g[0], n4_bit_gp_generator_4_group_p[3], n4_bit_gp_generator_4_group_p[2], n4_bit_gp_generator_4_group_p[1]);
  and and_4 (Group_P, n4_bit_gp_generator_4_group_p[3], n4_bit_gp_generator_4_group_p[2], n4_bit_gp_generator_4_group_p[1], n4_bit_gp_generator_4_group_p[0]);
  _4_bit_GP_Generator u_4_bit_gp_generator_1 (
    .A_0_3(A_0_15[15:12]), .B_0_3(B_0_15[15:12]), .Group_G(n4_bit_gp_generator_4_group_g[3]),
    .Group_P(n4_bit_gp_generator_4_group_p[3]), .P_0_3(n4_bit_gp_generator_1_p_0_3),
    .G_0_3(n4_bit_gp_generator_1_g_0_3));
  _4_bit_Sum_and_Carry_Generator u_4_bit_sum_and_carry_generator_1 (
    .P_0_3(n4_bit_gp_generator_1_p_0_3), .G_0_3(n4_bit_gp_generator_1_g_0_3),
    .C_in_0(n4_bit_sum_and_carry_generator_3_c_out_0_3[2]), .S_0_3(S_0_15[15:12]));  // open: C_out_0_3
  _4_bit_GP_Generator u_4_bit_gp_generator_2 (
    .A_0_3(A_0_15[11:8]), .B_0_3(B_0_15[11:8]), .Group_G(n4_bit_gp_generator_4_group_g[2]),
    .Group_P(n4_bit_gp_generator_4_group_p[2]), .P_0_3(n4_bit_gp_generator_2_p_0_3),
    .G_0_3(n4_bit_gp_generator_2_g_0_3));
  _4_bit_Sum_and_Carry_Generator u_4_bit_sum_and_carry_generator_2 (
    .P_0_3(n4_bit_gp_generator_2_p_0_3), .G_0_3(n4_bit_gp_generator_2_g_0_3),
    .C_in_0(n4_bit_sum_and_carry_generator_3_c_out_0_3[1]), .S_0_3(S_0_15[11:8]));  // open: C_out_0_3
  _4_bit_Sum_and_Carry_Generator u_4_bit_sum_and_carry_generator_3 (
    .P_0_3(n4_bit_gp_generator_4_group_p), .G_0_3(n4_bit_gp_generator_4_group_g), .C_in_0(External_Carry_in),
    .C_out_0_3(n4_bit_sum_and_carry_generator_3_c_out_0_3));  // open: S_0_3
  _4_bit_GP_Generator u_4_bit_gp_generator_3 (
    .A_0_3(A_0_15[7:4]), .B_0_3(B_0_15[7:4]), .Group_G(n4_bit_gp_generator_4_group_g[1]),
    .Group_P(n4_bit_gp_generator_4_group_p[1]), .P_0_3(n4_bit_gp_generator_3_p_0_3),
    .G_0_3(n4_bit_gp_generator_3_g_0_3));
  _4_bit_Sum_and_Carry_Generator u_4_bit_sum_and_carry_generator_4 (
    .P_0_3(n4_bit_gp_generator_3_p_0_3), .G_0_3(n4_bit_gp_generator_3_g_0_3),
    .C_in_0(n4_bit_sum_and_carry_generator_3_c_out_0_3[0]), .S_0_3(S_0_15[7:4]));  // open: C_out_0_3
  _4_bit_GP_Generator u_4_bit_gp_generator_4 (
    .A_0_3(A_0_15[3:0]), .B_0_3(B_0_15[3:0]), .Group_G(n4_bit_gp_generator_4_group_g[0]),
    .Group_P(n4_bit_gp_generator_4_group_p[0]), .P_0_3(n4_bit_gp_generator_4_p_0_3),
    .G_0_3(n4_bit_gp_generator_4_g_0_3));
  _4_bit_Sum_and_Carry_Generator u_4_bit_sum_and_carry_generator_5 (
    .P_0_3(n4_bit_gp_generator_4_p_0_3), .G_0_3(n4_bit_gp_generator_4_g_0_3), .C_in_0(External_Carry_in),
    .S_0_3(S_0_15[3:0]));  // open: C_out_0_3
endmodule

module Hierarchical_64_bit_Look_Ahead_Circuit__view (
  input  [7:0] in_1,
  input  [7:0] in_2,
  input  [7:0] in_3,
  input  [7:0] in_4,
  input  [7:0] in_5,
  input  [7:0] in_6,
  input  [7:0] in_7,
  input  [7:0] in_8,
  input  [7:0] in_9,
  input  [7:0] in_10,
  input  [7:0] in_11,
  input  [7:0] in_12,
  input  [7:0] in_13,
  input  [7:0] in_14,
  input  [7:0] in_15,
  input  [7:0] in_16,
  input  External_Carry_in,
  output out_18,
  output [7:0] out_19,
  output [7:0] out_20,
  output [7:0] out_21,
  output [7:0] out_22,
  output [7:0] out_23,
  output [7:0] out_24,
  output [7:0] out_25,
  output [7:0] out_26
);

  wire [2:0] n4_bit_sum_and_carry_generator_1_c_out_0_3;
  wire [3:0] hierarchy_16_bit_level_4_group_g, hierarchy_16_bit_level_4_group_p;

  Hierarchy_16_bit_level hierarchy_16_bit_level_1 (
    .A_0_15({in_1, in_2}), .B_0_15({in_9, in_10}), .S_0_15({out_19, out_20}),
    .Group_G(hierarchy_16_bit_level_4_group_g[3]), .Group_P(hierarchy_16_bit_level_4_group_p[3]),
    .External_Carry_in(n4_bit_sum_and_carry_generator_1_c_out_0_3[2]));
  Hierarchy_16_bit_level hierarchy_16_bit_level_2 (
    .A_0_15({in_3, in_4}), .B_0_15({in_11, in_12}), .S_0_15({out_21, out_22}),
    .Group_G(hierarchy_16_bit_level_4_group_g[2]), .Group_P(hierarchy_16_bit_level_4_group_p[2]),
    .External_Carry_in(n4_bit_sum_and_carry_generator_1_c_out_0_3[1]));
  _4_bit_Sum_and_Carry_Generator u_4_bit_sum_and_carry_generator_1 (
    .P_0_3(hierarchy_16_bit_level_4_group_p), .G_0_3(hierarchy_16_bit_level_4_group_g),
    .C_in_0(External_Carry_in), .C_out_0_3({out_18, n4_bit_sum_and_carry_generator_1_c_out_0_3}));  // open: S_0_3
  Hierarchy_16_bit_level hierarchy_16_bit_level_3 (
    .A_0_15({in_5, in_6}), .B_0_15({in_13, in_14}), .S_0_15({out_23, out_24}),
    .Group_G(hierarchy_16_bit_level_4_group_g[1]), .Group_P(hierarchy_16_bit_level_4_group_p[1]),
    .External_Carry_in(n4_bit_sum_and_carry_generator_1_c_out_0_3[0]));
  Hierarchy_16_bit_level hierarchy_16_bit_level_4 (
    .A_0_15({in_7, in_8}), .B_0_15({in_15, in_16}), .S_0_15({out_25, out_26}),
    .Group_G(hierarchy_16_bit_level_4_group_g[0]), .Group_P(hierarchy_16_bit_level_4_group_p[0]),
    .External_Carry_in(External_Carry_in));

  // Notes on the sheet:
  //   First Number A
  //   Second Number B
  //   Sum = 
endmodule
