// Logisim project AssignmentCounter.circ as structural Verilog: 1 circuit, main circuit main
module main (
  input  [3:0] Set_Value,
  input  ENABLE
);

  wire A_qn, and_1_out, and_2_out, and_3_out, and_4_out, and_5_out, and_6_out, and_7_out, and_8_out,
       and_9_out, and_10_out, and_11_out, and_12_out, and_13_out, and_14_out, and_15_out, and_16_out,
       and_17_out, and_18_out, and_19_out, and_20_out, and_21_out, and_22_out, B_qn, C_qn, CLK_out, D_qn,
       not_1_out, not_2_out, not_3_out, not_4_out, or_1_out, or_2_out, or_3_out, or_4_out, or_5_out,
       or_6_out, or_7_out, or_8_out, or_9_out, or_10_out, xnor_1_out, xor_1_out;
  wire [3:0] D_q, multiplexer_1_out;

  and and_1 (and_1_out, A_qn, D_q[2]);
  or or_1 (or_1_out, and_1_out, D_qn);
  or or_2 (or_2_out, D_q[2], D_qn, D_q[1]);
  or or_3 (or_3_out, D_q[3], D_q[1]);
  xor xor_1 (xor_1_out, D_q[3], D_q[0]);
  and and_2 (and_2_out, D_q[2], D_q[1]);
  or or_4 (or_4_out, and_2_out, D_q[0]);
  or or_5 (or_5_out, D_q[3], B_qn);
  xnor xnor_1 (xnor_1_out, D_q[2], D_q[1]);
  and and_3 (and_3_out, B_qn, D_q[1]);
  or or_6 (or_6_out, and_3_out, D_q[0]);
  and and_4 (and_4_out, A_qn, D_q[2], D_q[1], D_q[0]);
  and and_5 (and_5_out, or_1_out, D_q[1]);
  and and_6 (and_6_out, or_2_out, D_q[3]);
  and and_7 (and_7_out, or_3_out, D_q[2]);
  and and_8 (and_8_out, xor_1_out, D_q[1]);
  and and_9 (and_9_out, or_4_out, A_qn);
  and and_10 (and_10_out, or_5_out, C_qn);
  and and_11 (and_11_out, D_q[3], B_qn, D_qn);
  and and_12 (and_12_out, xnor_1_out, D_q[0]);
  and and_13 (and_13_out, or_6_out, D_q[3]);
  and and_14 (and_14_out, A_qn, D_q[2], C_qn, D_qn);
  Multiplexer #(.width(4)) multiplexer_1 (
    .in0(D_q), .in1(4'b0010), .out(multiplexer_1_out), .sel(and_4_out));  // open: en
  or or_7 (or_7_out, and_5_out, and_6_out);
  or or_8 (or_8_out, and_7_out, and_8_out);
  or or_9 (or_9_out, and_9_out, and_10_out, and_11_out);
  or or_10 (or_10_out, and_12_out, and_13_out, and_14_out);
  Hex_Digit_Display hex_digit_display_1 (.value(multiplexer_1_out));  // open: dp
  Clock CLK (.out(CLK_out));
  T_Flip_Flop A (
    .clk(CLK_out), .T(or_7_out), .Q(D_q[3]), .Qn(A_qn), .preset(and_16_out), .reset(and_15_out));  // open: en
  T_Flip_Flop B (
    .clk(CLK_out), .T(or_8_out), .Q(D_q[2]), .Qn(B_qn), .preset(and_18_out), .reset(and_17_out));  // open: en
  T_Flip_Flop C (
    .clk(CLK_out), .T(or_9_out), .Q(D_q[1]), .Qn(C_qn), .preset(and_20_out), .reset(and_19_out));  // open: en
  T_Flip_Flop D (
    .clk(CLK_out), .T(or_10_out), .Q(D_q[0]), .Qn(D_qn), .preset(and_22_out), .reset(and_21_out));  // open: en
  and and_15 (and_15_out, not_1_out, ENABLE);
  and and_16 (and_16_out, ENABLE, Set_Value[3]);
  and and_17 (and_17_out, not_2_out, ENABLE);
  and and_18 (and_18_out, ENABLE, Set_Value[2]);
  and and_19 (and_19_out, not_3_out, ENABLE);
  and and_20 (and_20_out, ENABLE, Set_Value[1]);
  and and_21 (and_21_out, not_4_out, ENABLE);
  and and_22 (and_22_out, ENABLE, Set_Value[0]);
  not not_1 (not_1_out, Set_Value[3]);
  not not_2 (not_2_out, Set_Value[2]);
  not not_3 (not_3_out, Set_Value[1]);
  not not_4 (not_4_out, Set_Value[0]);

  // Notes on the sheet:
  //   QD' QD QC' QC QB' QB QA' QA
endmodule
