// Logisim project Hex Display.circ as structural Verilog: 1 circuit, main circuit main
module main (
  input  ENABLE,
  input  [3:0] S3_0
);

  wire [7:0] multiplexer_1_out;

  Multiplexer #(.select(4), .width(8)) multiplexer_1 (
    .in0(8'hfc), .in1(8'h60), .in2(8'hda), .in3(8'hf2), .in4(8'h66), .in5(8'hb6), .in6(8'hbe), .in7(8'he0),
    .in8(8'hfe), .in9(8'hf6), .in10(8'hee), .in11(8'h3e), .in12(8'h9c), .in13(8'h7a), .in14(8'h9e),
    .in15(8'h8e), .out(multiplexer_1_out), .sel(S3_0), .en(ENABLE));
  _7_Segment_Display u_7_segment_display_1 (
    .g(multiplexer_1_out[1]), .f(multiplexer_1_out[2]), .a(multiplexer_1_out[7]), .b(multiplexer_1_out[6]),
    .e(multiplexer_1_out[3]), .d(multiplexer_1_out[4]), .c(multiplexer_1_out[5]), .dp(multiplexer_1_out[0]));
endmodule
