// Logisim project Rahul and Souvic 64 bit HCLA.circ as structural Verilog: 5 circuits, main circuit 4 Bit GP Generator
// GPG
module _4_Bit_GP_Generator (
  input  [3:0] A0_A3,
  input  [3:0] B0_B3,
  output [3:0] P0_P3,
  output [3:0] G0_G3
);

  xor xor_1 (P0_P3[0], B0_B3[0], A0_A3[0]);
  and and_1 (G0_G3[0], A0_A3[0], B0_B3[0]);
  xor xor_2 (P0_P3[1], B0_B3[1], A0_A3[1]);
  and and_2 (G0_G3[1], A0_A3[1], B0_B3[1]);
  xor xor_3 (P0_P3[2], B0_B3[2], A0_A3[2]);
  and and_3 (G0_G3[2], A0_A3[2], B0_B3[2]);
  xor xor_4 (P0_P3[3], B0_B3[3], A0_A3[3]);
  and and_4 (G0_G3[3], A0_A3[3], B0_B3[3]);

  // Notes on the sheet:
  //   P0
  //   G0
  //   P1
  //   G1
  //   P2
  //   G2
  //   P3
  //   G3
endmodule

// LA
module _4_BitLook_ahead (
  input  C0,
  input  [3:0] P0_P3,
  input  [3:0] G0_G3,
  output C1,
  output C2,
  output C3,
  output GG,
  output GP
);

  wire and_1_out, and_2_out, and_3_out, and_4_out, and_5_out, and_6_out, and_7_out, and_8_out, and_9_out;

  and and_1 (and_1_out, C0, P0_P3[0]);
  and and_2 (and_2_out, G0_G3[0], P0_P3[1]);
  and and_3 (and_3_out, C0, P0_P3[0], P0_P3[1]);
  and and_4 (and_4_out, P0_P3[2], G0_G3[1]);
  and and_5 (and_5_out, G0_G3[0], P0_P3[1], P0_P3[2]);
  and and_6 (and_6_out, P0_P3[2], P0_P3[1], P0_P3[0], C0);
  and and_7 (and_7_out, G0_G3[2], P0_P3[3]);
  and and_8 (and_8_out, G0_G3[1], P0_P3[2], P0_P3[3]);
  and and_9 (and_9_out, G0_G3[0], P0_P3[1], P0_P3[2], P0_P3[3]);
  and and_10 (GP, P0_P3[0], P0_P3[1], P0_P3[2], P0_P3[3]);
  or or_1 (C1, and_1_out, G0_G3[0]);
  or or_2 (C2, and_2_out, and_3_out, G0_G3[1]);
  or or_3 (C3, and_4_out, and_5_out, and_6_out, G0_G3[2]);
  or or_4 (GG, and_7_out, and_8_out, and_9_out, G0_G3[3]);
endmodule

module _4_Bit_Adder (
  input  C0,
  input  [3:0] A0_A3,
  input  [3:0] B0_B3,
  output [3:0] S0_S3,
  output GG,
  output GP
);

  wire n4_bitlook_ahead_1_c1, n4_bitlook_ahead_1_c2, n4_bitlook_ahead_1_c3;
  wire [3:0] n4_bit_gp_generator_1_g0_g3, n4_bit_gp_generator_1_p0_p3;

  _4_Bit_GP_Generator u_4_bit_gp_generator_1 (
    .A0_A3(A0_A3), .B0_B3(B0_B3), .P0_P3(n4_bit_gp_generator_1_p0_p3), .G0_G3(n4_bit_gp_generator_1_g0_g3));
  _4_BitLook_ahead u_4_bitlook_ahead_1 (
    .C0(C0), .P0_P3(n4_bit_gp_generator_1_p0_p3), .G0_G3(n4_bit_gp_generator_1_g0_g3),
    .C1(n4_bitlook_ahead_1_c1), .C2(n4_bitlook_ahead_1_c2), .C3(n4_bitlook_ahead_1_c3), .GG(GG), .GP(GP));
  xor xor_1 (S0_S3[0], C0, n4_bit_gp_generator_1_p0_p3[0]);
  xor xor_2 (S0_S3[1], n4_bitlook_ahead_1_c1, n4_bit_gp_generator_1_p0_p3[1]);
  xor xor_3 (S0_S3[2], n4_bitlook_ahead_1_c2, n4_bit_gp_generator_1_p0_p3[2]);
  xor xor_4 (S0_S3[3], n4_bitlook_ahead_1_c3, n4_bit_gp_generator_1_p0_p3[3]);
endmodule

module _16_Bit_Adder (
  input  [15:0] B0_B15,
  input  [15:0] A0_A15,
  input  C0,
  output [15:0] _16_Bit_Sum,
  output GP,
  output GG
);

  wire n4_bitlook_ahead_1_c1, n4_bitlook_ahead_1_c2, n4_bitlook_ahead_1_c3;
  wire [3:0] n4_bit_adder_4_gg, n4_bit_adder_4_gp;

  _4_Bit_Adder u_4_bit_adder_1 (
    .C0(n4_bitlook_ahead_1_c3), .A0_A3(A0_A15[15:12]), .B0_B3(B0_B15[15:12]), .S0_S3(_16_Bit_Sum[15:12]),
    .GG(n4_bit_adder_4_gg[3]), .GP(n4_bit_adder_4_gp[3]));
  _4_Bit_Adder u_4_bit_adder_2 (
    .C0(n4_bitlook_ahead_1_c2), .A0_A3(A0_A15[11:8]), .B0_B3(B0_B15[11:8]), .S0_S3(_16_Bit_Sum[11:8]),
    .GG(n4_bit_adder_4_gg[2]), .GP(n4_bit_adder_4_gp[2]));
  _4_BitLook_ahead u_4_bitlook_ahead_1 (
    .C0(C0), .P0_P3(n4_bit_adder_4_gp), .G0_G3(n4_bit_adder_4_gg), .C1(n4_bitlook_ahead_1_c1),
    .C2(n4_bitlook_ahead_1_c2), .C3(n4_bitlook_ahead_1_c3), .GG(GG), .GP(GP));
  _4_Bit_Adder u_4_bit_adder_3 (
    .C0(n4_bitlook_ahead_1_c1), .A0_A3(A0_A15[7:4]), .B0_B3(B0_B15[7:4]), .S0_S3(_16_Bit_Sum[7:4]),
    .GG(n4_bit_adder_4_gg[1]), .GP(n4_bit_adder_4_gp[1]));
  _4_Bit_Adder u_4_bit_adder_4 (
    .C0(C0), .A0_A3(A0_A15[3:0]), .B0_B3(B0_B15[3:0]), .S0_S3(_16_Bit_Sum[3:0]), .GG(n4_bit_adder_4_gg[0]),
    .GP(n4_bit_adder_4_gp[0]));
endmodule

module _64_Bit__AAdder (
  input  [31:0] B32_B63,
  input  [31:0] A32_A63,
  input  [31:0] B0_B31,
  input  [31:0] A0_A31,
  input  in_5,
  output [31:0] S32_S63,
  output [31:0] S0_S31,
  output C64
);

  wire and_1_out, n4_bitlook_ahead_1_c1, n4_bitlook_ahead_1_c2, n4_bitlook_ahead_1_c3, n4_bitlook_ahead_1_gg,
       n4_bitlook_ahead_1_gp;
  wire [3:0] n16_bit_adder_4_gg, n16_bit_adder_4_gp;

  _16_Bit_Adder u_16_bit_adder_1 (
    .C0(n4_bitlook_ahead_1_c3), .B0_B15(B32_B63[31:16]), .A0_A15(A32_A63[31:16]), .GP(n16_bit_adder_4_gp[3]),
    .GG(n16_bit_adder_4_gg[3]), ._16_Bit_Sum(S32_S63[31:16]));
  _16_Bit_Adder u_16_bit_adder_2 (
    .C0(n4_bitlook_ahead_1_c2), .B0_B15(B32_B63[15:0]), .A0_A15(A32_A63[15:0]), .GP(n16_bit_adder_4_gp[2]),
    .GG(n16_bit_adder_4_gg[2]), ._16_Bit_Sum(S32_S63[15:0]));
  and and_1 (and_1_out, n4_bitlook_ahead_1_gp, in_5);
  or or_1 (C64, n4_bitlook_ahead_1_gg, and_1_out);
  _4_BitLook_ahead u_4_bitlook_ahead_1 (
    .C0(in_5), .P0_P3(n16_bit_adder_4_gp), .G0_G3(n16_bit_adder_4_gg), .C1(n4_bitlook_ahead_1_c1),
    .C2(n4_bitlook_ahead_1_c2), .C3(n4_bitlook_ahead_1_c3), .GG(n4_bitlook_ahead_1_gg),
    .GP(n4_bitlook_ahead_1_gp));
  _16_Bit_Adder u_16_bit_adder_3 (
    .C0(n4_bitlook_ahead_1_c1), .B0_B15(B0_B31[31:16]), .A0_A15(A0_A31[31:16]), .GP(n16_bit_adder_4_gp[1]),
    .GG(n16_bit_adder_4_gg[1]), ._16_Bit_Sum(S0_S31[31:16]));
  _16_Bit_Adder u_16_bit_adder_4 (
    .C0(in_5), .B0_B15(B0_B31[15:0]), .A0_A15(A0_A31[15:0]), .GP(n16_bit_adder_4_gp[0]),
    .GG(n16_bit_adder_4_gg[0]), ._16_Bit_Sum(S0_S31[15:0]));
endmodule
