// Logisim project StopWatch.circ as structural Verilog: 4 circuits, main circuit 0-9 Counter
module _0_9_Counter (
  input  CLK,
  output _10,
  output [3:0] Count
);

  wire _0_qn, _2_qn, and_2_out, and_3_out;

  T_Flip_Flop _0 (.clk(CLK), .T(1'b1), .Q(Count[0]), .Qn(_0_qn), .reset(_10));  // open: preset, en
  and and_1 (_10, _0_qn, Count[1], _2_qn, Count[3]);
  T_Flip_Flop _1 (.clk(CLK), .T(Count[0]), .Q(Count[1]), .reset(_10));  // open: Qn, preset, en
  and and_2 (and_2_out, Count[0], Count[1]);
  T_Flip_Flop _2 (.clk(CLK), .T(and_2_out), .Q(Count[2]), .Qn(_2_qn), .reset(_10));  // open: preset, en
  and and_3 (and_3_out, and_2_out, Count[2]);
  T_Flip_Flop _3 (.clk(CLK), .T(and_3_out), .Q(Count[3]), .reset(_10));  // open: Qn, preset, en
endmodule

module _0_5_Counter (
  input  in_1,
  output _5,
  output [3:0] out_3
);

  wire _3_qn, and_2_out, and_3_out, and_4_out, and_5_out, not_1_out, not_2_out, or_1_out;

  T_Flip_Flop _0 (.clk(in_1), .T(1'b1), .Q(out_3[0]), .reset(_5));  // open: Qn, preset, en
  and and_1 (_5, not_1_out, not_2_out, out_3[2], out_3[1]);
  T_Flip_Flop _1 (.clk(in_1), .T(and_2_out), .Q(out_3[1]), .reset(_5));  // open: Qn, preset, en
  and and_2 (and_2_out, _3_qn, out_3[0]);
  not not_1 (not_1_out, out_3[3]);
  not not_2 (not_2_out, out_3[0]);
  and and_3 (and_3_out, out_3[3], out_3[0]);
  and and_4 (and_4_out, out_3[0], out_3[1]);
  T_Flip_Flop _2 (.clk(in_1), .T(and_4_out), .Q(out_3[2]), .reset(_5));  // open: Qn, preset, en
  and and_5 (and_5_out, and_4_out, out_3[2]);
  or or_1 (or_1_out, and_3_out, and_5_out);
  T_Flip_Flop _3 (.clk(in_1), .T(or_1_out), .Q(out_3[3]), .Qn(_3_qn), .reset(_5));  // open: preset, en
endmodule

// HH
module Hour_Counter (
  input  in_1,
  output [3:0] _2,
  output [3:0] _4
);

  wire _0_2_qn, _0_qn, _1_2_qn, _2_qn, and_1_out, and_2_out, and_3_out, and_4_out, not_1_out, not_2_out,
       not_3_out, or_1_out, or_2_out;

  or or_1 (or_1_out, and_4_out, and_1_out);
  T_Flip_Flop _0 (.clk(in_1), .T(1'b1), .Q(_4[0]), .Qn(_0_qn), .reset(or_1_out));  // open: preset, en
  and and_1 (and_1_out, _0_qn, _4[1], _2_qn, _4[3]);
  T_Flip_Flop _1 (.clk(in_1), .T(_4[0]), .Q(_4[1]), .reset(or_1_out));  // open: Qn, preset, en
  and and_2 (and_2_out, _4[0], _4[1]);
  T_Flip_Flop u__2 (.clk(in_1), .T(and_2_out), .Q(_4[2]), .Qn(_2_qn), .reset(or_1_out));  // open: preset, en
  and and_3 (and_3_out, and_2_out, _4[2]);
  T_Flip_Flop _3 (.clk(in_1), .T(and_3_out), .Q(_4[3]), .reset(or_1_out));  // open: Qn, preset, en
  not not_1 (not_1_out, _4[3]);
  not not_2 (not_2_out, _4[1]);
  not not_3 (not_3_out, _4[0]);
  T_Flip_Flop _0_2 (.clk(and_1_out), .T(_1_2_qn), .Q(_2[0]), .Qn(_0_2_qn), .reset(and_4_out));  // open: preset, en
  and and_4 (and_4_out, _4[2], not_3_out, not_2_out, not_1_out, _0_2_qn, _2[1]);
  or or_2 (or_2_out, _2[0], _2[1]);
  T_Flip_Flop _1_2 (.clk(and_1_out), .T(or_2_out), .Q(_2[1]), .Qn(_1_2_qn), .reset(and_4_out));  // open: preset, en

  assign _2[3:2] = 2'b00;
endmodule

module Stop_Watch (
);

  wire clock_1_out, n0_5_counter_1__5, n0_5_counter_2__5, n0_9_counter_1__10, n0_9_counter_2__10;
  wire [3:0] hour_counter_1__2, hour_counter_1__4, n0_5_counter_1_out_3, n0_5_counter_2_out_3,
       n0_9_counter_1_count, n0_9_counter_2_count;

  Hour_Counter hour_counter_1 (.in_1(n0_5_counter_1__5), ._2(hour_counter_1__2), ._4(hour_counter_1__4));
  _0_5_Counter u_0_5_counter_1 (.in_1(n0_9_counter_1__10), .out_3(n0_5_counter_1_out_3), ._5(n0_5_counter_1__5));
  Hex_Digit_Display hex_digit_display_1 (.value(hour_counter_1__4));  // open: dp
  Hex_Digit_Display hex_digit_display_2 (.value(hour_counter_1__2));  // open: dp
  Hex_Digit_Display hex_digit_display_3 (.value(n0_5_counter_1_out_3));  // open: dp
  Hex_Digit_Display hex_digit_display_4 (.value(n0_9_counter_1_count));  // open: dp
  Hex_Digit_Display hex_digit_display_5 (.value(n0_5_counter_2_out_3));  // open: dp
  _0_9_Counter u_0_9_counter_1 (.CLK(n0_5_counter_2__5), .Count(n0_9_counter_1_count), ._10(n0_9_counter_1__10));
  Hex_Digit_Display hex_digit_display_6 (.value(n0_9_counter_2_count));  // open: dp
  _0_5_Counter u_0_5_counter_2 (.in_1(n0_9_counter_2__10), .out_3(n0_5_counter_2_out_3), ._5(n0_5_counter_2__5));
  Clock clock_1 (.out(clock_1_out));
  _0_9_Counter u_0_9_counter_2 (.CLK(clock_1_out), .Count(n0_9_counter_2_count), ._10(n0_9_counter_2__10));

  // Notes on the sheet:
  //   HOUR
  //   MINUTES
  //   :
  //   :
  //   SECONDS
endmodule
