// Logisim project 8bit USR with Serial Communication.circ as structural Verilog: 2 circuits, main circuit 8bit USR
module _8bit_USR (
  input  [7:0] PDI_0_7,
  input  [1:0] S0_S1,
  input  SDI_Right,
  input  SDI_Left,
  input  CLK,
  output [7:0] PDO_0_7
);

  wire multiplexer_1_out, multiplexer_2_out, multiplexer_3_out, multiplexer_4_out, multiplexer_5_out,
       multiplexer_6_out, multiplexer_7_out, multiplexer_8_out;

  Multiplexer #(.select(2), .enable("false")) multiplexer_1 (
    .in0(PDO_0_7[7]), .in1(SDI_Left), .in2(PDO_0_7[6]), .in3(PDI_0_7[7]), .out(multiplexer_1_out), .sel(S0_S1));
  D_Flip_Flop d_ff_1 (.clk(CLK), .D(multiplexer_1_out), .Q(PDO_0_7[7]));  // open: Qn, preset, en, reset
  Multiplexer #(.select(2), .enable("false")) multiplexer_2 (
    .in0(PDO_0_7[6]), .in1(PDO_0_7[7]), .in2(PDO_0_7[5]), .in3(PDI_0_7[6]), .out(multiplexer_2_out),
    .sel(S0_S1));
  D_Flip_Flop d_ff_2 (.clk(CLK), .D(multiplexer_2_out), .Q(PDO_0_7[6]));  // open: Qn, preset, en, reset
  Multiplexer #(.select(2), .enable("false")) multiplexer_3 (
    .in0(PDO_0_7[5]), .in1(PDO_0_7[6]), .in2(PDO_0_7[4]), .in3(PDI_0_7[5]), .out(multiplexer_3_out),
    .sel(S0_S1));
  D_Flip_Flop d_ff_3 (.clk(CLK), .D(multiplexer_3_out), .Q(PDO_0_7[5]));  // open: Qn, preset, en, reset
  Multiplexer #(.select(2), .enable("false")) multiplexer_4 (
    .in0(PDO_0_7[4]), .in1(PDO_0_7[5]), .in2(PDO_0_7[3]), .in3(PDI_0_7[4]), .out(multiplexer_4_out),
    .sel(S0_S1));
  D_Flip_Flop d_ff_4 (.clk(CLK), .D(multiplexer_4_out), .Q(PDO_0_7[4]));  // open: Qn, preset, en, reset
  Multiplexer #(.select(2), .enable("false")) multiplexer_5 (
    .in0(PDO_0_7[3]), .in1(PDO_0_7[4]), .in2(PDO_0_7[2]), .in3(PDI_0_7[3]), .out(multiplexer_5_out),
    .sel(S0_S1));
  D_Flip_Flop d_ff_5 (.clk(CLK), .D(multiplexer_5_out), .Q(PDO_0_7[3]));  // open: Qn, preset, en, reset
  Multiplexer #(.select(2), .enable("false")) multiplexer_6 (
    .in0(PDO_0_7[2]), .in1(PDO_0_7[3]), .in2(PDO_0_7[1]), .in3(PDI_0_7[2]), .out(multiplexer_6_out),
    .sel(S0_S1));
  D_Flip_Flop d_ff_6 (.clk(CLK), .D(multiplexer_6_out), .Q(PDO_0_7[2]));  // open: Qn, preset, en, reset
  Multiplexer #(.select(2), .enable("false")) multiplexer_7 (
    .in0(PDO_0_7[1]), .in1(PDO_0_7[2]), .in2(PDO_0_7[0]), .in3(PDI_0_7[1]), .out(multiplexer_7_out),
    .sel(S0_S1));
  D_Flip_Flop d_ff_7 (.clk(CLK), .D(multiplexer_7_out), .Q(PDO_0_7[1]));  // open: Qn, preset, en, reset
  Multiplexer #(.select(2), .enable("false")) multiplexer_8 (
    .in0(PDO_0_7[0]), .in1(PDO_0_7[1]), .in2(SDI_Right), .in3(PDI_0_7[0]), .out(multiplexer_8_out),
    .sel(S0_S1));
  D_Flip_Flop d_ff_8 (.clk(CLK), .D(multiplexer_8_out), .Q(PDO_0_7[0]));  // open: Qn, preset, en, reset
endmodule

module _8bit_USR_Serial_Comm (
  input  [7:0] PDI1_0_7,
  input  [7:0] PDI2_0_7,
  input  [1:0] S0_S1,
  input  SDI1_Left,
  input  SDI2_Right,
  output [7:0] PDO1_0_7,
  output [7:0] PD02_0_7
);

  wire CLK_out;

  Clock CLK (.out(CLK_out));
  _8bit_USR u_8bit_usr_1 (
    .S0_S1(S0_S1), .SDI_Left(SDI1_Left), .SDI_Right(PD02_0_7[7]), .PDI_0_7(PDI1_0_7), .PDO_0_7(PDO1_0_7),
    .CLK(CLK_out));
  _8bit_USR u_8bit_usr_2 (
    .S0_S1(S0_S1), .SDI_Left(PDO1_0_7[0]), .SDI_Right(SDI2_Right), .PDI_0_7(PDI2_0_7), .PDO_0_7(PD02_0_7),
    .CLK(CLK_out));
endmodule
