// Logisim project Counter.circ as structural Verilog: 8 circuits, main circuit Ring Counter
module Ring_Counter (
  input  I_prime,
  output Q1,
  output Q2,
  output Q3,
  output Q4
);

  wire CLK_out;

  Clock CLK (.out(CLK_out));
  D_Flip_Flop D1 (.clk(CLK_out), .D(Q4), .Q(Q1), .preset(I_prime));  // open: Qn, en, reset
  D_Flip_Flop D2 (.clk(CLK_out), .D(Q1), .Q(Q2), .reset(I_prime));  // open: Qn, preset, en
  D_Flip_Flop D3 (.clk(CLK_out), .D(Q2), .Q(Q3), .reset(I_prime));  // open: Qn, preset, en
  D_Flip_Flop D4 (.clk(CLK_out), .D(Q3), .Q(Q4), .reset(I_prime));  // open: Qn, preset, en
endmodule

module Johnson_Counter (
  input  I_prime,
  output Q1,
  output Q2,
  output Q3,
  output Q4
);

  wire CLK_out, D4_qn;

  Clock CLK (.out(CLK_out));
  D_Flip_Flop D1 (.clk(CLK_out), .D(D4_qn), .Q(Q1), .preset(I_prime));  // open: Qn, en, reset
  D_Flip_Flop D2 (.clk(CLK_out), .D(Q1), .Q(Q2), .reset(I_prime));  // open: Qn, preset, en
  D_Flip_Flop D3 (.clk(CLK_out), .D(Q2), .Q(Q3), .reset(I_prime));  // open: Qn, preset, en
  D_Flip_Flop D4 (.clk(CLK_out), .D(Q3), .Q(Q4), .Qn(D4_qn), .reset(I_prime));  // open: preset, en
endmodule

module Asynchronous_Up_Counter (
  output Q1__L_S_B,
  output Q2,
  output Q3__M_S_B
);

  wire clock_1_out, T1_qn, T2_qn;

  Clock clock_1 (.out(clock_1_out));
  T_Flip_Flop T1 (.clk(clock_1_out), .T(1'b1), .Q(Q1__L_S_B), .Qn(T1_qn));  // open: preset, reset, en
  T_Flip_Flop T2 (.clk(T1_qn), .T(1'b1), .Q(Q2), .Qn(T2_qn));  // open: preset, reset, en
  T_Flip_Flop T3 (.clk(T2_qn), .T(1'b1), .Q(Q3__M_S_B));  // open: Qn, preset, reset, en
endmodule

module Asynchronous_Down_Counter (
  output Q1__L_S_B,
  output Q2,
  output Q3__M_S_B
);

  wire clock_1_out;

  Clock clock_1 (.out(clock_1_out));
  T_Flip_Flop T1 (.clk(clock_1_out), .T(1'b1), .Q(Q1__L_S_B));  // open: Qn, preset, reset, en
  T_Flip_Flop T2 (.clk(Q1__L_S_B), .T(1'b1), .Q(Q2));  // open: Qn, preset, reset, en
  T_Flip_Flop T3 (.clk(Q2), .T(1'b1), .Q(Q3__M_S_B));  // open: Qn, preset, reset, en
endmodule

module Bidirectional_Counter (
  input  DOWN_prime_UP,
  output Q1__L_S_B,
  output Q2,
  output Q3__M_S_B
);

  wire clock_1_out, multiplexer_1_out, multiplexer_2_out, T1_qn, T2_qn;

  Clock clock_1 (.out(clock_1_out));
  T_Flip_Flop T1 (.clk(clock_1_out), .T(1'b1), .Q(Q1__L_S_B), .Qn(T1_qn));  // open: preset, reset, en
  Multiplexer #(.enable("false")) multiplexer_1 (
    .in0(Q1__L_S_B), .in1(T1_qn), .out(multiplexer_1_out), .sel(DOWN_prime_UP));
  T_Flip_Flop T2 (.clk(multiplexer_1_out), .T(1'b1), .Q(Q2), .Qn(T2_qn));  // open: preset, reset, en
  Multiplexer #(.enable("false")) multiplexer_2 (.in0(Q2), .in1(T2_qn), .out(multiplexer_2_out), .sel(DOWN_prime_UP));
  T_Flip_Flop T3 (.clk(multiplexer_2_out), .T(1'b1), .Q(Q3__M_S_B));  // open: Qn, preset, reset, en
endmodule

module MOD_4_Counter (
  input  DOWN_prime_UP,
  output Q1__L_S_B,
  output Q2,
  output Q3__M_S_B
);

  wire clock_1_out, multiplexer_1_out, multiplexer_2_out, nand_1_out, not_1_out, not_2_out, T1_qn, T2_qn;

  Clock clock_1 (.out(clock_1_out));
  nand nand_1 (nand_1_out, not_1_out, not_2_out, Q3__M_S_B);
  T_Flip_Flop T1 (.clk(clock_1_out), .T(1'b1), .Q(Q1__L_S_B), .Qn(T1_qn), .reset(nand_1_out));  // open: preset, en
  not not_1 (not_1_out, Q1__L_S_B);
  Multiplexer #(.enable("false")) multiplexer_1 (
    .in0(Q1__L_S_B), .in1(T1_qn), .out(multiplexer_1_out), .sel(DOWN_prime_UP));
  not not_2 (not_2_out, Q2);
  T_Flip_Flop T2 (.clk(multiplexer_1_out), .T(1'b1), .Q(Q2), .Qn(T2_qn), .reset(nand_1_out));  // open: preset, en
  Multiplexer #(.enable("false")) multiplexer_2 (.in0(Q2), .in1(T2_qn), .out(multiplexer_2_out), .sel(DOWN_prime_UP));
  T_Flip_Flop T3 (.clk(multiplexer_2_out), .T(1'b1), .Q(Q3__M_S_B), .reset(nand_1_out));  // open: Qn, preset, en
endmodule

module Synchronous_Up_Counter (
  output Q1,
  output Q2,
  output Q3
);

  wire and_1_out, CLK_out;

  Clock CLK (.out(CLK_out));
  T_Flip_Flop T1 (.clk(CLK_out), .T(1'b1), .Q(Q1));  // open: Qn, preset, reset, en
  T_Flip_Flop T2 (.clk(CLK_out), .T(Q1), .Q(Q2));  // open: Qn, preset, reset, en
  T_Flip_Flop T3 (.clk(CLK_out), .T(and_1_out), .Q(Q3));  // open: Qn, preset, reset, en
  and and_1 (and_1_out, Q2, Q1);
endmodule

module Synchronous_Down_Counter (
  output Q1,
  output Q2,
  output Q3
);

  wire and_1_out, CLK_out, T1_qn, T2_qn;

  Clock CLK (.out(CLK_out));
  T_Flip_Flop T1 (.clk(CLK_out), .T(1'b1), .Q(Q1), .Qn(T1_qn));  // open: preset, reset, en
  T_Flip_Flop T2 (.clk(CLK_out), .T(T1_qn), .Q(Q2), .Qn(T2_qn));  // open: preset, reset, en
  T_Flip_Flop T3 (.clk(CLK_out), .T(and_1_out), .Q(Q3));  // open: Qn, preset, reset, en
  and and_1 (and_1_out, T2_qn, T1_qn);
endmodule
