// Logisim project Latch.circ as structural Verilog: 4 circuits, main circuit SR NAND Latch
module SR_NAND_Latch (
  input  R,
  input  Enable,
  input  S,
  output Q_prime,
  output Q
);

  wire NAND_2_out, NAND_out;

  nand NAND (NAND_out, R, Enable);
  nand NAND_2 (NAND_2_out, Enable, S);
  nand NAND_3 (Q_prime, NAND_out, Q);
  nand NAND_4 (Q, Q_prime, NAND_2_out);
endmodule

module Bistable_Cross_Coupled (
  input  R,
  input  S,
  output Q,
  output Q_prime
);

  nor nor_1 (Q, R, Q_prime);
  nor nor_2 (Q_prime, Q, S);
endmodule

module Enable (
  input  R,
  input  Enable,
  input  S,
  output R_2,
  output S_2
);

  and and_1 (R_2, R, Enable);
  and and_2 (S_2, Enable, S);
endmodule

module SR_NOR_Latch (
  input  R,
  input  Enable,
  input  S,
  output Q,
  output Q_prime
);

  wire enable_1_r_2, enable_1_s_2;

  Enable enable_1 (.R(R), .Enable(Enable), .S(S), .R_2(enable_1_r_2), .S_2(enable_1_s_2));
  Bistable_Cross_Coupled bistable_cross_coupled_1 (.R(enable_1_r_2), .S(enable_1_s_2), .Q(Q), .Q_prime(Q_prime));
endmodule
