// Logisim project Pratham Agarwal 24 Hour Clock.circ as structural Verilog: 11 circuits, main circuit Mod 10 Counter
module Mod_10_Counter (
  input  Clock,
  input  [3:0] Input,
  input  Clear,
  output Carry,
  output [3:0] Output
);

  wire or_1_out, t_ff_2_qn, t_ff_3_qn, t_ff_4_qn;

  T_Flip_Flop t_ff_1 (.clk(t_ff_2_qn), .T(1'b1), .Q(Output[3]), .preset(Input[3]), .reset(or_1_out));  // open: Qn, en
  or or_1 (or_1_out, Clear, Carry);
  and and_1 (Carry, Output[3], Output[1]);
  T_Flip_Flop t_ff_2 (
    .clk(t_ff_3_qn), .T(1'b1), .Q(Output[2]), .Qn(t_ff_2_qn), .preset(Input[2]), .reset(or_1_out));  // open: en
  T_Flip_Flop t_ff_3 (
    .clk(t_ff_4_qn), .T(1'b1), .Q(Output[1]), .Qn(t_ff_3_qn), .preset(Input[1]), .reset(or_1_out));  // open: en
  T_Flip_Flop t_ff_4 (
    .clk(Clock), .T(1'b1), .Q(Output[0]), .Qn(t_ff_4_qn), .preset(Input[0]), .reset(or_1_out));  // open: en
endmodule

module Mod_6_Counter (
  input  Clock,
  input  [3:0] Input,
  input  Clear,
  output Carry,
  output [3:0] Output
);

  wire or_1_out, t_ff_2_qn, t_ff_3_qn, t_ff_4_qn;

  T_Flip_Flop t_ff_1 (.clk(t_ff_2_qn), .T(1'b1), .Q(Output[3]), .preset(Input[3]), .reset(or_1_out));  // open: Qn, en
  or or_1 (or_1_out, Clear, Carry);
  and and_1 (Carry, Output[2], Output[1]);
  T_Flip_Flop t_ff_2 (
    .clk(t_ff_3_qn), .T(1'b1), .Q(Output[2]), .Qn(t_ff_2_qn), .preset(Input[2]), .reset(or_1_out));  // open: en
  T_Flip_Flop t_ff_3 (
    .clk(t_ff_4_qn), .T(1'b1), .Q(Output[1]), .Qn(t_ff_3_qn), .preset(Input[1]), .reset(or_1_out));  // open: en
  T_Flip_Flop t_ff_4 (
    .clk(Clock), .T(1'b1), .Q(Output[0]), .Qn(t_ff_4_qn), .preset(Input[0]), .reset(or_1_out));  // open: en
endmodule

module Mod_3_Counter (
  input  Clock,
  input  [3:0] Input,
  input  Clear,
  output Carry,
  output [3:0] Output
);

  wire or_1_out, t_ff_2_qn, t_ff_3_qn, t_ff_4_qn;

  T_Flip_Flop t_ff_1 (.clk(t_ff_2_qn), .T(1'b1), .Q(Output[3]), .preset(Input[3]), .reset(or_1_out));  // open: Qn, en
  or or_1 (or_1_out, Clear, Carry);
  and and_1 (Carry, Output[1], Output[0]);
  T_Flip_Flop t_ff_2 (
    .clk(t_ff_3_qn), .T(1'b1), .Q(Output[2]), .Qn(t_ff_2_qn), .preset(Input[2]), .reset(or_1_out));  // open: en
  T_Flip_Flop t_ff_3 (
    .clk(t_ff_4_qn), .T(1'b1), .Q(Output[1]), .Qn(t_ff_3_qn), .preset(Input[1]), .reset(or_1_out));  // open: en
  T_Flip_Flop t_ff_4 (
    .clk(Clock), .T(1'b1), .Q(Output[0]), .Qn(t_ff_4_qn), .preset(Input[0]), .reset(or_1_out));  // open: en
endmodule

module Hours__24 (
  input  [3:0] HT_set_in,
  input  [3:0] HO_set_in,
  input  Clock,
  input  Clear,
  output [3:0] Ten_s,
  output [3:0] Unit_s
);

  wire and_1_out, mod_10_counter_1_carry, or_1_out;

  Mod_3_Counter mod_3_counter_1 (
    .Clock(mod_10_counter_1_carry), .Input(HT_set_in), .Output(Ten_s), .Clear(or_1_out));  // open: Carry
  Hex_Digit_Display hex_digit_display_1 (.value(Unit_s));  // open: dp
  Hex_Digit_Display hex_digit_display_2 (.value(Ten_s));  // open: dp
  Mod_10_Counter mod_10_counter_1 (
    .Carry(mod_10_counter_1_carry), .Clock(Clock), .Output(Unit_s), .Clear(or_1_out), .Input(HO_set_in));
  or or_1 (or_1_out, and_1_out, Clear);
  and and_1 (and_1_out, Unit_s[2], Ten_s[1]);
endmodule

module Hours__12 (
  input  [3:0] HT_set_in,
  input  [3:0] HO_set_in,
  input  Clock,
  input  Clear,
  output Tick,
  output [3:0] Ten_s,
  output [3:0] Unit_s
);

  wire mod_10_counter_1_carry, nor_1_out, or_3_out;
  wire [3:0] and_2_out, and_3_out, bit_extender_1_out, mod_6_counter_1_output, mod_10_counter_1_output;

  assign Ten_s = and_2_out | mod_6_counter_1_output;  // OR_Gate or_1, 4 bits wide
  Mod_6_Counter mod_6_counter_1 (
    .Clock(mod_10_counter_1_carry), .Output(mod_6_counter_1_output), .Clear(or_3_out), .Input(HO_set_in));  // open: Carry
  assign Unit_s = and_3_out | mod_10_counter_1_output;  // OR_Gate or_2, 4 bits wide
  Mod_10_Counter mod_10_counter_1 (
    .Carry(mod_10_counter_1_carry), .Clock(Clock), .Output(mod_10_counter_1_output), .Clear(or_3_out),
    .Input(HT_set_in));
  or or_3 (or_3_out, Tick, Clear);
  and and_1 (Tick, mod_10_counter_1_output[1], mod_6_counter_1_output[0]);
  Hex_Digit_Display hex_digit_display_1 (.value(Ten_s));  // open: dp
  Hex_Digit_Display hex_digit_display_2 (.value(Unit_s));  // open: dp
  nor nor_1 (nor_1_out, mod_10_counter_1_output[0], mod_10_counter_1_output[1], mod_10_counter_1_output[2], mod_10_counter_1_output[3], mod_6_counter_1_output[0], mod_6_counter_1_output[1], mod_6_counter_1_output[2], mod_6_counter_1_output[3]);
  assign and_2_out = 4'b0001 & bit_extender_1_out;  // AND_Gate and_2, 4 bits wide
  assign and_3_out = bit_extender_1_out & 4'b0010;  // AND_Gate and_3, 4 bits wide
  assign bit_extender_1_out = {{3{nor_1_out}}, nor_1_out};  // Bit_Extender bit_extender_1
endmodule

module AM_PM (
  input  in_1
);

  wire undriven, undriven_2;

  _7_Segment_Display u_7_segment_display_1 (.g(1'b1), .f(1'b1), .a(1'b1), .b(1'b1), .e(1'b1), .c(in_1));  // open: d, dp
  _7_Segment_Display u_7_segment_display_2 (
    .g(undriven), .f(1'b1), .a(1'b1), .b(1'b1), .e(undriven_2), .c(1'b1));  // open: d, dp
  _7_Segment_Display u_7_segment_display_3 (
    .f(1'b1), .a(1'b1), .b(undriven), .e(1'b1), .dp(undriven_2));  // open: g, d, c
endmodule

module Time_Setter (
  input  HT_up,
  input  HO_up,
  input  MT_up,
  input  MO_up,
  input  ST_up,
  input  SO_up,
  input  Set,
  output [3:0] HT_dis,
  output [3:0] HO_dis,
  output [3:0] MT_dis,
  output [3:0] MO_dis,
  output [3:0] ST_dis,
  output [3:0] SO_dis,
  output [3:0] HT_set,
  output [3:0] HO_set,
  output [3:0] MT_set,
  output [3:0] MO_set,
  output [3:0] ST_set,
  output [3:0] SO_set
);

  wire and_1_out, or_1_out;
  wire [3:0] bit_extender_1_out;

  and and_1 (and_1_out, HT_dis[1], or_1_out);
  or or_1 (or_1_out, HO_dis[2], HO_dis[3]);
  Hex_Digit_Display hex_digit_display_1 (.value(HT_dis));  // open: dp
  assign HT_set = bit_extender_1_out & HT_dis;  // AND_Gate and_2, 4 bits wide
  Mod_3_Counter mod_3_counter_1 (.Clock(HT_up), .Output(HT_dis), .Clear(and_1_out));  // open: Carry, Input
  Hex_Digit_Display hex_digit_display_2 (.value(HO_dis));  // open: dp
  assign HO_set = bit_extender_1_out & HO_dis;  // AND_Gate and_3, 4 bits wide
  Mod_10_Counter mod_10_counter_1 (.Clock(HO_up), .Output(HO_dis), .Clear(and_1_out));  // open: Carry, Input
  Hex_Digit_Display hex_digit_display_3 (.value(MT_dis));  // open: dp
  assign MT_set = bit_extender_1_out & MT_dis;  // AND_Gate and_4, 4 bits wide
  Mod_6_Counter mod_6_counter_1 (.Clock(MT_up), .Output(MT_dis));  // open: Carry, Clear, Input
  Hex_Digit_Display hex_digit_display_4 (.value(MO_dis));  // open: dp
  Mod_10_Counter mod_10_counter_2 (.Clock(MO_up), .Output(MO_dis));  // open: Carry, Clear, Input
  assign MO_set = bit_extender_1_out & MO_dis;  // AND_Gate and_5, 4 bits wide
  Hex_Digit_Display hex_digit_display_5 (.value(ST_dis));  // open: dp
  assign ST_set = bit_extender_1_out & ST_dis;  // AND_Gate and_6, 4 bits wide
  Mod_6_Counter mod_6_counter_2 (.Clock(ST_up), .Output(ST_dis));  // open: Carry, Clear, Input
  Hex_Digit_Display hex_digit_display_6 (.value(SO_dis));  // open: dp
  Mod_10_Counter mod_10_counter_3 (.Clock(SO_up), .Output(SO_dis));  // open: Carry, Clear, Input
  assign SO_set = bit_extender_1_out & SO_dis;  // AND_Gate and_7, 4 bits wide
  assign bit_extender_1_out = {{3{Set}}, Set};  // Bit_Extender bit_extender_1
endmodule

module _24_Hour_Clock__view (
);

  wire CLK_out, mod_6_counter_1_carry, mod_6_counter_2_carry, mod_10_counter_1_carry, mod_10_counter_2_carry;
  wire [3:0] hours_24_1_ten_s, hours_24_1_unit_s, mod_6_counter_1_output, mod_6_counter_2_output,
       mod_10_counter_1_output, mod_10_counter_2_output;

  Hex_Digit_Display hex_digit_display_1 (.value(hours_24_1_unit_s));  // open: dp
  Hex_Digit_Display hex_digit_display_2 (.value(hours_24_1_ten_s));  // open: dp
  Hours__24 hours_24_1 (
    .Ten_s(hours_24_1_ten_s), .Unit_s(hours_24_1_unit_s), .Clock(mod_6_counter_1_carry));  // open: Clear, HT_set_in, HO_set_in
  Hex_Digit_Display hex_digit_display_3 (.value(mod_6_counter_1_output));  // open: dp
  Mod_6_Counter mod_6_counter_1 (
    .Carry(mod_6_counter_1_carry), .Clock(mod_10_counter_1_carry), .Output(mod_6_counter_1_output));  // open: Clear, Input
  Hex_Digit_Display hex_digit_display_4 (.value(mod_10_counter_1_output));  // open: dp
  Mod_10_Counter mod_10_counter_1 (
    .Carry(mod_10_counter_1_carry), .Clock(mod_6_counter_2_carry), .Output(mod_10_counter_1_output));  // open: Clear, Input
  Mod_6_Counter mod_6_counter_2 (
    .Carry(mod_6_counter_2_carry), .Clock(mod_10_counter_2_carry), .Output(mod_6_counter_2_output));  // open: Clear, Input
  Hex_Digit_Display hex_digit_display_5 (.value(mod_6_counter_2_output));  // open: dp
  Mod_10_Counter mod_10_counter_2 (
    .Carry(mod_10_counter_2_carry), .Clock(CLK_out), .Output(mod_10_counter_2_output));  // open: Clear, Input
  Clock CLK (.out(CLK_out));
  Hex_Digit_Display hex_digit_display_6 (.value(mod_10_counter_2_output));  // open: dp

  // Notes on the sheet:
  //   :
  //   :
endmodule

module _12_Hour_Clock__view (
);

  wire CLK_out, hours_12_1_tick, mod_6_counter_1_carry, mod_6_counter_2_carry, mod_10_counter_1_carry,
       mod_10_counter_2_carry, t_ff_1_qn;
  wire [3:0] hours_12_1_ten_s, hours_12_1_unit_s, mod_6_counter_1_output, mod_6_counter_2_output,
       mod_10_counter_1_output, mod_10_counter_2_output;

  Hex_Digit_Display hex_digit_display_1 (.value(hours_12_1_ten_s));  // open: dp
  Hex_Digit_Display hex_digit_display_2 (.value(hours_12_1_unit_s));  // open: dp
  Hours__12 hours_12_1 (
    .Clock(mod_6_counter_1_carry), .Tick(hours_12_1_tick), .Ten_s(hours_12_1_ten_s),
    .Unit_s(hours_12_1_unit_s));  // open: HT_set_in, HO_set_in, Clear
  Hex_Digit_Display hex_digit_display_3 (.value(mod_6_counter_1_output));  // open: dp
  Mod_10_Counter mod_10_counter_1 (
    .Carry(mod_10_counter_1_carry), .Clock(mod_6_counter_2_carry), .Output(mod_10_counter_1_output));  // open: Clear, Input
  Mod_6_Counter mod_6_counter_1 (
    .Carry(mod_6_counter_1_carry), .Clock(mod_10_counter_1_carry), .Output(mod_6_counter_1_output));  // open: Clear, Input
  Hex_Digit_Display hex_digit_display_4 (.value(mod_10_counter_1_output));  // open: dp
  Mod_6_Counter mod_6_counter_2 (
    .Carry(mod_6_counter_2_carry), .Clock(mod_10_counter_2_carry), .Output(mod_6_counter_2_output));  // open: Clear, Input
  Hex_Digit_Display hex_digit_display_5 (.value(mod_6_counter_2_output));  // open: dp
  Mod_10_Counter mod_10_counter_2 (
    .Carry(mod_10_counter_2_carry), .Clock(CLK_out), .Output(mod_10_counter_2_output));  // open: Clear, Input
  Clock CLK (.out(CLK_out));
  Hex_Digit_Display hex_digit_display_6 (.value(mod_10_counter_2_output));  // open: dp
  _7_Segment_Display u_7_segment_display_1 (
    .g(1'b1), .f(1'b1), .a(1'b1), .b(1'b1), .e(1'b1), .c(t_ff_1_qn));  // open: d, dp
  _7_Segment_Display u_7_segment_display_2 (.f(1'b1), .a(1'b1), .b(1'b1), .e(1'b1));  // open: g, d, c, dp
  _7_Segment_Display u_7_segment_display_3 (.f(1'b1), .a(1'b1), .b(1'b1), .c(1'b1));  // open: g, e, d, dp
  T_Flip_Flop t_ff_1 (.clk(hours_12_1_tick), .T(1'b1), .Qn(t_ff_1_qn));  // open: Q, preset, reset, en

  // Notes on the sheet:
  //   :
  //   :
endmodule

module _24_Hour_Clock_with_Time_Set__view (
  input  Enable
);

  wire and_1_out, button_1_out, button_2_out, button_3_out, button_4_out, button_5_out, button_6_out,
       Clear_out, Clock_out, mod_6_counter_1_carry, mod_6_counter_2_carry, mod_10_counter_1_carry,
       mod_10_counter_2_carry, Set_out;
  wire [3:0] hours_24_1_ten_s, hours_24_1_unit_s, mod_6_counter_1_output, mod_6_counter_2_output,
       mod_10_counter_1_output, mod_10_counter_2_output, time_setter_1_ho_dis, time_setter_1_ho_set,
       time_setter_1_ht_dis, time_setter_1_ht_set, time_setter_1_mo_dis, time_setter_1_mo_set,
       time_setter_1_mt_dis, time_setter_1_mt_set, time_setter_1_so_dis, time_setter_1_so_set,
       time_setter_1_st_dis, time_setter_1_st_set;

  Hex_Digit_Display hex_digit_display_1 (.value(time_setter_1_ht_dis));  // open: dp
  Hex_Digit_Display hex_digit_display_2 (.value(hours_24_1_ten_s));  // open: dp
  Hex_Digit_Display hex_digit_display_3 (.value(time_setter_1_ho_dis));  // open: dp
  Button button_1 (.out(button_1_out));
  Hours__24 hours_24_1 (
    .Ten_s(hours_24_1_ten_s), .Unit_s(hours_24_1_unit_s), .Clock(mod_6_counter_1_carry), .Clear(Clear_out),
    .HT_set_in(time_setter_1_ht_set), .HO_set_in(time_setter_1_ho_set));
  Hex_Digit_Display hex_digit_display_4 (.value(hours_24_1_unit_s));  // open: dp
  Button button_2 (.out(button_2_out));
  Button button_3 (.out(button_3_out));
  Hex_Digit_Display hex_digit_display_5 (.value(time_setter_1_mt_dis));  // open: dp
  Mod_6_Counter mod_6_counter_1 (
    .Carry(mod_6_counter_1_carry), .Clock(mod_10_counter_1_carry), .Output(mod_6_counter_1_output),
    .Clear(Clear_out), .Input(time_setter_1_mt_set));
  Hex_Digit_Display hex_digit_display_6 (.value(mod_6_counter_1_output));  // open: dp
  Button button_4 (.out(button_4_out));
  Hex_Digit_Display hex_digit_display_7 (.value(time_setter_1_mo_dis));  // open: dp
  Mod_10_Counter mod_10_counter_1 (
    .Carry(mod_10_counter_1_carry), .Clock(mod_6_counter_2_carry), .Output(mod_10_counter_1_output),
    .Clear(Clear_out), .Input(time_setter_1_mo_set));
  Hex_Digit_Display hex_digit_display_8 (.value(mod_10_counter_1_output));  // open: dp
  Hex_Digit_Display hex_digit_display_9 (.value(time_setter_1_st_dis));  // open: dp
  Hex_Digit_Display hex_digit_display_10 (.value(mod_6_counter_2_output));  // open: dp
  Button button_5 (.out(button_5_out));
  Hex_Digit_Display hex_digit_display_11 (.value(time_setter_1_so_dis));  // open: dp
  Mod_6_Counter mod_6_counter_2 (
    .Carry(mod_6_counter_2_carry), .Clock(mod_10_counter_2_carry), .Output(mod_6_counter_2_output),
    .Clear(Clear_out), .Input(time_setter_1_st_set));
  Hex_Digit_Display hex_digit_display_12 (.value(mod_10_counter_2_output));  // open: dp
  Button button_6 (.out(button_6_out));
  Time_Setter time_setter_1 (
    .HT_dis(time_setter_1_ht_dis), .HO_dis(time_setter_1_ho_dis), .MT_dis(time_setter_1_mt_dis),
    .MO_dis(time_setter_1_mo_dis), .ST_dis(time_setter_1_st_dis), .SO_dis(time_setter_1_so_dis),
    .Set(Set_out), .HT_up(button_1_out), .HO_up(button_2_out), .MT_up(button_3_out), .MO_up(button_4_out),
    .ST_up(button_5_out), .SO_up(button_6_out), .HT_set(time_setter_1_ht_set), .HO_set(time_setter_1_ho_set),
    .MT_set(time_setter_1_mt_set), .MO_set(time_setter_1_mo_set), .ST_set(time_setter_1_st_set),
    .SO_set(time_setter_1_so_set));
  and and_1 (and_1_out, Enable, Clock_out);
  Mod_10_Counter mod_10_counter_2 (
    .Carry(mod_10_counter_2_carry), .Clock(and_1_out), .Output(mod_10_counter_2_output), .Clear(Clear_out),
    .Input(time_setter_1_so_set));
  Button Set (.out(Set_out));
  Clock Clock (.out(Clock_out));
  Button Clear (.out(Clear_out));

  // Notes on the sheet:
  //   :
  //   :
  //   Set Time
  //   Clock
  //   :
  //   :
  //   2. Set "Enable" to 0 to stop the clock
  //   3. Press the "Clear" button to clear the time on the clock
  //   5. Set "Enable" to 1 to start the clock again
  //   6. To set a different time, start over from Step 1
  //   Instructions to set time
  //   1. Use the buttons at "Set Time" to change "Set Time" to whatever time you wish to set
  //   4. Press the "Set" button to set the Set Time as the Clock Time
  //   Caution: Do not press "Set" without pressing "Clear" first as this may cause unintended behavior
  //   Note: This clock ticks at the same speed as real time when Tick Frequency is set to 2 Hz
endmodule

module _12_Hour_Clock_with_Time_Set__view (
  input  Enable
);

  wire and_1_out, button_1_out, button_2_out, button_3_out, button_4_out, button_5_out, button_6_out,
       Clear_out, Clock_out, hours_12_1_tick, mod_6_counter_1_carry, mod_6_counter_2_carry,
       mod_10_counter_1_carry, mod_10_counter_2_carry, Set_out, t_ff_1_qn;
  wire [3:0] hours_12_1_ten_s, hours_12_1_unit_s, mod_6_counter_1_output, mod_6_counter_2_output,
       mod_10_counter_1_output, mod_10_counter_2_output, time_setter_1_ho_dis, time_setter_1_ho_set,
       time_setter_1_ht_dis, time_setter_1_ht_set, time_setter_1_mo_dis, time_setter_1_mo_set,
       time_setter_1_mt_dis, time_setter_1_mt_set, time_setter_1_so_dis, time_setter_1_so_set,
       time_setter_1_st_dis, time_setter_1_st_set;

  Hex_Digit_Display hex_digit_display_1 (.value(time_setter_1_ht_dis));  // open: dp
  Hex_Digit_Display hex_digit_display_2 (.value(hours_12_1_ten_s));  // open: dp
  Button button_1 (.out(button_1_out));
  Hex_Digit_Display hex_digit_display_3 (.value(time_setter_1_ho_dis));  // open: dp
  Hours__12 hours_12_1 (
    .Clock(mod_6_counter_1_carry), .Tick(hours_12_1_tick), .Ten_s(hours_12_1_ten_s),
    .Unit_s(hours_12_1_unit_s), .HT_set_in(time_setter_1_ht_set), .HO_set_in(time_setter_1_ho_set),
    .Clear(Clear_out));
  Hex_Digit_Display hex_digit_display_4 (.value(hours_12_1_unit_s));  // open: dp
  Button button_2 (.out(button_2_out));
  Hex_Digit_Display hex_digit_display_5 (.value(time_setter_1_mt_dis));  // open: dp
  Button button_3 (.out(button_3_out));
  Mod_6_Counter mod_6_counter_1 (
    .Carry(mod_6_counter_1_carry), .Clock(mod_10_counter_1_carry), .Output(mod_6_counter_1_output),
    .Clear(Clear_out), .Input(time_setter_1_mt_set));
  Hex_Digit_Display hex_digit_display_6 (.value(mod_6_counter_1_output));  // open: dp
  Hex_Digit_Display hex_digit_display_7 (.value(time_setter_1_mo_dis));  // open: dp
  Button button_4 (.out(button_4_out));
  Mod_10_Counter mod_10_counter_1 (
    .Carry(mod_10_counter_1_carry), .Clock(mod_6_counter_2_carry), .Output(mod_10_counter_1_output),
    .Clear(Clear_out), .Input(time_setter_1_mo_set));
  Hex_Digit_Display hex_digit_display_8 (.value(mod_10_counter_1_output));  // open: dp
  Hex_Digit_Display hex_digit_display_9 (.value(time_setter_1_st_dis));  // open: dp
  Hex_Digit_Display hex_digit_display_10 (.value(mod_6_counter_2_output));  // open: dp
  Button button_5 (.out(button_5_out));
  Hex_Digit_Display hex_digit_display_11 (.value(time_setter_1_so_dis));  // open: dp
  Mod_6_Counter mod_6_counter_2 (
    .Carry(mod_6_counter_2_carry), .Clock(mod_10_counter_2_carry), .Output(mod_6_counter_2_output),
    .Clear(Clear_out), .Input(time_setter_1_st_set));
  Hex_Digit_Display hex_digit_display_12 (.value(mod_10_counter_2_output));  // open: dp
  Button button_6 (.out(button_6_out));
  Time_Setter time_setter_1 (
    .HT_dis(time_setter_1_ht_dis), .HO_dis(time_setter_1_ho_dis), .MT_dis(time_setter_1_mt_dis),
    .MO_dis(time_setter_1_mo_dis), .ST_dis(time_setter_1_st_dis), .SO_dis(time_setter_1_so_dis),
    .Set(Set_out), .HT_up(button_1_out), .HO_up(button_2_out), .MT_up(button_3_out), .MO_up(button_4_out),
    .ST_up(button_5_out), .SO_up(button_6_out), .HT_set(time_setter_1_ht_set), .HO_set(time_setter_1_ho_set),
    .MT_set(time_setter_1_mt_set), .MO_set(time_setter_1_mo_set), .ST_set(time_setter_1_st_set),
    .SO_set(time_setter_1_so_set));
  Mod_10_Counter mod_10_counter_2 (
    .Carry(mod_10_counter_2_carry), .Clock(and_1_out), .Output(mod_10_counter_2_output), .Clear(Clear_out),
    .Input(time_setter_1_so_set));
  and and_1 (and_1_out, Enable, Clock_out);
  _7_Segment_Display u_7_segment_display_1 (.f(1'b1), .a(1'b1), .b(1'b1), .e(1'b1));  // open: g, d, c, dp
  _7_Segment_Display u_7_segment_display_2 (
    .g(1'b1), .f(1'b1), .a(1'b1), .b(1'b1), .e(1'b1), .c(t_ff_1_qn));  // open: d, dp
  Button Set (.out(Set_out));
  Clock Clock (.out(Clock_out));
  Button Clear (.out(Clear_out));
  _7_Segment_Display u_7_segment_display_3 (.f(1'b1), .a(1'b1), .b(1'b1), .c(1'b1));  // open: g, e, d, dp
  T_Flip_Flop t_ff_1 (.clk(hours_12_1_tick), .T(1'b1), .Qn(t_ff_1_qn));  // open: Q, preset, reset, en

  // Notes on the sheet:
  //   :
  //   :
  //   Set Time
  //   Clock
  //   :
  //   :
  //   2. Set "Enable" to 0 to stop the clock
  //   3. Press the "Clear" button to clear the time on the clock
  //   5. Set "Enable" to 1 to start the clock again
  //   6. To set a different time, start over from Step 1
  //   Instructions to set time
  //   1. Use the buttons at "Set Time" to change "Set Time" to whatever time you wish to set
  //   4. Press the "Set" button to set the Set Time as the Clock Time
  //   Caution: Do not press "Set" without pressing "Clear" first as this may cause unintended behavior
  //   Note: This clock ticks at the same speed as real time when Tick Frequency is set to 2 Hz
endmodule
