// Logisim project Sequence (2,3,4,7,4).circ as structural Verilog: 1 circuit, main circuit main
module main (
);

  wire and_1_out, and_2_out, and_3_out, CLK_out, or_1_out, or_2_out, or_3_out, TA_qn, TB_qn;
  wire [2:0] multiplexer_1_out, TC_q;

  and and_1 (and_1_out, TA_qn, TC_q[0]);
  and and_2 (and_2_out, TC_q[0], TB_qn);
  Clock CLK (.out(CLK_out));
  or or_1 (or_1_out, and_1_out, and_2_out);
  T_Flip_Flop TA (.clk(CLK_out), .T(or_1_out), .Q(TC_q[2]), .Qn(TA_qn));  // open: preset, reset, en
  or or_2 (or_2_out, TC_q[2], TC_q[0]);
  T_Flip_Flop TB (.clk(CLK_out), .T(or_2_out), .Q(TC_q[1]), .Qn(TB_qn));  // open: preset, reset, en
  and and_3 (and_3_out, TC_q[2], TB_qn, TC_q[0]);
  Multiplexer #(.width(3), .enable("false")) multiplexer_1 (
    .in0(TC_q), .in1(3'b100), .out(multiplexer_1_out), .sel(and_3_out));
  or or_3 (or_3_out, TB_qn, TA_qn);
  Hex_Digit_Display hex_digit_display_1 (.value({1'b0, multiplexer_1_out}));  // open: dp
  T_Flip_Flop TC (.clk(CLK_out), .T(or_3_out), .Q(TC_q[0]));  // open: Qn, preset, reset, en
endmodule
