// Logisim project Sequence Detector.circ as structural Verilog: 1 circuit, main circuit main
module main (
  output Output__Y,
  output out_2
);

  wire A_q, A_qn, and_1_out, and_2_out, B_q, B_qn, CLK_out, Input_Sequence_out, not_1_out, or_1_out,
       xor_1_out;

  Shift_Register #(.length(16)) Input_Sequence (
    .in(Input_Sequence_out), .clk(CLK_out), .out(Input_Sequence_out), .q15(out_2));  // open: shift, load, clr, d0, q0, d1, q1, d2, q2, d3, q3, d4, q4, d5, q5, d6, q6, d7, q7, d8, q8, d9, q9, d10, q10, d11, q11, d12, q12, d13, q13, d14, q14, d15
  not not_1 (not_1_out, Input_Sequence_out);
  and and_1 (and_1_out, A_q, B_qn);
  xor xor_1 (xor_1_out, A_q, B_q);
  and and_2 (and_2_out, xor_1_out, Input_Sequence_out);
  or or_1 (or_1_out, and_1_out, not_1_out);
  and and_3 (Output__Y, A_q, B_q, not_1_out);
  Clock CLK (.out(CLK_out));
  D_Flip_Flop A (.clk(CLK_out), .D(and_2_out), .Q(A_q), .Qn(A_qn));  // open: preset, en, reset
  D_Flip_Flop B (.clk(CLK_out), .D(or_1_out), .Q(B_q), .Qn(B_qn));  // open: preset, en, reset
  Shift_Register #(.length(3)) shift_register_1 (
    .in(Input_Sequence_out), .clk(CLK_out));  // open: shift, out, load, clr, d0, q0, d1, q1, d2, q2

  // Notes on the sheet:
  //   X
  //    X'
  //       QB' QB QA' QA
  //   SEQUENCE DETECTOR - 0110
  //   Output Sequence
endmodule
