// Logisim project Sequence Generator.circ as structural Verilog: 1 circuit, main circuit Sequence Generator
module Sequence_Generator (
);

  wire clock_1_out, T1_q, T1_qn, T2_q, T2_qn, T3_q, T3_qn;

  Clock clock_1 (.out(clock_1_out));
  T_Flip_Flop T1 (.clk(clock_1_out), .Q(T1_q), .Qn(T1_qn));  // open: T, preset, reset, en
  T_Flip_Flop T2 (.clk(clock_1_out), .Q(T2_q), .Qn(T2_qn));  // open: T, preset, reset, en
  T_Flip_Flop T3 (.clk(clock_1_out), .Q(T3_q), .Qn(T3_qn));  // open: T, preset, reset, en
endmodule
