// Logisim project SequenceCounter_14.circ as structural Verilog: 3 circuits, main circuit Sequence Counter
module Sequence_Counter (
  input  [3:0] Input,
  input  Set_Counter_prime
);

  wire and_1_out, and_2_out, and_3_out, and_4_out, and_5_out, and_6_out, CLK_out, n2_1_mux_1_y, n2_1_mux_2_y,
       n2_1_mux_3_y, not_1_out, not_2_out, not_3_out, not_4_out, not_5_out, not_6_out, not_7_out, not_8_out,
       not_9_out, not_10_out, not_11_out, t_ff_1_q, t_ff_1_qn, t_ff_2_q, t_ff_2_qn, t_ff_3_q;
  wire [2:0] input_1_output;
  wire [3:0] or_4_out;

  Clock CLK (.out(CLK_out));
  or or_1 (or_4_out[3], 1'b0, and_2_out, 1'b0, 1'b0, and_5_out);
  or or_2 (or_4_out[2], 1'b0, 1'b0, and_3_out, 1'b0, 1'b0);
  or or_3 (or_4_out[1], and_1_out, and_2_out, 1'b0, and_4_out, 1'b0);
  and and_1 (and_1_out, not_1_out, not_2_out, not_3_out);
  and and_2 (and_2_out, t_ff_1_q, not_4_out, not_5_out);
  and and_3 (and_3_out, not_6_out, t_ff_2_q, not_7_out);
  and and_4 (and_4_out, t_ff_1_q, t_ff_2_q, not_8_out);
  and and_5 (and_5_out, not_9_out, not_10_out, t_ff_3_q);
  or or_4 (or_4_out[0], 1'b0, 1'b0, and_3_out, 1'b0, 1'b0);
  Input input_1 (.Input(Input), .Output(input_1_output));
  T_Flip_Flop t_ff_1 (
    .clk(CLK_out), .T(1'b1), .Q(t_ff_1_q), .Qn(t_ff_1_qn), .preset(n2_1_mux_3_y), .reset(and_6_out));  // open: en
  and and_6 (and_6_out, t_ff_3_q, not_11_out, t_ff_1_q);
  not not_1 (not_1_out, t_ff_1_q);
  not not_2 (not_2_out, t_ff_2_q);
  not not_3 (not_3_out, t_ff_3_q);
  not not_4 (not_4_out, t_ff_2_q);
  not not_5 (not_5_out, t_ff_3_q);
  not not_6 (not_6_out, t_ff_1_q);
  not not_7 (not_7_out, t_ff_3_q);
  not not_8 (not_8_out, t_ff_3_q);
  not not_9 (not_9_out, t_ff_1_q);
  not not_10 (not_10_out, t_ff_2_q);
  _2_1_MUX u_2_1_mux_1 (.Y0(1'b0), .Y1(input_1_output[2]), .S0(Set_Counter_prime), .Y(n2_1_mux_1_y));
  not not_11 (not_11_out, t_ff_2_q);
  _2_1_MUX u_2_1_mux_2 (.Y0(1'b0), .Y1(input_1_output[1]), .S0(Set_Counter_prime), .Y(n2_1_mux_2_y));
  _2_1_MUX u_2_1_mux_3 (.Y0(1'b0), .Y1(input_1_output[0]), .S0(Set_Counter_prime), .Y(n2_1_mux_3_y));
  T_Flip_Flop t_ff_2 (
    .clk(t_ff_1_qn), .T(1'b1), .Q(t_ff_2_q), .Qn(t_ff_2_qn), .preset(n2_1_mux_2_y), .reset(and_6_out));  // open: en
  T_Flip_Flop t_ff_3 (
    .clk(t_ff_2_qn), .T(1'b1), .Q(t_ff_3_q), .preset(n2_1_mux_1_y), .reset(and_6_out));  // open: Qn, en
  Hex_Digit_Display hex_digit_display_1 (.value(or_4_out));  // open: dp
endmodule

module Input (
  input  [3:0] Input,
  output [2:0] Output
);

  wire and_1_out, and_2_out, and_3_out, and_4_out, and_5_out, and_6_out, and_7_out, and_8_out, and_9_out,
       and_10_out, and_11_out, and_12_out, not_1_out, not_2_out, not_3_out, not_4_out, not_5_out, not_6_out,
       not_7_out, not_8_out, not_9_out, not_10_out, not_11_out, not_12_out, not_13_out, not_14_out,
       not_15_out, not_16_out, not_17_out, not_18_out, not_19_out, not_20_out, or_4_out, or_5_out, or_6_out;

  or or_1 (Output[2], 1'b0, 1'b0, or_6_out);
  or or_2 (Output[1], 1'b0, or_5_out, 1'b0);
  or or_3 (Output[0], or_4_out, 1'b0, 1'b0);
  or or_4 (or_4_out, and_1_out, and_2_out, and_3_out, and_4_out, and_5_out, and_6_out);
  or or_5 (or_5_out, and_7_out, and_8_out, and_9_out);
  or or_6 (or_6_out, and_10_out, and_11_out, and_12_out);
  and and_1 (and_1_out, Input[3], not_1_out, Input[1], not_2_out);
  and and_2 (and_2_out, Input[3], not_3_out, Input[1], Input[0]);
  and and_3 (and_3_out, Input[3], Input[2], not_4_out, not_5_out);
  and and_4 (and_4_out, Input[3], Input[2], not_6_out, Input[0]);
  and and_5 (and_5_out, Input[3], Input[2], Input[1], not_7_out);
  and and_6 (and_6_out, Input[3], Input[2], Input[1], Input[0]);
  and and_7 (and_7_out, not_8_out, Input[2], not_9_out, not_10_out);
  and and_8 (and_8_out, not_11_out, Input[2], not_12_out, Input[0]);
  and and_9 (and_9_out, not_13_out, Input[2], Input[1], not_14_out);
  and and_10 (and_10_out, not_15_out, Input[2], Input[1], Input[0]);
  and and_11 (and_11_out, Input[3], not_16_out, not_17_out, not_18_out);
  and and_12 (and_12_out, Input[3], not_19_out, not_20_out, Input[0]);
  not not_1 (not_1_out, Input[2]);
  not not_2 (not_2_out, Input[0]);
  not not_3 (not_3_out, Input[2]);
  not not_4 (not_4_out, Input[1]);
  not not_5 (not_5_out, Input[0]);
  not not_6 (not_6_out, Input[1]);
  not not_7 (not_7_out, Input[0]);
  not not_8 (not_8_out, Input[3]);
  not not_9 (not_9_out, Input[1]);
  not not_10 (not_10_out, Input[0]);
  not not_11 (not_11_out, Input[3]);
  not not_12 (not_12_out, Input[1]);
  not not_13 (not_13_out, Input[3]);
  not not_14 (not_14_out, Input[0]);
  not not_15 (not_15_out, Input[3]);
  not not_16 (not_16_out, Input[2]);
  not not_17 (not_17_out, Input[1]);
  not not_18 (not_18_out, Input[0]);
  not not_19 (not_19_out, Input[2]);
  not not_20 (not_20_out, Input[1]);
endmodule

module _2_1_MUX (
  input  Y0,
  input  Y1,
  input  S0,
  output Y
);

  wire and_1_out, and_2_out, not_1_out;

  not not_1 (not_1_out, S0);
  and and_1 (and_1_out, Y0, not_1_out);
  and and_2 (and_2_out, Y1, S0);
  or or_1 (Y, and_1_out, and_2_out);
endmodule
