// Logisim project Types of Latch.circ as structural Verilog: 2 circuits, main circuit Master-Slave JK Latch
// JK Latch
module Master_Slave_JK_Latch (
  input  K,
  input  ENABLE,
  input  J,
  output Q,
  output Q_prime
);

  wire nand_1_out, nand_2_out, nand_3_out, nand_4_out, nand_5_out, nand_6_out, not_1_out;

  nand nand_1 (nand_1_out, Q_prime, K, ENABLE);
  nand nand_2 (nand_2_out, ENABLE, J, Q);
  not not_1 (not_1_out, ENABLE);
  nand nand_3 (nand_3_out, nand_1_out, nand_4_out);
  nand nand_4 (nand_4_out, nand_3_out, nand_2_out);
  nand nand_5 (nand_5_out, nand_3_out, not_1_out);
  nand nand_6 (nand_6_out, not_1_out, nand_4_out);
  nand nand_7 (Q, nand_5_out, Q_prime);
  nand nand_8 (Q_prime, Q, nand_6_out);
endmodule

module Data_Latch__D_Latch (
  input  D,
  input  ENABLE,
  output Q,
  output Q_prime
);

  wire NAND_2_out, NAND_out, not_1_out;

  not not_1 (not_1_out, D);
  nand NAND (NAND_out, D, ENABLE);
  nand NAND_2 (NAND_2_out, ENABLE, not_1_out);
  nand NAND_3 (Q, NAND_out, Q_prime);
  nand NAND_4 (Q_prime, Q, NAND_2_out);
endmodule
