// Logisim project Universal Shift Register With Circular Shift.circ as structural Verilog: 4 circuits, main circuit D Latch
module D_Latch (
  input  D,
  input  E,
  output Q,
  output Q_prime
);

  wire nand_1_out, nand_2_out, not_1_out;

  not not_1 (not_1_out, D);
  nand nand_1 (nand_1_out, D, E);
  nand nand_2 (nand_2_out, E, not_1_out);
  nand nand_3 (Q, nand_1_out, Q_prime);
  nand nand_4 (Q_prime, Q, nand_2_out);
endmodule

module _4_1_MUX (
  input  i0,
  input  i1,
  input  i2,
  input  i3,
  input  s1,
  input  s0,
  output Y
);

  wire and_1_out, and_2_out, and_3_out, and_4_out, not_1_out, not_2_out;

  not not_1 (not_1_out, s1);
  not not_2 (not_2_out, s0);
  and and_1 (and_1_out, i0, not_1_out, not_2_out);
  and and_2 (and_2_out, i1, not_1_out, s0);
  and and_3 (and_3_out, i2, s1, not_2_out);
  and and_4 (and_4_out, i3, s1, s0);
  or or_1 (Y, and_1_out, and_2_out, and_3_out, and_4_out);
endmodule

module USR (
  input  PDI3,
  input  PDI2,
  input  PDI1,
  input  PDI0,
  input  S1,
  input  S0,
  input  SDI_R,
  input  SDI_L,
  input  ENABLE,
  input  CLEAR,
  input  PRESET,
  output PDO3,
  output PDO2,
  output PDO1,
  output PDO3_2
);

  wire CLK_out, n4_1_mux_1_y, n4_1_mux_2_y, n4_1_mux_3_y, n4_1_mux_4_y;

  Clock CLK (.out(CLK_out));
  _4_1_MUX u_4_1_mux_1 (.i0(PDO3), .i1(SDI_R), .i2(PDO2), .i3(PDI3), .Y(n4_1_mux_1_y), .s1(S1), .s0(S0));
  D_Flip_Flop d_ff_1 (
    .clk(CLK_out), .D(n4_1_mux_1_y), .Q(PDO3), .preset(PRESET), .en(ENABLE), .reset(CLEAR));  // open: Qn
  _4_1_MUX u_4_1_mux_2 (.i0(PDO2), .i1(PDO3), .i2(PDO1), .i3(PDI2), .Y(n4_1_mux_2_y), .s1(S1), .s0(S0));
  D_Flip_Flop d_ff_2 (
    .clk(CLK_out), .D(n4_1_mux_2_y), .Q(PDO2), .preset(PRESET), .en(ENABLE), .reset(CLEAR));  // open: Qn
  _4_1_MUX u_4_1_mux_3 (.i0(PDO1), .i1(PDO2), .i2(PDO3_2), .i3(PDI1), .Y(n4_1_mux_3_y), .s1(S1), .s0(S0));
  D_Flip_Flop d_ff_3 (
    .clk(CLK_out), .D(n4_1_mux_3_y), .Q(PDO1), .preset(PRESET), .en(ENABLE), .reset(CLEAR));  // open: Qn
  _4_1_MUX u_4_1_mux_4 (.i0(PDO3_2), .i1(PDO1), .i2(SDI_L), .i3(PDI0), .Y(n4_1_mux_4_y), .s1(S1), .s0(S0));
  D_Flip_Flop d_ff_4 (
    .clk(CLK_out), .D(n4_1_mux_4_y), .Q(PDO3_2), .preset(PRESET), .en(ENABLE), .reset(CLEAR));  // open: Qn
endmodule

module TFF (
  input  in_1,
  input  in_2,
  output out_3,
  output out_4
);

  wire nand_1_out, nand_2_out, nand_3_out, nand_4_out, nand_5_out, nand_6_out, not_1_out;

  nand nand_1 (nand_1_out, in_1, in_2);
  nand nand_2 (nand_2_out, in_2, in_1);
  nand nand_3 (nand_3_out, nand_1_out, nand_4_out);
  nand nand_4 (nand_4_out, nand_3_out, nand_2_out);
  not not_1 (not_1_out, in_2);
  nand nand_5 (nand_5_out, nand_3_out, not_1_out);
  nand nand_6 (nand_6_out, not_1_out, nand_4_out);
  nand nand_7 (in_1, nand_5_out, in_1);
  nand nand_8 (in_1, in_1, nand_6_out);

  assign out_3 = in_1;
  assign out_4 = in_1;
endmodule
